// Logisim project Project 1.circ as structural Verilog: 3 circuits, main circuit Compare
module Compare (
  input  X2,
  input  Y2,
  input  X1,
  input  Y1,
  input  X0,
  input  Y0,
  output E,
  output N
);

  wire and_1_out, and_2_out, and_3_out, and_4_out, and_5_out, not_1_out, not_2_out, not_3_out, xnor_1_out,
       xnor_2_out, xnor_3_out;

  not not_1 (not_1_out, X2);
  not not_2 (not_2_out, X1);
  not not_3 (not_3_out, X0);
  xnor xnor_1 (xnor_1_out, X2, Y2);
  xnor xnor_2 (xnor_2_out, X1, Y1);
  xnor xnor_3 (xnor_3_out, X0, Y0);
  and and_1 (and_1_out, not_1_out, Y2);
  and and_2 (and_2_out, not_2_out, Y1);
  and and_3 (and_3_out, not_3_out, Y0);
  and and_4 (and_4_out, xnor_1_out, and_2_out);
  and and_5 (and_5_out, xnor_1_out, xnor_2_out, and_3_out);
  and and_6 (E, xnor_1_out, xnor_2_out, xnor_3_out);
  or or_1 (N, and_1_out, and_4_out, and_5_out);
endmodule

module Gray (
  input  B3,
  input  B2,
  input  B1,
  input  B0,
  output G3,
  output G2,
  output G1,
  output G0
);

  wire and_1_out, and_2_out, and_3_out, and_4_out, and_5_out, and_6_out, and_7_out, and_8_out, not_1_out,
       not_2_out, not_3_out, not_4_out;

  not not_1 (not_1_out, B3);
  not not_2 (not_2_out, B2);
  not not_3 (not_3_out, B1);
  not not_4 (not_4_out, B0);
  and and_1 (and_1_out, not_1_out, B2);
  and and_2 (and_2_out, not_1_out, B1);
  and and_3 (and_3_out, B3, not_2_out, not_3_out);
  and and_4 (and_4_out, not_1_out, not_2_out);
  and and_5 (and_5_out, not_1_out, not_3_out);
  and and_6 (and_6_out, B3, B2, B1);
  and and_7 (and_7_out, not_3_out, not_4_out);
  and and_8 (and_8_out, B1, B0);
  or or_1 (G3, and_1_out, and_2_out, and_3_out);
  or or_2 (G2, and_4_out, and_5_out, and_6_out);
  or or_3 (G0, and_7_out, and_8_out);

  assign G1 = B2;
endmodule

module FiveSeven (
  input  V,
  input  W,
  input  X,
  input  Y,
  input  Z,
  output A,
  output B,
  output C,
  output D,
  output E,
  output F,
  output G
);

  wire and_1_out, and_2_out, and_3_out, and_4_out, and_5_out, and_6_out, and_7_out, and_8_out, and_9_out,
       and_10_out, and_11_out, and_12_out, and_13_out, and_14_out, and_15_out, and_16_out, and_17_out,
       and_18_out, and_19_out, and_20_out, and_21_out, and_22_out, and_23_out, and_24_out, and_25_out,
       and_26_out, and_27_out, and_28_out, and_29_out, and_30_out, and_31_out, and_32_out, and_33_out,
       and_34_out, and_35_out, and_36_out, and_37_out, and_38_out, and_39_out, and_40_out, and_41_out,
       and_42_out, and_43_out, and_44_out, and_45_out, and_46_out, and_47_out, and_48_out, and_49_out,
       and_50_out, and_51_out, and_52_out, and_53_out, and_54_out, and_55_out, and_56_out, and_57_out,
       and_58_out, and_59_out, and_60_out, and_61_out, and_62_out, and_63_out, and_64_out, and_65_out,
       and_66_out, and_67_out, and_68_out, and_69_out, and_70_out, and_71_out, and_72_out, and_73_out,
       and_74_out, and_75_out, and_76_out, and_77_out, not_1_out, not_2_out, not_3_out, not_4_out, not_5_out;

  not not_1 (not_1_out, V);
  not not_2 (not_2_out, W);
  not not_3 (not_3_out, X);
  not not_4 (not_4_out, Y);
  not not_5 (not_5_out, Z);
  and and_1 (and_1_out, not_1_out, W, X);
  and and_2 (and_2_out, V, not_2_out, X);
  and and_3 (and_3_out, W, not_3_out, Y);
  and and_4 (and_4_out, not_1_out, not_2_out, not_3_out, not_4_out);
  and and_5 (and_5_out, not_2_out, X, Y);
  and and_6 (and_6_out, V, not_2_out, Y);
  and and_7 (and_7_out, V, W, not_4_out);
  and and_8 (and_8_out, W, X);
  and and_9 (and_9_out, W, Y);
  and and_10 (and_10_out, V, Y);
  and and_11 (and_11_out, X, Y);
  and and_12 (and_12_out, V, W);
  and and_13 (and_13_out, V, X);
  and and_14 (and_14_out, not_1_out, Z);
  and and_15 (and_15_out, not_4_out, Z);
  and and_16 (and_16_out, not_1_out, not_2_out, not_3_out);
  and and_17 (and_17_out, not_1_out, not_2_out, not_4_out);
  and and_18 (and_18_out, W, X, Y);
  and and_19 (and_19_out, not_1_out, not_3_out, not_4_out);
  and and_20 (and_20_out, V, W, X);
  and and_21 (and_21_out, not_2_out, not_3_out, not_4_out);
  and and_22 (and_22_out, V, W, Y);
  and and_23 (and_23_out, V, X, Y, not_5_out);
  and and_24 (and_24_out, not_3_out, Z);
  and and_25 (and_25_out, not_1_out, not_2_out, not_3_out, not_4_out);
  and and_26 (and_26_out, not_1_out, not_2_out, not_3_out, Z);
  and and_27 (and_27_out, not_1_out, not_2_out, not_4_out, Z);
  and and_28 (and_28_out, not_1_out, not_3_out, not_4_out, Z);
  and and_29 (and_29_out, not_1_out, X, Y, not_5_out);
  and and_30 (and_30_out, W, X, not_4_out, not_5_out);
  and and_31 (and_31_out, W, X, Y, Z);
  and and_32 (and_32_out, W, not_3_out, Y, not_5_out);
  and and_33 (and_33_out, not_2_out, not_3_out, not_4_out, Z);
  and and_34 (and_34_out, V, not_2_out, Y, not_5_out);
  and and_35 (and_35_out, V, not_2_out, X, Y);
  and and_36 (and_36_out, V, X, not_4_out, not_5_out);
  and and_37 (and_37_out, V, W, not_4_out, not_5_out);
  and and_38 (and_38_out, V, W, X, Z);
  and and_39 (and_39_out, V, W, Y, Z);
  and and_40 (and_40_out, not_1_out, not_2_out, not_3_out, not_4_out, not_5_out);
  and and_41 (and_41_out, not_1_out, not_2_out, not_3_out, Y, Z);
  and and_42 (and_42_out, not_1_out, not_2_out, X, not_4_out, Z);
  and and_43 (and_43_out, not_1_out, not_2_out, X, Y, not_5_out);
  and and_44 (and_44_out, not_1_out, W, X, not_4_out, not_5_out);
  and and_45 (and_45_out, not_1_out, W, X, Y, Z);
  and and_46 (and_46_out, not_1_out, W, not_3_out, not_4_out, Z);
  and and_47 (and_47_out, not_1_out, W, not_3_out, Y, not_5_out);
  and and_48 (and_48_out, V, not_2_out, not_3_out, not_4_out, Z);
  and and_49 (and_49_out, V, not_2_out, not_3_out, Y, not_5_out);
  and and_50 (and_50_out, V, not_2_out, X, not_4_out, not_5_out);
  and and_51 (and_51_out, V, not_2_out, X, Y, Z);
  and and_52 (and_52_out, V, W, X, not_4_out, Z);
  and and_53 (and_53_out, V, W, not_3_out, not_4_out, not_5_out);
  and and_54 (and_54_out, V, W, not_3_out, Y, Z);
  and and_55 (and_55_out, not_1_out, not_2_out, not_3_out, not_4_out);
  and and_56 (and_56_out, not_1_out, not_2_out, not_3_out, Z);
  and and_57 (and_57_out, not_1_out, not_2_out, not_4_out, Z);
  and and_58 (and_58_out, not_1_out, not_3_out, not_4_out, Z);
  and and_59 (and_59_out, not_2_out, not_3_out, not_4_out, Z);
  and and_60 (and_60_out, W, X, Y, Z);
  and and_61 (and_61_out, V, W, X, Z);
  and and_62 (and_62_out, V, W, X, Y);
  and and_63 (and_63_out, V, W, Y, Z);
  and and_64 (and_64_out, not_1_out, not_2_out, not_4_out, Z);
  and and_65 (and_65_out, not_1_out, not_2_out, not_3_out, Z);
  and and_66 (and_66_out, not_1_out, not_3_out, not_4_out, Z);
  and and_67 (and_67_out, not_2_out, not_3_out, not_4_out, Z);
  and and_68 (and_68_out, W, X, not_4_out, not_5_out);
  and and_69 (and_69_out, X, Y, not_5_out);
  and and_70 (and_70_out, W, X, Y);
  and and_71 (and_71_out, W, Y, not_5_out);
  and and_72 (and_72_out, V, X, not_4_out, not_5_out);
  and and_73 (and_73_out, V, W, not_4_out, not_5_out);
  and and_74 (and_74_out, V, W, X);
  and and_75 (and_75_out, V, X, Y);
  and and_76 (and_76_out, V, W, Y);
  and and_77 (and_77_out, V, Y, not_5_out);
  or or_1 (A, Z, and_1_out, and_2_out, and_3_out, and_4_out, and_5_out, and_6_out, and_7_out);
  or or_2 (B, not_5_out, and_8_out, and_9_out, and_10_out, and_11_out, and_12_out, and_13_out);
  or or_3 (C, and_14_out, and_15_out, and_16_out, and_17_out, and_18_out, and_19_out, and_20_out, and_21_out, and_22_out, and_23_out, and_24_out);
  or or_4 (D, and_25_out, and_26_out, and_27_out, and_28_out, and_29_out, and_30_out, and_31_out, and_32_out, and_33_out, and_34_out, and_35_out, and_36_out, and_37_out, and_38_out, and_39_out);
  or or_5 (E, and_40_out, and_41_out, and_42_out, and_43_out, and_44_out, and_45_out, and_46_out, and_47_out, and_48_out, and_49_out, and_50_out, and_51_out, and_52_out, and_53_out, and_54_out);
  or or_6 (F, and_55_out, and_56_out, and_57_out, and_58_out, and_59_out, and_60_out, and_61_out, and_62_out, and_63_out);
  or or_7 (G, and_64_out, and_65_out, and_66_out, and_67_out, and_68_out, and_69_out, and_70_out, and_71_out, and_72_out, and_73_out, and_74_out, and_75_out, and_76_out, and_77_out);

  // Notes on the sheet:
  //   V
  //   V
  //   V
  //   V
  //   V
  //   V
  //   V
  //   V
  //   W
  //   ~V
  //   W
  //   ~V
  //   W
  //   ~V
  //   W
  //   ~V
  //   W
  //   ~V
  //   W
  //   ~V
  //   W
  //   ~V
  //   W
  //   ~V
  //   ~W
  //   ~W
  //   ~W
  //   ~W
  //   ~W
  //   ~W
  //   ~W
  //   ~W
  //   X
  //   ~X
  //   X
  //   ~X
  //   ~X
  //   X
  //   X
  //   ~X
  //   ~X
  //   X
  //   ~X
  //   X
  //   ~X
  //   X
  //   X
  //   ~X
  //   Y
  //   ~Y
  //   Y
  //   Y
  //   Y
  //   ~Y
  //   Y
  //   Y
  //   Y
  //   Y
  //   Z
  //   ~Y
  //   Z
  //   ~Y
  //   Z
  //   Z
  //   ~Y
  //   Z
  //   ~Y
  //   Z
  //   ~Y
  //   Z
  //   ~Y
  //   Z
  //   ~Z
  //   ~Z
  //   ~Z
  //   ~Z
  //   ~Z
  //   ~Z
  //   ~Z
  //   ~Z
endmodule
