// Logisim project Project 2.circ as structural Verilog: 2 circuits, main circuit Panel
module Panel (
  input  R0,
  input  R1,
  input  R2,
  input  R3,
  input  C0,
  input  C1,
  input  C2,
  output V,
  output B0,
  output B1,
  output B2,
  output B3
);

  wire and_1_out, and_2_out, and_3_out, and_4_out, and_5_out, and_6_out, and_7_out, and_8_out, and_9_out,
       and_10_out, and_11_out, and_12_out, and_13_out, and_14_out, and_15_out, and_16_out, or_1_out,
       or_2_out, or_3_out, or_4_out;

  or or_1 (or_1_out, R0, R2);
  or or_2 (or_2_out, C0, C2);
  and and_1 (and_1_out, ~R0, ~R1, ~R2, R3);  // AND_Gate
  and and_2 (and_2_out, ~R0, ~R1, ~R3, R2);  // AND_Gate
  and and_3 (and_3_out, ~R0, ~R2, ~R3, R1);  // AND_Gate
  and and_4 (and_4_out, ~R1, ~R2, ~R3, R0);  // AND_Gate
  and and_5 (and_5_out, ~C0, ~C1, C2);  // AND_Gate
  and and_6 (and_6_out, ~C1, ~C2, C0);  // AND_Gate
  and and_7 (and_7_out, ~C2, ~C0, C1);  // AND_Gate
  and and_8 (and_8_out, or_1_out, or_2_out);
  and and_9 (and_9_out, R1, C1);
  and and_10 (and_10_out, R3, C2);
  and and_11 (and_11_out, R0, ~C0);  // AND_Gate
  and and_12 (and_12_out, C2, ~R2);  // AND_Gate
  and and_13 (and_13_out, C0, ~R0, ~R1);  // AND_Gate
  and and_14 (and_14_out, R2, C0);
  and and_15 (and_15_out, R2, ~C0);  // AND_Gate
  and and_16 (and_16_out, R3, ~C1);  // AND_Gate
  or or_3 (or_3_out, and_1_out, and_2_out, and_3_out, and_4_out);
  or or_4 (or_4_out, and_5_out, and_6_out, and_7_out);
  and and_17 (V, or_3_out, or_4_out);
  or or_5 (B0, and_8_out, and_9_out, and_10_out);
  or or_6 (B1, and_11_out, and_12_out, and_13_out);
  or or_7 (B2, R1, and_14_out);
  or or_8 (B3, and_15_out, and_16_out);

  // Notes on the sheet:
  //   R1
  //   R0
  //   R1
  //   R0
  //   R2
  //   R2
  //   R3
  //   R3
  //   C0
  //   C0
  //   C2
  //   C1
  //   C2
  //   C1
endmodule

module InputBuffer (
  input  B3,
  input  B2,
  input  B1,
  input  B0,
  input  V
);

  D_Flip_Flop d_ff_1 ();  // open: clk, D, Q, Qn, preset, en, reset
  Clock CLK ();  // open: out
endmodule
