// Logisim project Project2Given.circ as structural Verilog: 4 circuits, main circuit main
module main (
);

  wire and_1_out, and_2_out, B0, B1, B2, B3, B4, B5, B6, B7, B8, B9, BL, BU, C0, C1, C2, CLK, lock_1_l,
       lock_1_u, not_1_out, or_8_out, panel_1_v, R0, R1, R3, R4, Valid;
  wire [2:0] counter_1_q;
  wire [3:0] inputbuffer_1_c0, panel_1_b0, register_2_q, register_3_q, register_4_q, register_5_q;

  Button _2 (.out(B2));
  Button _1 (.out(B1));
  Button _4 (.out(B4));
  Button _5 (.out(B5));
  Button _8 (.out(B8));
  Button _7 (.out(B7));
  Button L (.out(BL));
  Button _0 (.out(B0));
  Button _3 (.out(B3));
  Button _6 (.out(B6));
  Button _9 (.out(B9));
  Button U (.out(BU));
  or or_1 (R0, B3, B2, B1);
  or or_2 (R1, B6, B5, B4);
  or or_3 (R3, B9, B8, B7);
  or or_4 (R4, BU, B0, BL);
  or or_5 (C0, B1, B4, B7, BL);
  or or_6 (C1, B2, B5, B8, B0);
  or or_7 (C2, B3, B6, B9, BU);
  Clock clock_1 (.out(CLK));
  // Probe on panel_1_b0
  Panel panel_1 (
    .R0(R0), .R1(R1), .R2(R3), .R3(R4), .C0(C0), .C1(C1), .C2(C2), .B0(panel_1_b0[0]), .B1(panel_1_b0[1]),
    .B2(panel_1_b0[2]), .B3(panel_1_b0[3]), .V(panel_1_v));
  not not_1 (not_1_out, CLK);
  LED Press (.in(panel_1_v));
  nand nand_1 (Valid, inputbuffer_1_c0[0], inputbuffer_1_c0[1], inputbuffer_1_c0[2], inputbuffer_1_c0[3]);
  // Probe on inputbuffer_1_c0
  InputBuffer inputbuffer_1 (
    .B0(panel_1_b0[0]), .B1(panel_1_b0[1]), .B2(panel_1_b0[2]), .B3(panel_1_b0[3]), .V(panel_1_v),
    .CLK(not_1_out), .C0(inputbuffer_1_c0[0]), .C1(inputbuffer_1_c0[1]), .C2(inputbuffer_1_c0[2]),
    .C3(inputbuffer_1_c0[3]));
  Lock lock_1 (
    .C0(inputbuffer_1_c0[0]), .C1(inputbuffer_1_c0[1]), .C2(inputbuffer_1_c0[2]), .C3(inputbuffer_1_c0[3]),
    .CLK(CLK), .L(lock_1_l), .U(lock_1_u));
  Register #(.width(4)) register_1 (.D(register_2_q), .en(Valid), .clk(CLK));  // open: Q, clr
  Counter #(.width(3), .max('h7), .ongoal("stay")) counter_1 (
    .load(lock_1_u), .count(or_8_out), .Q(counter_1_q), .clk(CLK));  // open: D, carry, clr
  or or_8 (or_8_out, lock_1_l, lock_1_u);
  Register #(.width(4)) register_2 (.D(register_3_q), .en(Valid), .Q(register_2_q), .clk(CLK));  // open: clr
  Register #(.width(4)) register_3 (.D(register_4_q), .en(Valid), .Q(register_3_q), .clk(CLK));  // open: clr
  LED Locked (.in(and_2_out));
  LED Unlocked (.in(and_1_out));
  and and_1 (and_1_out, ~counter_1_q[0], ~counter_1_q[1], ~counter_1_q[2]);  // AND_Gate
  and and_2 (and_2_out, ~counter_1_q[0], ~counter_1_q[1], counter_1_q[2]);  // AND_Gate
  Register #(.width(4)) register_4 (.D(register_5_q), .en(Valid), .Q(register_4_q), .clk(CLK));  // open: clr
  Register #(.width(4)) register_5 (.D(inputbuffer_1_c0), .en(Valid), .Q(register_5_q), .clk(CLK));  // open: clr
endmodule

module Panel (
  input  R0,
  input  R1,
  input  R2,
  input  R3,
  input  C0,
  input  C1,
  input  C2,
  output B0,
  output B1,
  output B2,
  output B3,
  output V
);

  wire and_1_out, and_2_out, and_3_out, and_4_out, and_5_out, and_6_out, and_7_out, and_8_out, and_9_out,
       and_10_out, and_11_out, and_12_out, and_13_out, and_14_out, and_15_out, and_16_out, or_1_out,
       or_2_out, or_3_out, or_4_out;

  or or_1 (or_1_out, R0, R2);
  or or_2 (or_2_out, C0, C2);
  and and_1 (and_1_out, ~R0, ~R1, ~R2, R3);  // AND_Gate
  and and_2 (and_2_out, ~R0, ~R1, ~R3, R2);  // AND_Gate
  and and_3 (and_3_out, ~R0, ~R2, ~R3, R1);  // AND_Gate
  and and_4 (and_4_out, ~R1, ~R2, ~R3, R0);  // AND_Gate
  and and_5 (and_5_out, ~C0, ~C1, C2);  // AND_Gate
  and and_6 (and_6_out, ~C1, ~C2, C0);  // AND_Gate
  and and_7 (and_7_out, ~C2, ~C0, C1);  // AND_Gate
  and and_8 (and_8_out, or_1_out, or_2_out);
  and and_9 (and_9_out, R1, C1);
  and and_10 (and_10_out, R3, C2);
  and and_11 (and_11_out, R0, ~C0);  // AND_Gate
  and and_12 (and_12_out, C2, ~R2);  // AND_Gate
  and and_13 (and_13_out, C0, ~R0, ~R1);  // AND_Gate
  and and_14 (and_14_out, R2, C0);
  and and_15 (and_15_out, R2, ~C0);  // AND_Gate
  and and_16 (and_16_out, R3, ~C1);  // AND_Gate
  or or_3 (or_3_out, and_1_out, and_2_out, and_3_out, and_4_out);
  or or_4 (or_4_out, and_5_out, and_6_out, and_7_out);
  and and_17 (V, or_3_out, or_4_out);
  or or_5 (B0, and_8_out, and_9_out, and_10_out);
  or or_6 (B1, and_11_out, and_12_out, and_13_out);
  or or_7 (B2, R1, and_14_out);
  or or_8 (B3, and_15_out, and_16_out);

  // Notes on the sheet:
  //   R1
  //   R0
  //   R1
  //   R0
  //   R2
  //   R2
  //   R3
  //   R3
  //   C0
  //   C1
  //   C0
  //   C1
  //   C2
  //   C2
endmodule

module InputBuffer (
  input  B0,
  input  B1,
  input  B2,
  input  B3,
  input  V,
  input  CLK,
  output C0,
  output C1,
  output C2,
  output C3
);

  wire and_1_out, and_2_out, and_3_out, and_4_out, and_5_out, and_6_out, and_7_out, and_8_out, and_9_out,
       and_10_out, and_11_out, d_ff_1_q, d_ff_1_qn, d_ff_2_q, d_ff_2_qn, not_1_out, or_1_out, or_2_out,
       or_3_out, or_4_out, or_5_out, or_6_out, or_7_out;

  not not_1 (not_1_out, V);
  and and_1 (and_1_out, ~d_ff_1_q, V, d_ff_2_q);  // AND_Gate
  and and_2 (and_2_out, d_ff_1_q, ~d_ff_2_q, V);  // AND_Gate
  and and_3 (and_3_out, ~d_ff_1_q, ~d_ff_2_q, V);  // AND_Gate
  or or_1 (or_1_out, and_1_out, and_2_out);
  buf or_2 (or_2_out, and_3_out);  // OR_Gate
  D_Flip_Flop d_ff_1 (.clk(CLK), .D(or_1_out), .Q(d_ff_1_q), .Qn(d_ff_1_qn), .reset(not_1_out));  // open: preset, en
  D_Flip_Flop d_ff_2 (.clk(CLK), .D(or_2_out), .Q(d_ff_2_q), .Qn(d_ff_2_qn), .reset(not_1_out));  // open: preset, en
  and and_4 (and_4_out, d_ff_1_qn, d_ff_2_qn, V);
  and and_5 (and_5_out, d_ff_1_qn, d_ff_2_q);
  and and_6 (and_6_out, d_ff_1_q, d_ff_2_qn);
  and and_7 (and_7_out, d_ff_1_qn, d_ff_2_qn, ~V);  // AND_Gate
  or or_3 (or_3_out, and_5_out, and_6_out, and_7_out);
  and and_8 (and_8_out, and_4_out, B0);
  and and_9 (and_9_out, and_4_out, B1);
  and and_10 (and_10_out, and_4_out, B2);
  and and_11 (and_11_out, and_4_out, B3);
  or or_4 (or_4_out, and_8_out, or_3_out);
  or or_5 (or_5_out, and_9_out, or_3_out);
  or or_6 (or_6_out, and_10_out, or_3_out);
  or or_7 (or_7_out, and_11_out, or_3_out);
  D_Flip_Flop d_ff_3 (.clk(CLK), .D(or_4_out), .Q(C0));  // open: Qn, preset, en, reset
  D_Flip_Flop d_ff_4 (.clk(CLK), .D(or_5_out), .Q(C1));  // open: Qn, preset, en, reset
  D_Flip_Flop d_ff_5 (.clk(CLK), .D(or_6_out), .Q(C2));  // open: Qn, preset, en, reset
  D_Flip_Flop d_ff_6 (.clk(CLK), .D(or_7_out), .Q(C3));  // open: Qn, preset, en, reset

  // Notes on the sheet:
  //   Y1
  //   Y0
endmodule

module Lock (
  input  C0,
  input  C1,
  input  C2,
  input  C3,
  input  CLK,
  output L,
  output U
);

  wire and_1_out, and_2_out, and_3_out, and_4_out, and_5_out, and_6_out, and_7_out, and_8_out, and_9_out,
       and_10_out, and_11_out, and_12_out, and_13_out, and_14_out, and_15_out, and_16_out, and_17_out,
       and_18_out, and_19_out, and_20_out, and_26_out, and_27_out, and_28_out, and_29_out, and_30_out,
       and_31_out, and_32_out, and_33_out, and_34_out, and_35_out, and_36_out, and_37_out, and_38_out,
       and_39_out, and_40_out, and_41_out, and_42_out, and_43_out, and_44_out, and_45_out, and_46_out,
       and_47_out, and_48_out, and_49_out, and_50_out, and_51_out, and_52_out, and_53_out, and_54_out,
       and_55_out, and_56_out, and_57_out, E, i, i2, nand_1_out, nS0, nS1, nS2, nT0, nT1, nY0, nY1, nY2, nZ,
       or_1_out, or_5_out, or_6_out, or_7_out, or_8_out, or_9_out, or_10_out, or_11_out, or_12_out,
       or_14_out, S0, S1, S2, T0, T1, tunnel, xor_1_out, xor_2_out, xor_3_out, Y0, Y0_prime, Y1, Y1_prime,
       Y2, Y2_prime, Z;
  wire [3:0] D0, D1, D2, P1, P2, xnor_1_out, xnor_2_out, xnor_3_out, xnor_4_out;

  and and_1 (and_1_out, T1, Z);
  assign xnor_1_out = ~({C3, C2, C1, C0} ^ D0);  // XNOR_Gate xnor_1, 4 bits wide
  and and_2 (and_2_out, nY2, Y1, nY0, nT0);
  or or_1 (or_1_out, and_1_out, nT1);
  and and_3 (and_3_out, nY2, Y1, Y0, Z);
  and and_4 (and_4_out, nY2, nY1, Y0, nT0);
  and and_5 (and_5_out, Y2, Y1, nY0, nZ);
  and and_6 (and_6_out, xnor_1_out[0], xnor_1_out[1], xnor_1_out[2], xnor_1_out[3]);
  and and_7 (and_7_out, nY2, nY1, nT1, nT0);
  and and_8 (and_8_out, and_2_out, or_1_out);
  and and_9 (and_9_out, nY2, nY1, Y0, T1, T0);
  // Probe on {S2, S1, S0}
  nand nand_1 (nand_1_out, Y2, Y1, nY0, Z);
  and and_10 (and_10_out, nand_1_out, Y2);
  and and_11 (and_11_out, E, and_6_out);
  Register #(.width(4)) register_1 (.D(P2), .en(and_12_out), .Q(D2), .clk(CLK));  // open: clr
  and and_12 (and_12_out, tunnel, nY2, Y1, nY0, nS2, nS0, S1);
  // Probe on E
  or or_2 (Y2_prime, and_3_out, and_10_out);
  and and_13 (and_13_out, nY2, Y1, Y0, nZ);
  and and_14 (and_14_out, nY2, Y1, nY0, T1);
  and and_15 (and_15_out, Y2, nY1, Y0, T1, nT0, Z, and_11_out);
  and and_16 (and_16_out, nY2, Y1, Y0, nZ);
  and and_17 (and_17_out, Y2, nY1, nT1, T0);
  and and_18 (and_18_out, Y2, nY1, Y0, T1, nT0, nZ);
  not not_1 (nT1, T1);
  not not_2 (nT0, T0);
  or or_3 (Y0_prime, and_16_out, and_7_out, and_8_out, and_17_out, and_9_out, or_5_out);
  and and_19 (and_19_out, Y2, nY1, Y0, T1, T0);
  Register #(.width(4)) register_2 (.D(P1), .en(and_12_out), .Q(D1), .clk(CLK));  // open: clr
  and and_20 (and_20_out, C3, ~C2, C1);  // AND_Gate
  and and_21 (tunnel, T1, ~T0);  // AND_Gate
  // Probe on {L, U}
  or or_4 (Y1_prime, and_13_out, and_4_out, and_5_out, and_14_out, and_15_out);
  or or_5 (or_5_out, and_18_out, and_19_out);
  not not_3 (T1, and_20_out);
  and and_22 (T0, C3, C1, C0);
  D_Flip_Flop d_ff_1 (.clk(CLK), .D(Y2_prime), .Q(Y2), .Qn(nY2));  // open: preset, en, reset
  D_Flip_Flop d_ff_2 (.clk(CLK), .D(Y1_prime), .Q(Y1), .Qn(nY1));  // open: preset, en, reset
  D_Flip_Flop d_ff_3 (.clk(CLK), .D(Y0_prime), .Q(Y0), .Qn(nY0));  // open: preset, en, reset
  and and_23 (L, nY2, Y1, Y0);
  and and_24 (U, Y2, Y1, nY0);
  Register #(.width(4)) register_3 (.D({C3, C2, C1, C0}), .en(and_12_out), .Q(D0), .clk(CLK));  // open: clr
  and and_25 (i, T1, T0);
  xor xor_1 (xor_1_out, Y2, Y0);
  Register #(.width(4)) register_4 (.D({C3, C2, C1, C0}), .en(and_26_out), .Q(P2), .clk(CLK));  // open: clr
  and and_26 (and_26_out, tunnel, nY2, nY1, Y0);
  and and_27 (and_27_out, S1, i2);
  and and_28 (and_28_out, nY2, nY1, Y0);
  and and_29 (and_29_out, nY2, Y1, nY0, nS2, S1, nS0, tunnel);
  and and_30 (and_30_out, Y2, nY1, Y0, nS2, tunnel, nS0);
  and and_31 (and_31_out, xor_1_out, Y1, nS2, S1, nS0);
  and and_32 (and_32_out, ~Y2, Y1, Y0);  // AND_Gate
  or or_6 (or_6_out, and_32_out, and_33_out);
  and and_33 (and_33_out, Y2, Y1, ~Y0);  // AND_Gate
  and and_34 (and_34_out, nY2, Y1, nY0);
  or or_7 (or_7_out, and_34_out, and_35_out);
  and and_35 (and_35_out, Y2, nY1, Y0);
  xor xor_2 (xor_2_out, S1, S0);
  and and_36 (and_36_out, tunnel, nY2, Y1, nY0, nS2, nS1, S0);
  and and_37 (and_37_out, or_6_out, S0, S1, nS2);
  and and_38 (and_38_out, S2, i2);
  and and_39 (and_39_out, or_7_out, nS2, nS1, S0, tunnel);
  and and_40 (and_40_out, nY2, Y1, Y0, nS2, xor_2_out);
  and and_41 (and_41_out, xor_2_out, Y2, Y1, nY0, nS2);
  and and_42 (and_42_out, S0, i2);
  Register #(.width(4)) register_5 (.D({C3, C2, C1, C0}), .en(and_36_out), .Q(P1), .clk(CLK));  // open: clr
  or or_8 (or_8_out, and_37_out, and_38_out);
  or or_9 (or_9_out, and_39_out, and_27_out, and_40_out, and_41_out);
  or or_10 (or_10_out, and_28_out, and_29_out, and_30_out, and_31_out, and_42_out);
  D_Flip_Flop d_ff_4 (.clk(CLK), .D(or_8_out), .Q(S2), .Qn(nS2));  // open: preset, en, reset
  D_Flip_Flop d_ff_5 (.clk(CLK), .D(or_9_out), .Q(S1), .Qn(nS1));  // open: preset, en, reset
  D_Flip_Flop d_ff_6 (.clk(CLK), .D(or_10_out), .Q(S0), .Qn(nS0));  // open: preset, en, reset
  assign xnor_2_out = ~({C3, C2, C1, C0} ^ D0);  // XNOR_Gate xnor_2, 4 bits wide
  assign xnor_3_out = ~({C3, C2, C1, C0} ^ D1);  // XNOR_Gate xnor_3, 4 bits wide
  assign xnor_4_out = ~({C3, C2, C1, C0} ^ D2);  // XNOR_Gate xnor_4, 4 bits wide
  and and_43 (and_43_out, xnor_2_out[0], xnor_2_out[1], xnor_2_out[2], xnor_2_out[3]);
  and and_44 (and_44_out, and_43_out, S1, nS0, E);
  and and_45 (and_45_out, xnor_3_out[0], xnor_3_out[1], xnor_3_out[2], xnor_3_out[3]);
  and and_46 (and_46_out, and_45_out, nS1, S0, E);
  and and_47 (and_47_out, xnor_4_out[0], xnor_4_out[1], xnor_4_out[2], xnor_4_out[3]);
  and and_48 (and_48_out, and_47_out, nS1, nS0);
  and and_49 (and_49_out, nY2, Y1, nY0);
  and and_50 (and_50_out, Y2, nY1, Y0);
  xor xor_3 (xor_3_out, Y2, Y0);
  or or_11 (or_11_out, and_44_out, and_46_out, and_48_out);
  not not_4 (nZ, Z);
  or or_12 (or_12_out, and_49_out, and_50_out);
  and and_51 (and_51_out, or_12_out, nS2, S1, nS0);
  and and_52 (and_52_out, xor_3_out, S2, nS1, nS0, Y1);
  and and_53 (and_53_out, tunnel, Y2, nY1, Y0, nS2);
  or or_13 (Z, and_51_out, and_52_out);
  and and_54 (and_54_out, and_53_out, or_11_out);
  and and_55 (and_55_out, i, Y2, nY1, Y0, E);
  and and_56 (and_56_out, nY2, Y1, nY0, i);
  and and_57 (and_57_out, Y2, nY1, Y0, i);
  D_Flip_Flop d_ff_7 (.clk(CLK), .D(or_14_out), .Q(E));  // open: Qn, preset, en, reset
  or or_14 (or_14_out, and_54_out, and_55_out);
  or or_15 (i2, and_56_out, and_57_out);

  // Notes on the sheet:
  //   3-digit code is stored in thses 4-bit registers.
  //   This sub-circuit checks if the code is L(00), U(01), or a #(10). or invalid (11)
  //   This is the auto-counter!
  //   This sub-circuit checks if the entered three digit code matches.
  //   E = 1 when code matches in U1
endmodule
