// Logisim project Project3Given.circ as structural Verilog: 12 circuits, main circuit CPU15
module main (
  input  Enable_Breakpoint
);

  wire chipset_1_irq, CLK, clock_1_out, cpu15_1_c, cpu15_1_e, cpu15_1_i, cpu15_1_n, cpu15_1_o, cpu15_1_z,
       KBCLR, KBIRQ, KBRD, MEMCS, nand_1_out, RE, TTYCLR, TTYWE, WE;
  wire [6:0] KBDATA, TTYDATA;
  wire [7:0] cpu15_1_srf;
  wire [14:0] ADDR, chipset_1_ivect, chipset_1_led0, chipset_1_led1, chipset_1_led2, chipset_1_led3,
       chipset_1_led4, chipset_1_led5, chipset_1_led6, chipset_1_led7, chipset_1_led8, chipset_1_led9,
       chipset_1_leda, chipset_1_ledb, chipset_1_ledc, chipset_1_ledd, chipset_1_lede, cpu15_1_ib,
       cpu15_1_pc, cpu15_1_r0, cpu15_1_r1, cpu15_1_r2, cpu15_1_r3, cpu15_1_r4, cpu15_1_r5, cpu15_1_r6,
       cpu15_1_r7, cpu15_1_srp, DATA, xnor_1_out;

  Clock clock_1 (.out(clock_1_out));
  nand nand_1 (nand_1_out, Enable_Breakpoint, xnor_1_out[0], xnor_1_out[1], xnor_1_out[2], xnor_1_out[3], xnor_1_out[4], xnor_1_out[5], xnor_1_out[6], xnor_1_out[7], xnor_1_out[8], xnor_1_out[9], xnor_1_out[10], xnor_1_out[11], xnor_1_out[12], xnor_1_out[13], xnor_1_out[14], 1'b1);
  and and_1 (CLK, clock_1_out, nand_1_out);
  assign xnor_1_out = ~(15'h36 ^ cpu15_1_pc);  // XNOR_Gate xnor_1, 15 bits wide
  LED I (.in(cpu15_1_i));
  LED Z (.in(cpu15_1_z));
  LED N (.in(cpu15_1_n));
  LED O (.in(cpu15_1_o));
  LED C (.in(cpu15_1_c));
  LED E (.in(cpu15_1_e));
  // Probe on cpu15_1_pc
  // Probe on cpu15_1_ib
  // Probe on cpu15_1_srp
  // Probe on cpu15_1_srf
  // Probe on cpu15_1_r0
  // Probe on cpu15_1_r1
  // Probe on cpu15_1_r2
  // Probe on cpu15_1_r3
  // Probe on cpu15_1_r4
  // Probe on cpu15_1_r5
  // Probe on cpu15_1_r6
  // Probe on cpu15_1_r7
  CPU15 cpu15_1 (
    .I(cpu15_1_i), .Z(cpu15_1_z), .N(cpu15_1_n), .O(cpu15_1_o), .C(cpu15_1_c), .E(cpu15_1_e),
    .PC(cpu15_1_pc), .IB(cpu15_1_ib), .SRP(cpu15_1_srp), .SRF(cpu15_1_srf), .R0(cpu15_1_r0), .R1(cpu15_1_r1),
    .R2(cpu15_1_r2), .R3(cpu15_1_r3), .R4(cpu15_1_r4), .R5(cpu15_1_r5), .R6(cpu15_1_r6), .R7(cpu15_1_r7),
    .CLK(CLK), .IRQ(chipset_1_irq), .RE(RE), .WE(WE), .ADDR(ADDR), .DATAIN(DATA), .DATAOUT(DATA));
  // Probe on ADDR
  // Probe on DATA
  // Probe on chipset_1_ivect
  RAM #(.addrWidth(15), .dataWidth(15)) ram_1 (.addr(ADDR), .data(DATA), .sel(MEMCS), .clk(CLK), .ld(RE));  // open: clr
  // Probe on TTYDATA
  CHIPSET chipset_1 (
    .RE(RE), .WE(WE), .ADDR(ADDR), .CPUDATAIN(DATA), .CPUDATAOUT(DATA), .IRQ(chipset_1_irq),
    .IVECT(chipset_1_ivect), .CLK(CLK), .MEMCS(MEMCS), .TTYWR(TTYWE), .TTYCLR(TTYCLR), .TTYDATA(TTYDATA),
    .KBRD(KBRD), .KBCLR(KBCLR), .KBIRQ(KBIRQ), .KBDATA(KBDATA), .LED0(chipset_1_led0), .LED1(chipset_1_led1),
    .LED2(chipset_1_led2), .LED3(chipset_1_led3), .LED4(chipset_1_led4), .LED5(chipset_1_led5),
    .LED6(chipset_1_led6), .LED7(chipset_1_led7), .LED8(chipset_1_led8), .LED9(chipset_1_led9),
    .LEDA(chipset_1_leda), .LEDB(chipset_1_ledb), .LEDC(chipset_1_ledc), .LEDD(chipset_1_ledd),
    .LEDE(chipset_1_lede));
  TTY tty_1 (.data(TTYDATA), .clk(CLK), .we(TTYWE), .clr(TTYCLR));
  Keyboard keyboard_1 (.clk(CLK), .re(KBRD), .clr(KBCLR), .avail(KBIRQ), .data(KBDATA));
  DotMatrix #(.matrixcols(15), .matrixrows(15)) dotmatrix_1 (
    .col0(chipset_1_led0), .col1(chipset_1_led1), .col2(chipset_1_led2), .col3(chipset_1_led3),
    .col4(chipset_1_led4), .col5(chipset_1_led5), .col6(chipset_1_led6), .col7(chipset_1_led7),
    .col8(chipset_1_led8), .col9(chipset_1_led9), .col10(chipset_1_leda), .col11(chipset_1_ledb),
    .col12(chipset_1_ledc), .col13(chipset_1_ledd), .col14(chipset_1_lede));
endmodule

// CPU
module CPU15 (
  input  [14:0] DATAIN,
  input  CLK,
  input  IRQ,
  output [14:0] PC,
  output [14:0] IB,
  output [14:0] SRP,
  output [7:0] SRF,
  output [14:0] R0,
  output [14:0] R1,
  output [14:0] R2,
  output [14:0] R3,
  output [14:0] R4,
  output [14:0] R5,
  output [14:0] R6,
  output [14:0] R7,
  output RE,
  output WE,
  output I,
  output Z,
  output [14:0] ADDR,
  output N,
  output O,
  output C,
  output E,
  output [14:0] DATAOUT
);

  wire Al, all1_2_out_2, and_2_out, and_6_out, and_7_out, and_8_out, and_9_out, and_10_out, and_11_out,
       and_12_out, and_13_out, and_14_out, CPURWE, d_t, EIRQ, FD, i4, INTERRUPT, invert, multiplexer_2_out,
       multiplexer_10_out, NOP, not_2_out, or_1_out, or_2_out, rotate, RWE, WB;
  wire [2:0] Aptr, Cptr, RWA;
  wire [3:0] _4_bit, CPUIN;
  wire [4:4] F;
  wire [7:0] ALUFLAGS, CPUFLAGS, edit_flag_1_f_star, F_star, FLAGS_q, LDFIFLAGS, LIHDATA, MOVFLAGS,
       multiplexer_19_out, SRF_star, SWIFLAGS;
  wire [14:0] A, ALURESULT, B, BRPC, cla15_1_s, cla15_2_s, CPUPC1, CPURESULT, multiplexer_11_out,
       multiplexer_17_out, multiplexer_18_out, multiplexer_22_out, o2, PC1, PC_star, RWB, SRP_star,
       xnor_1_out, xnor_2_out;
  wire [14:8] LILDATA;
  wire [14:14] _0x7fff;

  not not_1 (_0x7fff[14], 1'b0);
  // Probe on PC
  Multiplexer #(.width(15), .enable("false")) multiplexer_1 (
    .in0(DATAIN), .in1(IB), .out({i4, CPUIN, Cptr, Aptr, _4_bit}), .sel(WB));
  // Probe on DATAIN
  and and_1 (NOP, ~i4, CPUIN[3], multiplexer_2_out);  // AND_Gate
  Multiplexer #(.select(3), .enable("false")) multiplexer_2 (
    .in0(1'b0), .in1(1'b0), .in2(1'b1), .in3(1'b1), .in4(1'b1), .in5(1'b1), .in6(1'b0), .in7(1'b0),
    .out(multiplexer_2_out), .sel(CPUIN[2:0]));
  // Probe on ADDR
  and and_2 (and_2_out, CPUIN[3], ~CPUIN[1], ~CPUIN[0]);  // AND_Gate
  and and_3 (EIRQ, IRQ, E);
  Multiplexer #(.width(15), .enable("false")) multiplexer_3 (
    .in0(B), .in1({{12{_4_bit[3]}}, _4_bit[2:0]}), .out(o2), .sel(and_2_out));
  and and_4 (rotate, CPUIN[2], CPUIN[3]);
  and and_5 (invert, ~CPUIN[2], CPUIN[3]);  // AND_Gate
  assign xnor_1_out = ~(IB ^ 15'h7000);  // XNOR_Gate xnor_1, 15 bits wide
  ALU alu_1 (
    .A(A), .B(o2), .PC(PC), ._15_bit_1({{14{1'b0}}, _0x7fff[14]}), ._15_bit_0({15{1'b0}}),
    ._3_bit_Instruction(CPUIN[2:0]), .FLAGS({d_t, I, Al, F[4], C, O, N, Z}), .rotate(rotate),
    .invert(invert), .RESULT(ALURESULT), .PC1(PC1), .F_star(ALUFLAGS));
  ALL1 all1_1 (.in_1(xnor_1_out));  // open: out_2
  D_Flip_Flop d_ff_1 (.clk(CLK), .D(IRQ), .Q(INTERRUPT), .Qn(E), .en(WB));  // open: preset, reset
  Register #(.width(15)) u_SRP (.D(SRP_star), .en(WB), .Q(SRP), .clk(CLK));  // open: clr
  Register u_SRF (.D(SRF_star), .en(WB), .Q(SRF), .clk(CLK));  // open: clr
  Multiplexer #(.select(4), .width(15), .enable("false")) multiplexer_4 (
    .in0({LILDATA, IB[10], IB[6:0]}), .in1({LILDATA, IB[10], IB[6:0]}), .in2(DATAIN),
    .in3({LILDATA, LIHDATA}), .in4({IB[6:0], LIHDATA}), .in5(A), .in6(PC1), .in7({15{1'b0}}),
    .in8({15{1'b0}}), .in9({LILDATA, d_t, I, Al, F[4], C, O, N, Z}), .in10(SRP), .in11({LILDATA, SRF}),
    .in12({15{1'b0}}), .in13({15{1'b0}}), .in14({15{1'b0}}), .in15({15{1'b0}}), .out(CPURESULT), .sel(CPUIN));
  T_Flip_Flop Writeback (.clk(CLK), .T(1'b1), .Q(WB), .Qn(FD));  // open: preset, reset, en
  Register #(.width(15)) u_PC (.D(PC_star), .en(WB), .Q(PC), .clk(CLK));  // open: clr
  Register FLAGS (.D(F_star), .en(WB), .Q(FLAGS_q), .clk(CLK));  // open: clr
  EDIT_Flag edit_flag_1 (.FLAGS(FLAGS_q), .BIT(3'b101), .V(1'b1), .Enable(1'b1), .F_star(edit_flag_1_f_star));
  EDIT_Flag edit_flag_2 (
    .FLAGS(edit_flag_1_f_star), .BIT(3'b110), .V(INTERRUPT), .Enable(1'b1),
    .F_star({d_t, I, Al, F[4], C, O, N, Z}));
  and and_6 (and_6_out, ~NOP, ~i4);  // AND_Gate
  Multiplexer #(.width(8), .enable("false")) multiplexer_5 (
    .in0(CPUFLAGS), .in1(ALUFLAGS), .out(F_star), .sel(and_7_out));
  and and_7 (and_7_out, ~NOP, ~i4);  // AND_Gate
  Multiplexer #(.width(15), .enable("false")) multiplexer_6 (
    .in0(CPURESULT), .in1(ALURESULT), .out(RWB), .sel(and_8_out));
  and and_8 (and_8_out, ~NOP, ~i4);  // AND_Gate
  Multiplexer #(.disabled(0)) multiplexer_7 (.in0(CPURWE), .in1(1'b1), .out(RWE), .sel(and_9_out), .en(WB));
  and and_9 (and_9_out, ~NOP, ~i4);  // AND_Gate
  Multiplexer #(.width(3), .enable("false")) multiplexer_8 (.in0(Cptr), .in1(Cptr), .out(RWA), .sel(and_6_out));
  Multiplexer #(.select(4), .enable("false")) multiplexer_9 (
    .in0(1'b1), .in1(1'b1), .in2(1'b1), .in3(1'b0), .in4(1'b1), .in5(1'b1), .in6(1'b1), .in7(1'b0),
    .in8(1'b0), .in9(_4_bit[0]), .in10(_4_bit[0]), .in11(_4_bit[0]), .in12(1'b0), .in13(1'b0), .in14(1'b0),
    .in15(1'b0), .out(CPURWE), .sel(CPUIN));
  CLA15 cla15_1 (.A(PC), .B({{9{IB[6]}}, IB[5:0]}), .S(cla15_1_s));  // open: Cin, Cout
  Multiplexer #(.select(3), .enable("false")) multiplexer_10 (
    .in0(Z), .in1(N), .in2(O), .in3(C), .in4(F[4]), .in5(Al), .in6(I), .in7(d_t), .out(multiplexer_10_out),
    .sel(Cptr));
  Multiplexer #(.width(15), .enable("false")) multiplexer_11 (
    .in0(DATAIN), .in1(15'h7000), .out(multiplexer_11_out), .sel(EIRQ));
  or or_1 (or_1_out, FD, and_10_out);
  // NAND_Gate nand_1 has open pins: in0=i4, in1=CPUIN[3], in2=CPUIN[2], out=open
  Multiplexer #(.select(4), .width(8), .enable("false")) multiplexer_12 (
    .in0({d_t, I, Al, F[4], C, O, N, Z}), .in1({d_t, I, Al, F[4], C, O, N, Z}),
    .in2({d_t, I, Al, F[4], C, O, N, Z}), .in3({d_t, I, Al, F[4], C, O, N, Z}),
    .in4({d_t, I, Al, F[4], C, O, N, Z}), .in5({d_t, I, Al, F[4], C, O, N, Z}),
    .in6({d_t, I, Al, F[4], C, O, N, Z}), .in7({d_t, I, Al, F[4], C, O, N, Z}), .in8(LDFIFLAGS),
    .in9(MOVFLAGS), .in10({d_t, I, Al, F[4], C, O, N, Z}), .in11({d_t, I, Al, F[4], C, O, N, Z}),
    .in12(SWIFLAGS), .in13(SRF), .in14({d_t, I, Al, F[4], C, O, N, Z}),
    .in15({d_t, I, Al, F[4], C, O, N, Z}), .out(CPUFLAGS), .sel(CPUIN));
  Multiplexer #(.width(15), .enable("false")) multiplexer_13 (
    .in0(PC1), .in1(cla15_1_s), .out(BRPC), .sel(multiplexer_10_out));
  R_File r_file_1 (
    .clock(CLK), .write_address(RWA), .WRITE_data(RWB), .write_enable(RWE), .in_5(Aptr), .in_6(_4_bit[3:1]),
    .D1(A), .D2(B), .R0(R0), .R1(R1), .R2(R2), .R3(R3), .R4(R4), .R5(R5), .R6(R6), .R7(R7),
    .D3({LILDATA, LIHDATA}));
  Register #(.width(15), .trigger("high")) u_IB (
    .D(multiplexer_11_out), .en(or_1_out), .Q(IB), .clk(CLK));  // open: clr
  and and_10 (and_10_out, WB, EIRQ);
  Multiplexer #(.width(15), .enable("false")) multiplexer_14 (.in0(CPUPC1), .in1(PC1), .out(PC_star), .sel(not_2_out));
  not not_2 (not_2_out, i4);
  EDIT_Flag edit_flag_3 (
    .FLAGS({d_t, I, Al, F[4], C, O, N, Z}), .BIT(Cptr), .V(_4_bit[0]), .F_star(LDFIFLAGS));  // open: Enable
  Multiplexer #(.width(8), .enable("false")) multiplexer_15 (
    .in0(A[7:0]), .in1({d_t, I, Al, F[4], C, O, N, Z}), .out(MOVFLAGS), .sel(_4_bit[0]));
  EDIT_Flag edit_flag_4 (
    .FLAGS({d_t, I, Al, F[4], C, O, N, Z}), .BIT(3'b100), .V(1'b0), .F_star(SWIFLAGS));  // open: Enable
  Multiplexer #(.select(4), .width(15), .enable("false")) multiplexer_16 (
    .in0(PC1), .in1(PC1), .in2(PC1), .in3(PC1), .in4(PC1), .in5(PC1), .in6(A), .in7(PC1), .in8(PC1),
    .in9(PC1), .in10(PC1), .in11(PC1), .in12(DATAIN), .in13(SRP), .in14(BRPC), .in15({LILDATA, LIHDATA}),
    .out(CPUPC1), .sel(CPUIN));
  // Probe on CPUIN
  and and_11 (and_11_out, ~CPUIN[3], ~CPUIN[2], CPUIN[1]);  // AND_Gate
  and and_12 (and_12_out, CPUIN[3], CPUIN[2], ~CPUIN[1]);  // AND_Gate
  and and_13 (and_13_out, CPUIN[0], WB);
  CLA15 cla15_2 (.A(A), .B({{12{IB[3]}}, IB[2:0]}), .Cin(1'b0), .S(cla15_2_s));  // open: Cout
  Multiplexer #(.width(15), .enable("false")) multiplexer_17 (
    .in0(A), .in1(SRP), .out(multiplexer_17_out), .sel(_4_bit[0]));
  Multiplexer #(.width(15), .enable("false")) multiplexer_18 (
    .in0(PC1), .in1(PC), .out(multiplexer_18_out), .sel(EIRQ));
  Multiplexer #(.width(8), .enable("false")) multiplexer_19 (
    .in0(A[7:0]), .in1(SRF), .out(multiplexer_19_out), .sel(_4_bit[0]));
  and and_14 (and_14_out, WB, i4, ~CPUIN[0], or_2_out);  // AND_Gate
  or or_2 (or_2_out, and_11_out, and_12_out);
  and and_15 (WE, i4, ~CPUIN[3], ~CPUIN[2], CPUIN[1], and_13_out);  // AND_Gate
  assign xnor_2_out = ~(IB ^ 15'h7000);  // XNOR_Gate xnor_2, 15 bits wide
  Multiplexer #(.width(15), .enable("false")) multiplexer_20 (
    .in1({LILDATA, LIHDATA}), .out(DATAOUT), .sel(WE));  // open: in0
  or or_3 (RE, FD, and_14_out);
  Multiplexer #(.width(15), .enable("false")) multiplexer_21 (.in0(multiplexer_22_out), .in1(PC), .out(ADDR), .sel(FD));
  Multiplexer #(.width(15), .enable("false")) multiplexer_22 (
    .in0(cla15_2_s), .in1({15{_0x7fff[14]}}), .out(multiplexer_22_out), .sel(all1_2_out_2));
  ALL1 all1_2 (.in_1(xnor_2_out), .out_2(all1_2_out_2));
  Multiplexer #(.select(4), .width(15), .enable("false")) multiplexer_23 (
    .in0(SRP), .in1(SRP), .in2(SRP), .in3(SRP), .in4(SRP), .in5(SRP), .in6(SRP), .in7(SRP), .in8(SRP),
    .in9(SRP), .in10(multiplexer_17_out), .in11(SRP), .in12(multiplexer_18_out), .in13(SRP), .in14(SRP),
    .in15(SRP), .out(SRP_star), .sel(CPUIN));
  Multiplexer #(.select(4), .width(8), .enable("false")) multiplexer_24 (
    .in0(SRF), .in1(SRF), .in2(SRF), .in3(SRF), .in4(SRF), .in5(SRF), .in6(SRF), .in7(SRF), .in8(SRF),
    .in9(SRF), .in10(SRF), .in11(multiplexer_19_out), .in12({d_t, I, Al, F[4], C, O, N, Z}), .in13(SRF),
    .in14(SRF), .in15(SRF), .out(SRF_star), .sel(CPUIN));

  // Other names for the same wires on the sheet: INSTR[4:0] = {i4, CPUIN}; i0 = CPUIN[0]; i1 = CPUIN[1];
  //   i2 = CPUIN[2]; LIHDATA[14:8] = IB[6:0]; LILDATA[7:0] = {IB[10], IB[6:0]}; o1[14:0] = A;
  //   _0x7fff[13:0] = {14{_0x7fff[14]}}; _1[0] = _0x7fff[14]; _4to15[14:0] = {{12{_4_bit[3]}}, _4_bit[2:0]};
  //   D = _4_bit[0]; Bptr[2:0] = _4_bit[3:1]; CPURWA[2:0] = Cptr; i3 = CPUIN[3]; DATA[14:0] = DATAIN;
  //   LDDATA[14:0] = DATAIN; ENABLED = E; RC[14:0] = {LILDATA, LIHDATA};
  //   MOVFDATA[14:0] = {LILDATA, d_t, I, Al, F[4], C, O, N, Z}; MSRFDATA[14:0] = {LILDATA, SRF};
  //   F (some bits) = {d_t, I, Al, C, O, N, Z}

  // Notes on the sheet:
  //   DATAIN: pull=down
  //   NOP instruction
  //   ADDI
  //   not NOP and ALU op
  //   not NOP and ALU op
  //   not NOP and ALU op
  //   not NOP and ALU op
endmodule

module CHIPSET (
  input  RE,
  input  WE,
  input  [14:0] ADDR,
  input  [14:0] CPUDATAIN,
  input  KBIRQ,
  input  [6:0] KBDATA,
  input  CLK,
  output MEMCS,
  output TTYWR,
  output [14:0] IVECT,
  output TTYCLR,
  output [6:0] TTYDATA,
  output KBRD,
  output KBCLR,
  output [14:0] CPUDATAOUT,
  output IRQ,
  output [14:0] LED0,
  output [14:0] LED1,
  output [14:0] LED2,
  output [14:0] LED3,
  output [14:0] LED4,
  output [14:0] LED5,
  output [14:0] LED6,
  output [14:0] LED7,
  output [14:0] LED8,
  output [14:0] LED9,
  output [14:0] LEDA,
  output [14:0] LEDB,
  output [14:0] LEDC,
  output [14:0] LEDD,
  output [14:0] LEDE
);

  wire and_1_out, and_8_out, and_10_out, DATA7, IOCS, IVECTADDR, IVECTEN, IVECTRE, KBCS, LED0EN, LED0END,
       LED1EN, LED1END, LED2EN, LED2END, LED3EN, LED3END, LED4EN, LED4END, LED5EN, LED5END, LED6EN, LED6END,
       LED7EN, LED7END, LED8EN, LED8END, LED9EN, LED9END, LEDAEN, LEDAEND, LEDBEN, LEDBEND, LEDCEN, LEDCEND,
       LEDCS, LEDDEN, LEDDEND, LEDEEN, LEDEEND, LEDFEND, LEDRE, multiplexer_17_out, multiplexer_18_out, RWE,
       TTYCS;
  wire [14:0] DATAL0, DATAL1, DATAL2, DATAL3, DATAL4, DATAL5, DATAL6, DATAL7, DATAL8, DATAL9, DATALA, DATALB,
       DATALC, DATALD, DATALE, LEDDATA;
  wire [14:8] KBDATA15;

  assign CPUDATAOUT = KBRD ? {KBDATA15, DATA7, KBDATA} : 15'bz;  // Controlled_Buffer controlled_buffer_1
  assign CPUDATAOUT = LEDRE ? LEDDATA : 15'bz;  // Controlled_Buffer controlled_buffer_2
  assign CPUDATAOUT = IVECTRE ? IVECT : 15'bz;  // Controlled_Buffer controlled_buffer_3
  Register #(.width(15)) register_1 (.D(DATAL0), .en(LED0EN), .Q(LED0), .clk(CLK));  // open: clr
  Register #(.width(15)) register_2 (.D(DATAL1), .en(LED1EN), .Q(LED1), .clk(CLK));  // open: clr
  Register #(.width(15)) register_3 (.D(DATAL2), .en(LED2EN), .Q(LED2), .clk(CLK));  // open: clr
  Register #(.width(15)) register_4 (.D(DATAL3), .en(LED3EN), .Q(LED3), .clk(CLK));  // open: clr
  Register #(.width(15)) register_5 (.D(DATAL4), .en(LED4EN), .Q(LED4), .clk(CLK));  // open: clr
  and and_1 (and_1_out, WE, LEDCS);
  Decoder #(.select(4), .disabled(0)) decoder_1 (
    .out0(LED0END), .out1(LED1END), .out2(LED2END), .out3(LED3END), .out4(LED4END), .out5(LED5END),
    .out6(LED6END), .out7(LED7END), .out8(LED8END), .out9(LED9END), .out10(LEDAEND), .out11(LEDBEND),
    .out12(LEDCEND), .out13(LEDDEND), .out14(LEDEEND), .out15(LEDFEND), .sel(ADDR[3:0]), .en(and_1_out));
  Register #(.width(15)) register_6 (.D(DATAL5), .en(LED5EN), .Q(LED5), .clk(CLK));  // open: clr
  Register #(.width(15)) register_7 (.D(DATAL6), .en(LED6EN), .Q(LED6), .clk(CLK));  // open: clr
  Register #(.width(15)) register_8 (.D(DATAL7), .en(LED7EN), .Q(LED7), .clk(CLK));  // open: clr
  Register #(.width(15)) register_9 (.D(DATAL8), .en(LED8EN), .Q(LED8), .clk(CLK));  // open: clr
  Register #(.width(15)) register_10 (.D(DATAL9), .en(LED9EN), .Q(LED9), .clk(CLK));  // open: clr
  or or_1 (LED0EN, LED0END, LEDFEND);
  or or_2 (LED1EN, LED1END, LEDFEND);
  or or_3 (LED2EN, LED2END, LEDFEND);
  or or_4 (LED3EN, LED3END, LEDFEND);
  or or_5 (LED4EN, LED4END, LEDFEND);
  or or_6 (LED5EN, LED5END, LEDFEND);
  or or_7 (LED6EN, LED6END, LEDFEND);
  or or_8 (LED7EN, LED7END, LEDFEND);
  or or_9 (LED8EN, LED8END, LEDFEND);
  or or_10 (LED9EN, LED9END, LEDFEND);
  or or_11 (LEDAEN, LEDAEND, LEDFEND);
  or or_12 (LEDBEN, LEDBEND, LEDFEND);
  or or_13 (LEDCEN, LEDCEND, LEDFEND);
  or or_14 (LEDDEN, LEDDEND, LEDFEND);
  or or_15 (LEDEEN, LEDEEND, LEDFEND);
  Pull_Resistor pull_resistor_1 (.node(KBDATA15[11]));
  Pull_Resistor pull_resistor_2 (.node(KBDATA15[12]));
  Pull_Resistor pull_resistor_3 (.node(KBDATA15[13]));
  Pull_Resistor pull_resistor_4 (.node(KBDATA15[14]));
  Pull_Resistor pull_resistor_5 (.node(KBDATA15[8]));
  Pull_Resistor pull_resistor_6 (.node(DATA7));
  Pull_Resistor pull_resistor_7 (.node(KBDATA15[9]));
  Pull_Resistor pull_resistor_8 (.node(KBDATA15[10]));
  Register #(.width(15)) register_11 (.D(DATALA), .en(LEDAEN), .Q(LEDA), .clk(CLK));  // open: clr
  Register #(.width(15)) register_12 (.D(DATALB), .en(LEDBEN), .Q(LEDB), .clk(CLK));  // open: clr
  Register #(.width(15)) register_13 (.D(DATALC), .en(LEDCEN), .Q(LEDC), .clk(CLK));  // open: clr
  Register #(.width(15)) register_14 (.D(DATALD), .en(LEDDEN), .Q(LEDD), .clk(CLK));  // open: clr
  Register #(.width(15)) register_15 (.D(DATALE), .en(LEDEEN), .Q(LEDE), .clk(CLK));  // open: clr
  Multiplexer #(.width(15), .enable("false")) multiplexer_1 (.in0(CPUDATAIN), .in1(LED1), .out(DATAL0), .sel(LEDFEND));
  Multiplexer #(.width(15), .enable("false")) multiplexer_2 (.in0(CPUDATAIN), .in1(LED2), .out(DATAL1), .sel(LEDFEND));
  Multiplexer #(.width(15), .enable("false")) multiplexer_3 (.in0(CPUDATAIN), .in1(LED3), .out(DATAL2), .sel(LEDFEND));
  Multiplexer #(.width(15), .enable("false")) multiplexer_4 (.in0(CPUDATAIN), .in1(LED4), .out(DATAL3), .sel(LEDFEND));
  Multiplexer #(.width(15), .enable("false")) multiplexer_5 (.in0(CPUDATAIN), .in1(LED5), .out(DATAL4), .sel(LEDFEND));
  Multiplexer #(.select(4), .width(15)) multiplexer_6 (
    .in0(LED0), .in1(LED1), .in2(LED2), .in3(LED3), .in4(LED4), .in5(LED5), .in6(LED6), .in7(LED7),
    .in8(LED8), .in9(LED9), .in10(LEDA), .in11(LEDB), .in12(LEDC), .in13(LEDD), .in14(LEDE),
    .in15({15{1'b0}}), .out(LEDDATA), .sel(ADDR[3:0]), .en(LEDRE));
  Multiplexer #(.width(15), .enable("false")) multiplexer_7 (.in0(CPUDATAIN), .in1(LED6), .out(DATAL5), .sel(LEDFEND));
  Multiplexer #(.width(15), .enable("false")) multiplexer_8 (.in0(CPUDATAIN), .in1(LED7), .out(DATAL6), .sel(LEDFEND));
  Multiplexer #(.width(15), .enable("false")) multiplexer_9 (.in0(CPUDATAIN), .in1(LED8), .out(DATAL7), .sel(LEDFEND));
  Multiplexer #(.width(15), .enable("false")) multiplexer_10 (.in0(CPUDATAIN), .in1(LED9), .out(DATAL8), .sel(LEDFEND));
  Multiplexer #(.width(15), .enable("false")) multiplexer_11 (.in0(CPUDATAIN), .in1(LEDA), .out(DATAL9), .sel(LEDFEND));
  and and_2 (LEDRE, RE, LEDCS);
  Multiplexer #(.width(15), .enable("false")) multiplexer_12 (.in0(CPUDATAIN), .in1(LEDB), .out(DATALA), .sel(LEDFEND));
  Multiplexer #(.width(15), .enable("false")) multiplexer_13 (.in0(CPUDATAIN), .in1(LEDC), .out(DATALB), .sel(LEDFEND));
  Multiplexer #(.width(15), .enable("false")) multiplexer_14 (.in0(CPUDATAIN), .in1(LEDD), .out(DATALC), .sel(LEDFEND));
  Multiplexer #(.width(15), .enable("false")) multiplexer_15 (.in0(CPUDATAIN), .in1(LEDE), .out(DATALD), .sel(LEDFEND));
  Multiplexer #(.width(15), .enable("false")) multiplexer_16 (
    .in0(CPUDATAIN), .in1(CPUDATAIN), .out(DATALE), .sel(LEDFEND));
  and and_3 (IOCS, ADDR[5], ADDR[6], ADDR[7], ADDR[8], ADDR[9], ADDR[10], ADDR[11], ADDR[12], ADDR[13], ADDR[14], 1'b1);
  and and_4 (TTYCS, IOCS, ADDR[0], ~ADDR[1], ~ADDR[2], ~ADDR[3], ADDR[4]);  // AND_Gate
  and and_5 (KBCS, IOCS, ~ADDR[0], ~ADDR[1], ~ADDR[2], ~ADDR[3], ADDR[4]);  // AND_Gate
  and and_6 (IVECTADDR, ADDR[0], ADDR[1], ADDR[2], ADDR[3], ADDR[4], ADDR[5], ADDR[6], ADDR[7], ADDR[8], ADDR[9], ADDR[10], ADDR[11], ADDR[12], ADDR[13], ADDR[14]);
  and and_7 (TTYWR, TTYCS, WE);
  and and_8 (and_8_out, TTYWR, DATA7);
  and and_9 (KBRD, KBCS, RE);
  and and_10 (and_10_out, KBCS, WE);
  Multiplexer #(.enable("false")) multiplexer_17 (.in0(and_10_out), .in1(1'b0), .out(multiplexer_17_out), .sel(KBCLR));
  and and_11 (LEDCS, IOCS, ~ADDR[4], RWE);  // AND_Gate
  and and_12 (IVECTEN, IVECTADDR, WE);
  and and_13 (IVECTRE, IVECTADDR, RE);
  or or_16 (RWE, RE, WE);
  and and_14 (MEMCS, ~IOCS, RWE);  // AND_Gate
  Multiplexer #(.enable("false")) multiplexer_18 (.in0(and_8_out), .in1(1'b0), .out(multiplexer_18_out), .sel(TTYCLR));
  D_Flip_Flop d_ff_1 (.clk(CLK), .D(multiplexer_17_out), .Q(KBCLR));  // open: Qn, preset, en, reset
  Register #(.width(15)) register_16 (.D(CPUDATAIN), .en(IVECTEN), .Q(IVECT), .clk(CLK));  // open: clr
  D_Flip_Flop d_ff_2 (.clk(CLK), .D(multiplexer_18_out), .Q(TTYCLR));  // open: Qn, preset, en, reset

  assign IRQ = KBIRQ;
  assign TTYDATA = CPUDATAIN[6:0];

  // Other names for the same wires on the sheet: DATA[14:0] = CPUDATAIN; KBDATA15[7:0] = {DATA7, KBDATA}
endmodule

module ALU (
  input  [14:0] A,
  input  [14:0] B,
  input  [14:0] PC,
  input  [14:0] _15_bit_1,
  input  [14:0] _15_bit_0,
  input  [2:0] _3_bit_Instruction,
  input  [7:0] FLAGS,
  input  rotate,
  input  invert,
  output [14:0] RESULT,
  output [14:0] PC1,
  output [7:0] F_star
);

  wire add_o, ADDC, and_2_out, and_3_out, and_4_out, and_5_out, and_6_out, and_7_out, sub_o, SUBC,
       zn_2_negative, zn_3_negative, zn_4_negative, zn_5_negative, zn_6_negative, zn_7_negative,
       zn_8_negative, zn_9_negative, zn_10_negative, zn_11_negative, zn_12_negative, zn_13_negative;
  wire [0:0] LEFT;
  wire [14:0] ADD, AND, NOT, not_1_out, OR, SUB, XOR;
  wire [14:14] RIGHT;

  CLA15 cla15_1 (.A(PC), .B(_15_bit_1), .Cin(1'b0), .S(PC1));  // open: Cout
  assign not_1_out = ~B;  // NOT_Gate not_1, 15 bits wide
  Multiplexer #(.enable("false")) multiplexer_1 (.in0(A[14]), .in1(FLAGS[3]), .out(RIGHT[14]), .sel(rotate));
  // Probe on ADD
  CLA15 cla15_2 (.A(A), .B(B), .Cin(1'b0), .S(ADD), .Cout(ADDC));
  CLA15 cla15_3 (.A(A), .B(not_1_out), .Cin(1'b1), .S(SUB), .Cout(SUBC));
  assign AND = A & B;  // AND_Gate and, 15 bits wide
  assign OR = A | B;  // OR_Gate or, 15 bits wide
  assign XOR = A ^ B;  // XOR_Gate xor, 15 bits wide
  assign NOT = ~A;  // NOT_Gate not_2, 15 bits wide
  Multiplexer #(.enable("false")) multiplexer_2 (.in0(1'b0), .in1(FLAGS[3]), .out(LEFT[0]), .sel(rotate));
  and and_2 (and_2_out, SUBC, ~invert);  // AND_Gate
  Multiplexer #(.select(3), .width(15), .enable("false")) multiplexer_3 (
    .in0(ADD), .in1(SUB), .in2(AND), .in3(OR), .in4(XOR), .in5(NOT), .in6({RIGHT[14], A[14:1]}),
    .in7({A[13:0], LEFT[0]}), .out(RESULT), .sel(_3_bit_Instruction));
  Multiplexer #(.select(3), .enable("false")) multiplexer_4 (
    .in0(ADDC), .in1(and_2_out), .in2(FLAGS[3]), .in3(FLAGS[3]), .in4(FLAGS[3]), .in5(FLAGS[3]), .in6(A[0]),
    .in7(A[14]), .out(F_star[3]), .sel(_3_bit_Instruction));
  ZN zn_1 (.A(RESULT), .zero(F_star[0]), .negative(F_star[1]));
  ZN zn_2 (.A(A), .negative(zn_2_negative));  // open: zero
  ZN zn_3 (.A(B), .negative(zn_3_negative));  // open: zero
  ZN zn_4 (.A(ADD), .negative(zn_4_negative));  // open: zero
  ZN zn_5 (.A(A), .negative(zn_5_negative));  // open: zero
  ZN zn_6 (.A(B), .negative(zn_6_negative));  // open: zero
  ZN zn_7 (.A(ADD), .negative(zn_7_negative));  // open: zero
  ZN zn_8 (.A(A), .negative(zn_8_negative));  // open: zero
  ZN zn_9 (.A(B), .negative(zn_9_negative));  // open: zero
  ZN zn_10 (.A(SUB), .negative(zn_10_negative));  // open: zero
  ZN zn_11 (.A(A), .negative(zn_11_negative));  // open: zero
  ZN zn_12 (.A(B), .negative(zn_12_negative));  // open: zero
  ZN zn_13 (.A(SUB), .negative(zn_13_negative));  // open: zero
  and and_3 (and_3_out, zn_2_negative, zn_3_negative, ~zn_4_negative);  // AND_Gate
  or or_2 (add_o, and_3_out, and_4_out);
  and and_4 (and_4_out, ~zn_5_negative, ~zn_6_negative, zn_7_negative);  // AND_Gate
  and and_5 (and_5_out, ~zn_8_negative, zn_9_negative, zn_10_negative);  // AND_Gate
  or or_3 (sub_o, and_5_out, and_6_out);
  and and_6 (and_6_out, zn_11_negative, ~zn_12_negative, ~zn_13_negative);  // AND_Gate
  and and_7 (and_7_out, sub_o, ~invert);  // AND_Gate
  Multiplexer #(.select(3), .enable("false")) multiplexer_5 (
    .in0(add_o), .in1(and_7_out), .in2(FLAGS[2]), .in3(FLAGS[2]), .in4(FLAGS[2]), .in5(FLAGS[2]),
    .in6(FLAGS[2]), .in7(FLAGS[2]), .out(F_star[2]), .sel(_3_bit_Instruction));

  assign F_star[7:4] = FLAGS[7:4];

  // Other names for the same wires on the sheet: _0[14:0] = _15_bit_0; _1[14:0] = _15_bit_1; F[7:0] = FLAGS;
  //   Z = FLAGS[0]; N = FLAGS[1]; O = FLAGS[2]; C = FLAGS[3]; z_t = F_star[0]; n_t = F_star[1]; o_t = F_star[2];
  //   c_t = F_star[3]; E = FLAGS[4]; Al = FLAGS[5]; I = FLAGS[6]; d = FLAGS[7]; i_t[2:0] = _3_bit_Instruction;
  //   inv = invert; cr = A[0]; LEFT[14:1] = A[13:0]; RIGHT[13:0] = A[14:1]; r = rotate; cl = A[14]

  // Notes on the sheet:
  //   rotate: pull=down
  //   invert: pull=down
  //   ALU
  //   PC + 1
  //   ADD
  //   SUB
  //   right
  //   left
endmodule

module CLA5 (
  input  [4:0] A,
  input  [4:0] B,
  input  Cin,
  output [4:0] S,
  output Cout
);

  wire and_1_out, and_2_out, and_3_out, and_4_out, and_5_out, and_6_out, and_7_out, and_8_out, and_9_out,
       and_10_out, and_11_out, and_12_out, and_13_out, and_14_out, and_15_out, C0, C1, C2, C3, G0, G1, G2,
       G3, G4, P0, P1, P2, P3, P4;

  PG pg_1 (.A(A[0]), .B(B[0]), .P(P0), .G(G0));
  PG pg_2 (.A(A[1]), .B(B[1]), .P(P1), .G(G1));
  PG pg_3 (.A(A[2]), .B(B[2]), .P(P2), .G(G2));
  PG pg_4 (.A(A[3]), .B(B[3]), .P(P3), .G(G3));
  PG pg_5 (.A(A[4]), .B(B[4]), .P(P4), .G(G4));
  and and_1 (and_1_out, P0, Cin);
  and and_2 (and_2_out, P1, G0);
  and and_3 (and_3_out, P1, Cin, P0);
  and and_4 (and_4_out, P2, G1);
  and and_5 (and_5_out, P1, G0, P2);
  and and_6 (and_6_out, P1, Cin, P0, P2);
  and and_7 (and_7_out, P3, G2);
  and and_8 (and_8_out, P3, G1, P2);
  and and_9 (and_9_out, P1, G0, P3, P2);
  and and_10 (and_10_out, P1, Cin, P0, P3, P2);
  or or_1 (C0, G0, and_1_out);
  or or_2 (C1, G1, and_2_out, and_3_out);
  or or_3 (C2, G2, and_4_out, and_5_out, and_6_out);
  or or_4 (C3, G3, and_7_out, and_8_out, and_9_out, and_10_out);
  and and_11 (and_11_out, P4, G3);
  and and_12 (and_12_out, P3, G2, P4);
  and and_13 (and_13_out, P4, G1, P3, P2);
  and and_14 (and_14_out, P1, G0, P4, P3, P2);
  and and_15 (and_15_out, P1, Cin, P4, P0, P3, P2);
  or or_5 (Cout, G4, and_11_out, and_12_out, and_13_out, and_14_out, and_15_out);
  xor xor_1 (S[0], P0, Cin);
  xor xor_2 (S[1], P1, C0);
  xor xor_3 (S[2], P2, C1);
  xor xor_4 (S[3], P3, C2);
  xor xor_5 (S[4], P4, C3);

  // Other names for the same wires on the sheet: C4 = Cout

  // Notes on the sheet:
  //   5-bit Carry-Lookahead Adder
endmodule

module _1BFA (
  input  A,
  input  B,
  input  Cin,
  output S,
  output Cout
);

  wire and_1_out, and_2_out, xor_1_out;

  xor xor_1 (xor_1_out, A, B);
  and and_1 (and_1_out, xor_1_out, Cin);
  xor xor_2 (S, Cin, xor_1_out);
  and and_2 (and_2_out, A, B);
  or or_1 (Cout, and_1_out, and_2_out);

  // Notes on the sheet:
  //   1 bit Full Adder
endmodule

module PG (
  input  A,
  input  B,
  output P,
  output G
);

  xor xor_1 (P, A, B);
  and and_1 (G, A, B);

  // Notes on the sheet:
  //   Calculate Propogate & Generate
endmodule

// CLA
module CLA15 (
  input  [14:0] A,
  input  [14:0] B,
  input  Cin,
  output [14:0] S,
  output Cout
);

  wire cla5_1_cout, cla5_2_cout;

  CLA5 cla5_1 (.A(A[4:0]), .B(B[4:0]), .Cin(Cin), .S(S[4:0]), .Cout(cla5_1_cout));
  CLA5 cla5_2 (.A(A[9:5]), .B(B[9:5]), .Cin(cla5_1_cout), .S(S[9:5]), .Cout(cla5_2_cout));
  CLA5 cla5_3 (.A(A[14:10]), .B(B[14:10]), .Cin(cla5_2_cout), .S(S[14:10]), .Cout(Cout));

  // Notes on the sheet:
  //   Cin: pull=down
endmodule

module ZN (
  input  [14:0] A,
  output zero,
  output negative
);

  nor nor_1 (zero, A[0], A[1], A[2], A[3], A[4], A[5], A[6], A[7], A[8], A[9], A[10], A[11], A[12], A[13], A[14]);

  assign negative = A[14];
endmodule

// REGISTERS
module R_File (
  input  clock,
  input  [2:0] write_address,
  input  [14:0] WRITE_data,
  input  write_enable,
  input  [2:0] in_5,
  input  [2:0] in_6,
  output [14:0] R0,
  output [14:0] R1,
  output [14:0] R2,
  output [14:0] R3,
  output [14:0] D1,
  output [14:0] R4,
  output [14:0] R5,
  output [14:0] R6,
  output [14:0] R7,
  output [14:0] D2,
  output [14:0] D3
);

  wire and_1_out, and_2_out, and_3_out, and_4_out, and_5_out, and_6_out, and_7_out, and_8_out;
  wire [2:0] xnor_1_out, xnor_2_out, xnor_3_out, xnor_4_out, xnor_5_out, xnor_6_out, xnor_7_out, xnor_8_out;
  wire [14:0] _1, _2, _3, _4, _5, _6, _7, _8;

  Multiplexer #(.select(3), .width(15), .enable("false")) multiplexer_1 (
    .in0(R0), .in1(R1), .in2(R2), .in3(R3), .in4(R4), .in5(R5), .in6(R6), .in7(R7), .out(D1), .sel(in_5));
  Multiplexer #(.select(3), .width(15), .enable("false")) multiplexer_2 (
    .in0(R0), .in1(R1), .in2(R2), .in3(R3), .in4(R4), .in5(R5), .in6(R6), .in7(R7), .out(D2), .sel(in_6));
  Register #(.width(15)) register_1 (.D(_1), .en(write_enable), .Q(R0), .clk(clock));  // open: clr
  Register #(.width(15)) register_2 (.D(_5), .en(write_enable), .Q(R4), .clk(clock));  // open: clr
  Register #(.width(15)) register_3 (.D(_2), .en(write_enable), .Q(R1), .clk(clock));  // open: clr
  Register #(.width(15)) register_4 (.D(_6), .en(write_enable), .Q(R5), .clk(clock));  // open: clr
  Multiplexer #(.select(3), .width(15), .enable("false")) multiplexer_3 (
    .in0(R0), .in1(R1), .in2(R2), .in3(R3), .in4(R4), .in5(R5), .in6(R6), .in7(R7), .out(D3),
    .sel(write_address));
  Register #(.width(15)) register_5 (.D(_3), .en(write_enable), .Q(R2), .clk(clock));  // open: clr
  Register #(.width(15)) register_6 (.D(_7), .en(write_enable), .Q(R6), .clk(clock));  // open: clr
  Register #(.width(15)) register_7 (.D(_4), .en(write_enable), .Q(R3), .clk(clock));  // open: clr
  Register #(.width(15)) register_8 (.D(_8), .en(write_enable), .Q(R7), .clk(clock));  // open: clr
  and and_1 (and_1_out, xnor_1_out[0], xnor_1_out[1], xnor_1_out[2]);
  assign xnor_1_out = ~(write_address ^ 3'b000);  // XNOR_Gate xnor_1, 3 bits wide
  and and_2 (and_2_out, xnor_2_out[0], xnor_2_out[1], xnor_2_out[2]);
  assign xnor_2_out = ~(write_address ^ 3'b010);  // XNOR_Gate xnor_2, 3 bits wide
  and and_3 (and_3_out, xnor_3_out[0], xnor_3_out[1], xnor_3_out[2]);
  assign xnor_3_out = ~(write_address ^ 3'b100);  // XNOR_Gate xnor_3, 3 bits wide
  Multiplexer #(.width(15), .enable("false")) multiplexer_4 (.in0(R6), .in1(WRITE_data), .out(_7), .sel(and_4_out));
  and and_4 (and_4_out, xnor_4_out[0], xnor_4_out[1], xnor_4_out[2]);
  assign xnor_4_out = ~(write_address ^ 3'b110);  // XNOR_Gate xnor_4, 3 bits wide
  Multiplexer #(.width(15), .enable("false")) multiplexer_5 (.in0(R0), .in1(WRITE_data), .out(_1), .sel(and_1_out));
  Multiplexer #(.width(15), .enable("false")) multiplexer_6 (.in0(R2), .in1(WRITE_data), .out(_3), .sel(and_2_out));
  Multiplexer #(.width(15), .enable("false")) multiplexer_7 (.in0(R4), .in1(WRITE_data), .out(_5), .sel(and_3_out));
  assign xnor_5_out = ~(write_address ^ 3'b001);  // XNOR_Gate xnor_5, 3 bits wide
  assign xnor_6_out = ~(write_address ^ 3'b011);  // XNOR_Gate xnor_6, 3 bits wide
  assign xnor_7_out = ~(write_address ^ 3'b101);  // XNOR_Gate xnor_7, 3 bits wide
  and and_5 (and_5_out, xnor_8_out[0], xnor_8_out[1], xnor_8_out[2]);
  assign xnor_8_out = ~(write_address ^ 3'b111);  // XNOR_Gate xnor_8, 3 bits wide
  Multiplexer #(.width(15), .enable("false")) multiplexer_8 (.in0(R1), .in1(WRITE_data), .out(_2), .sel(and_6_out));
  and and_6 (and_6_out, xnor_5_out[0], xnor_5_out[1], xnor_5_out[2]);
  Multiplexer #(.width(15), .enable("false")) multiplexer_9 (.in0(R3), .in1(WRITE_data), .out(_4), .sel(and_7_out));
  and and_7 (and_7_out, xnor_6_out[0], xnor_6_out[1], xnor_6_out[2]);
  Multiplexer #(.width(15), .enable("false")) multiplexer_10 (.in0(R5), .in1(WRITE_data), .out(_6), .sel(and_8_out));
  and and_8 (and_8_out, xnor_7_out[0], xnor_7_out[1], xnor_7_out[2]);
  Multiplexer #(.width(15), .enable("false")) multiplexer_11 (.in0(R7), .in1(WRITE_data), .out(_8), .sel(and_5_out));

  // Other names for the same wires on the sheet: CLK = clock; RADDR1[2:0] = in_5; RADDR2[2:0] = in_6;
  //   W[14:0] = WRITE_data; WADDR[2:0] = write_address; WE = write_enable

  // Notes on the sheet:
  //   in_6: pull=down
  //   write_address: pull=down
  //   write_enable: pull=down
  //   WRITE_data: pull=down
  //   000
  //   100
  //   001
  //   101
  //   010
  //   110
  //   011
  //   111
endmodule

// EDIT FLAGS
module EDIT_Flag (
  input  [7:0] FLAGS,
  input  [2:0] BIT,
  input  V,
  input  Enable,
  output [7:0] F_star
);

  wire and_9_out, and_10_out, and_11_out, and_12_out, and_13_out, and_14_out, and_15_out, and_16_out,
       and_17_out, and_18_out, and_19_out, and_20_out, and_21_out, and_22_out, and_23_out, and_24_out,
       demultiplexer_1_out0, demultiplexer_1_out1, demultiplexer_1_out2, demultiplexer_1_out3,
       demultiplexer_1_out4, demultiplexer_1_out5, demultiplexer_1_out6, demultiplexer_1_out7, s0, s1, s2,
       s3, s4, s5, s6, s7;

  Demultiplexer #(.select(3), .disabled(0), .enable("false")) demultiplexer_1 (
    .out0(demultiplexer_1_out0), .out1(demultiplexer_1_out1), .out2(demultiplexer_1_out2),
    .out3(demultiplexer_1_out3), .out4(demultiplexer_1_out4), .out5(demultiplexer_1_out5),
    .out6(demultiplexer_1_out6), .out7(demultiplexer_1_out7), .in(1'b1), .sel(BIT));
  and and_1 (s0, Enable, demultiplexer_1_out0);
  and and_2 (s1, Enable, demultiplexer_1_out1);
  and and_3 (s2, Enable, demultiplexer_1_out2);
  and and_4 (s3, Enable, demultiplexer_1_out3);
  and and_5 (s4, Enable, demultiplexer_1_out4);
  and and_6 (s5, Enable, demultiplexer_1_out5);
  and and_7 (s6, Enable, demultiplexer_1_out6);
  and and_8 (s7, Enable, demultiplexer_1_out7);
  and and_9 (and_9_out, s0, V);
  and and_10 (and_10_out, ~s0, FLAGS[0]);  // AND_Gate
  and and_11 (and_11_out, s1, V);
  and and_12 (and_12_out, ~s1, FLAGS[1]);  // AND_Gate
  and and_13 (and_13_out, s2, V);
  and and_14 (and_14_out, ~s2, FLAGS[2]);  // AND_Gate
  and and_15 (and_15_out, s3, V);
  and and_16 (and_16_out, ~s3, FLAGS[3]);  // AND_Gate
  and and_17 (and_17_out, s4, V);
  and and_18 (and_18_out, ~s4, FLAGS[4]);  // AND_Gate
  and and_19 (and_19_out, s5, V);
  and and_20 (and_20_out, ~s5, FLAGS[5]);  // AND_Gate
  and and_21 (and_21_out, s6, V);
  and and_22 (and_22_out, ~s6, FLAGS[6]);  // AND_Gate
  and and_23 (and_23_out, s7, V);
  and and_24 (and_24_out, ~s7, FLAGS[7]);  // AND_Gate
  or or_1 (F_star[0], and_9_out, and_10_out);
  or or_2 (F_star[1], and_11_out, and_12_out);
  or or_3 (F_star[2], and_13_out, and_14_out);
  or or_4 (F_star[3], and_15_out, and_16_out);
  or or_5 (F_star[4], and_17_out, and_18_out);
  or or_6 (F_star[5], and_19_out, and_20_out);
  or or_7 (F_star[6], and_21_out, and_22_out);
  or or_8 (F_star[7], and_23_out, and_24_out);

  // Other names for the same wires on the sheet: b1 = BIT[0]; b2 = BIT[1]; b3 = BIT[2]; E = Enable; F[7:0] = FLAGS

  // Notes on the sheet:
  //   Enable: pull=up
endmodule

module ALL1 (
  input  [14:0] in_1,
  output out_2
);

  and and_1 (out_2, in_1[0], in_1[1], in_1[2], in_1[3], in_1[4], in_1[5], in_1[6], in_1[7], in_1[8], in_1[9], in_1[10], in_1[11], in_1[12], in_1[13], in_1[14]);
endmodule
