// Logisim project P4-03-14-6pm.circ as structural Verilog: 24 circuits, main circuit NIC
module main (
  input  En_Noise
);

  wire CLK, keyboard_1_avail, multiplexer_1_out, nic_1_minus_int, nic_1_tx, noisychannel_1_out,
       terminalcontroller_1_cs, terminalcontroller_1_kben, terminalcontroller_1_o,
       terminalcontroller_1_ttyen, terminalcontroller_1_w;
  wire [1:0] terminalcontroller_1_addr;
  wire [6:0] keyboard_1_data, terminalcontroller_1_ttydata;
  wire [7:0] nic_1_dataout, terminalcontroller_1_dataout, terminalcontroller_1_status;

  TTY tty_1 (.data(terminalcontroller_1_ttydata), .clk(CLK), .we(terminalcontroller_1_ttyen));  // open: clr
  Keyboard keyboard_1 (
    .clk(CLK), .re(terminalcontroller_1_kben), .avail(keyboard_1_avail), .data(keyboard_1_data));  // open: clr
  LED DR (.in(terminalcontroller_1_status[1]));
  LED TBNF (.in(terminalcontroller_1_status[2]));
  LED TXI (.in(terminalcontroller_1_status[3]));
  LED NF (.in(terminalcontroller_1_status[4]));
  LED OR (.in(terminalcontroller_1_status[5]));
  LED SDE (.in(terminalcontroller_1_status[6]));
  LED FE (.in(terminalcontroller_1_status[7]));
  Clock clock_1 (.out(CLK));
  TerminalController terminalcontroller_1 (
    .TTYEN(terminalcontroller_1_ttyen), .TTYDATA(terminalcontroller_1_ttydata),
    .STATUS(terminalcontroller_1_status), .KBEN(terminalcontroller_1_kben), .KBRDY(keyboard_1_avail),
    .KBDATA(keyboard_1_data), .CLK(CLK), .DIV(4'b0011), .INT(nic_1_minus_int), .CS(terminalcontroller_1_cs),
    .O(terminalcontroller_1_o), .W(terminalcontroller_1_w), .ADDR(terminalcontroller_1_addr),
    .DATAOUT(terminalcontroller_1_dataout), .DATAIN(nic_1_dataout));
  NIC nic_1 (
    .minus_INT(nic_1_minus_int), .minus_CS(terminalcontroller_1_cs), .minus_O(terminalcontroller_1_o),
    .minus_W(terminalcontroller_1_w), .ADDR(terminalcontroller_1_addr),
    .DATAIN(terminalcontroller_1_dataout), .DATAOUT(nic_1_dataout), .CLK(CLK), .TX(nic_1_tx),
    .RX(multiplexer_1_out));
  Shift_Register #(.length(32)) shift_register_1 (
    .in(nic_1_tx), .clk(CLK));  // open: shift, out, load, clr, d0, q0, d1, q1, d2, q2, d3, q3, d4, q4, d5, q5, d6, q6, d7, q7, d8, q8, d9, q9, d10, q10, d11, q11, d12, q12, d13, q13, d14, q14, d15, q15, d16, q16, d17, q17, d18, q18, d19, q19, d20, q20, d21, q21, d22, q22, d23, q23, d24, q24, d25, q25, d26, q26, d27, q27, d28, q28, d29, q29, d30, q30, d31, q31
  Shift_Register #(.length(32)) shift_register_2 (
    .in(multiplexer_1_out), .clk(CLK));  // open: shift, out, load, clr, d0, q0, d1, q1, d2, q2, d3, q3, d4, q4, d5, q5, d6, q6, d7, q7, d8, q8, d9, q9, d10, q10, d11, q11, d12, q12, d13, q13, d14, q14, d15, q15, d16, q16, d17, q17, d18, q18, d19, q19, d20, q20, d21, q21, d22, q22, d23, q23, d24, q24, d25, q25, d26, q26, d27, q27, d28, q28, d29, q29, d30, q30, d31, q31
  NoisyChannel noisychannel_1 (.In(nic_1_tx), .Rate(16'h800), .CLK(CLK), .Out(noisychannel_1_out));
  Multiplexer #(.enable("false")) multiplexer_1 (
    .in0(nic_1_tx), .in1(noisychannel_1_out), .out(multiplexer_1_out), .sel(En_Noise));

  // Notes on the sheet:
  //   Div
  //   Main of Rosalia Dupont and Dhawal Majithia
  //   Noise Rate
endmodule

module TerminalController (
  input  KBRDY,
  input  [6:0] KBDATA,
  input  INT,
  input  [7:0] DATAIN,
  input  CLK,
  input  [3:0] DIV,
  output KBEN,
  output CS,
  output O,
  output TTYEN,
  output W,
  output [6:0] TTYDATA,
  output [1:0] ADDR,
  output [7:0] STATUS,
  output [7:0] DATAOUT
);

  wire DOCHECKS, JMP, not_4_out, not_5_out, not_6_out, STATUSEN, TF, TTYDATAOUTSEL, TTYENP;
  wire [1:0] and_2_out, DATAOUTSEL;
  wire [7:0] DATABUSBYTE, INST, JUMPTARGET, multiplexer_1_out, multiplexer_3_out;
  wire [7:7] multiplexer_2_out;
  wire [23:11] rom_1_data;

  ROM #(.dataWidth(24)) rom_1 (
    .addr(INST),
    .data({rom_1_data[23:21], ADDR, KBEN, TTYENP, DATAOUTSEL, TTYDATAOUTSEL, rom_1_data[13:11], DOCHECKS, STATUSEN, JMP, DATABUSBYTE}),
    .sel(1'b1));
  not not_1 (W, rom_1_data[21]);
  not not_2 (O, rom_1_data[22]);
  not not_3 (CS, rom_1_data[23]);
  Multiplexer #(.select(2), .width(8), .enable("false")) multiplexer_1 (
    .in0({4'b0000, DIV}), .in1(DATABUSBYTE), .in2({1'b1, KBDATA}), .in3({8{1'b0}}), .out(multiplexer_1_out),
    .sel(DATAOUTSEL));
  assign DATAOUT = not_4_out ? multiplexer_1_out : 8'bz;  // Controlled_Buffer controlled_buffer_1
  not not_4 (not_4_out, W);
  Multiplexer #(.width(8), .enable("false")) multiplexer_2 (
    .in0(DATAIN), .in1(DATABUSBYTE), .out({multiplexer_2_out[7], TTYDATA}), .sel(TTYDATAOUTSEL));
  and and_1 (TTYEN, multiplexer_2_out[7], TTYENP);
  Counter counter_1 (.load(JMP), .D(JUMPTARGET), .count(not_5_out), .Q(INST), .clk(CLK));  // open: carry, clr
  not not_5 (not_5_out, JMP);
  Multiplexer #(.width(8), .enable("false")) multiplexer_3 (
    .in0(8'h20), .in1(8'h30), .out(multiplexer_3_out), .sel(TF));
  and and_2 (and_2_out[0], KBRDY, DOCHECKS);
  and and_3 (and_2_out[1], DOCHECKS, not_6_out);
  not not_6 (not_6_out, INT);
  Comparator #(.width(7), .mode("unsigned")) comparator_1 (.a(KBDATA), .b(7'b0001010), .eq(TF));  // open: gt, lt
  Register register_1 (.D(DATAIN), .en(STATUSEN), .Q(STATUS), .clk(CLK));  // open: clr
  Multiplexer #(.select(2), .width(8), .enable("false")) multiplexer_4 (
    .in0(DATABUSBYTE), .in1(multiplexer_3_out), .in2(8'h10), .in3(8'h10), .out(JUMPTARGET), .sel(and_2_out));

  // Other names for the same wires on the sheet: KBDATABUSBYTE[6:0] = KBDATA

  // Notes on the sheet:
  //   contents of rom_1 (hex, n*v repeats v):
  //   0 b80000 b80000 0 a88002 a88002 0 a08001 a08001 0 c00000 c00000 c00200 509 0 0 d00000 d00000 d20000
  //   109 12*0 b10000 b10000 b10000 40000 109 11*0 b10000 b10000 b10000 40000 a08003 a08003 109
endmodule

module NIC (
  input  minus_CS,
  input  minus_O,
  input  minus_W,
  input  RX,
  input  [1:0] ADDR,
  input  [7:0] DATAIN,
  input  CLK,
  output minus_INT,
  output TX,
  output [7:0] DATAOUT
);

  wire and_2_out, and_3_out, and_4_out, and_5_out, and_6_out, and_7_out, and_8_out, and_9_out, and_10_out,
       BRD_WRITEENABLE, BYTECOUNT, CLK_t, clock_2_out, comparator_1_lt, comparator_2_gt, CS, d_ff_1_qn,
       d_ff_2_qn, DATA_WRITEENABLE, demultiplexer_2_out13, DR, DRIM, ENA, ENA_IN, FE, FE_W, FEC, FEIM,
       IM_WRITEENABLE, INT, multiplexer_9_out, nand_1_out, nand_2_out, NF, NF_W, NFC, not_1_out, not_8_out,
       O, Oold, OR, or_2_out, or_3_out, or_4_out, or_5_out, or_6_out, or_7_out, OR_W, ORC, READold,
       SC_WRITEENABLE, SHOULDTRANSMIT, TBF, TF, TF_W, TIDLE, TTX, TXBUFFEREMPTY, TXIO, undriven, W, WRITE;
  wire [6:0] IM, multiplexer_3_out;
  wire [6:1] SCIN;
  wire [6:2] SC;
  wire [6:6] SC_W;
  wire [7:0] and_1_out, BRD, BRD_W, DATA_FROM_RX, DATA_W, edit_register_1_updated_8_bits, IM_star, IM_W,
       INTERRUPT_MASKS_q, multiplexer_2_out, not_6_out, SC_star, TXBUFFER, UPDATE_VALS;
  wire [15:8] WORDIN;

  Demultiplexer #(.select(2), .width(8), .enable("false")) demultiplexer_1 (
    .out0({FEC, SCIN[6], ORC, NFC, SCIN[3:1], ENA_IN}), .out1(IM_W), .out2(DATA_W), .out3(BRD_W),
    .in(DATAIN), .sel(ADDR));
  Multiplexer #(.width(8), .enable("false")) multiplexer_1 (.in1(UPDATE_VALS), .out(DATAOUT), .sel(O));  // open: in0
  Multiplexer #(.width(8), .enable("false")) multiplexer_2 (
    .in0({FE, SC[6], OR, NF, SC[3:2], DR, ENA}), .in1({FE_W, SC_W[6], OR_W, NF_W, SC[3:2], DR, ENA_IN}),
    .out(multiplexer_2_out), .sel(SC_WRITEENABLE));
  assign and_1_out = {FEIM, IM[6:2], DRIM, IM[0]} & {FE, SC[6], OR, NF, SC[3:2], DR, ENA};  // AND_Gate and_1, 8 bits wide
  Clock clock_1 (.out(CLK_t));
  edit_register edit_register_1 (
    ._8_bit(multiplexer_2_out), .BIT(3'b011), .V(TIDLE), .Enable(1'b1),
    .updated_8_bits(edit_register_1_updated_8_bits));
  not not_1 (not_1_out, TBF);
  edit_register edit_register_2 (
    ._8_bit(IM_star), .BIT(3'b000), .V(1'b0), .Enable(1'b1), .updated_8_bits({FEIM, IM[6:2], DRIM, IM[0]}));
  not not_2 (minus_INT, INT);
  not not_3 (CS, minus_CS);
  not not_4 (O, minus_O);
  not not_5 (W, minus_W);
  edit_register edit_register_3 (
    ._8_bit(edit_register_1_updated_8_bits), .BIT(3'b010), .V(not_1_out), .Enable(1'b1),
    .updated_8_bits(SC_star));
  or or_1 (INT, and_1_out[0], and_1_out[1], and_1_out[2], and_1_out[3], and_1_out[4], and_1_out[5], and_1_out[6], and_1_out[7]);
  Multiplexer #(.width(7)) multiplexer_3 (
    .in0(7'b0110000), .in1(7'b0110001), .out(multiplexer_3_out), .sel(TX));  // open: en
  Clock clock_2 (.out(clock_2_out));
  TTY #(.rows(45), .cols(6)) tty_1 (.data(multiplexer_3_out), .clk(clock_2_out));  // open: we, clr
  Register STATUS_COMMAND (
    .D(SC_star), .en(undriven), .Q({FE, SC[6], OR, NF, SC[3:2], DR, ENA}), .clk(CLK_t));  // open: clr
  Multiplexer #(.enable("false")) multiplexer_4 (.in0(TF), .in1(1'b0), .out(TF_W), .sel(TXBUFFEREMPTY));
  Multiplexer #(.enable("false")) multiplexer_5 (.in0(NF), .in1(1'b0), .out(NF_W), .sel(or_2_out));
  or or_2 (or_2_out, NFC, ~ENA_IN);  // OR_Gate
  Multiplexer #(.enable("false")) multiplexer_6 (.in0(OR), .in1(1'b0), .out(OR_W), .sel(or_3_out));
  or or_3 (or_3_out, ORC, ~ENA_IN);  // OR_Gate
  Multiplexer #(.enable("false")) multiplexer_7 (.in0(SC[6]), .in1(1'b0), .out(SC_W[6]), .sel(or_4_out));
  or or_4 (or_4_out, SCIN[6], ~ENA_IN);  // OR_Gate
  Multiplexer #(.enable("false")) multiplexer_8 (.in0(FE), .in1(1'b0), .out(FE_W), .sel(or_5_out));
  or or_5 (or_5_out, FEC, ~ENA_IN);  // OR_Gate
  D_Flip_Flop d_ff_1 (.clk(CLK_t), .D(W), .Qn(d_ff_1_qn), .en(CS), .reset(minus_CS));  // open: Q, preset
  D_Flip_Flop d_ff_2 (.clk(CLK_t), .D(Oold), .Qn(d_ff_2_qn), .en(CS), .reset(minus_CS));  // open: Q, preset
  and and_2 (and_2_out, W, d_ff_1_qn);
  and and_3 (and_3_out, Oold, d_ff_2_qn);
  D_Flip_Flop d_ff_3 (.clk(CLK_t), .D(and_2_out), .Q(WRITE), .en(CS), .reset(minus_CS));  // open: Qn, preset
  D_Flip_Flop d_ff_4 (.clk(CLK_t), .D(and_3_out), .Q(READold), .en(CS), .reset(minus_CS));  // open: Qn, preset
  assign not_6_out = ~UPDATE_VALS;  // NOT_Gate not_6, 8 bits wide
  assign IM_star = ~INTERRUPT_MASKS_q;  // NOT_Gate not_7, 8 bits wide
  Register INTERRUPT_MASKS (.D(not_6_out), .en(IM_WRITEENABLE), .Q(INTERRUPT_MASKS_q), .clk(CLK_t));  // open: clr
  and and_4 (and_4_out, BYTECOUNT, DATA_WRITEENABLE);
  or or_6 (or_6_out, and_4_out, and_5_out);
  and and_5 (and_5_out, SCIN[1], BYTECOUNT);
  Multiplexer #(.disabled(0), .enable("false")) multiplexer_9 (
    .in0(1'b0), .in1(1'b1), .out(multiplexer_9_out), .sel(and_6_out));
  and and_6 (and_6_out, SCIN[1], BYTECOUNT);
  and and_7 (and_7_out, ~BYTECOUNT, DATA_WRITEENABLE);  // AND_Gate
  Transmitter transmitter_1 (
    .CLK(CLK_t), .BRD(BRD), .E(ENA), .WI({WORDIN, TXBUFFER}), .WIS(or_6_out), .BTS(and_8_out), .FULL(TBF),
    .IDLE(TIDLE), .TX(TTX), .BUFFER_EMPTY(TXBUFFEREMPTY));
  and and_8 (and_8_out, ~TXBUFFEREMPTY, WRITE, or_7_out);  // AND_Gate
  or or_7 (or_7_out, and_9_out, SHOULDTRANSMIT);
  D_Flip_Flop d_ff_5 (.clk(CLK_t), .D(multiplexer_9_out), .Q(SHOULDTRANSMIT));  // open: Qn, preset, en, reset
  // Probe on TXBUFFER
  Register u_TXBUFFER (.D(UPDATE_VALS), .en(and_7_out), .Q(TXBUFFER), .clk(CLK_t));  // open: clr
  T_Flip_Flop t_ff_1 (
    .clk(CLK_t), .T(1'b1), .Q(BYTECOUNT), .reset(SHOULDTRANSMIT), .en(DATA_WRITEENABLE));  // open: Qn, preset
  Multiplexer #(.width(8), .enable("false")) multiplexer_10 (
    .in0({8{1'b0}}), .in1(DATAIN), .out(WORDIN), .sel(and_10_out));
  and and_9 (and_9_out, ~BYTECOUNT, SCIN[1]);  // AND_Gate
  // Probe on {WORDIN, TXBUFFER}
  and and_10 (and_10_out, BYTECOUNT, DATA_WRITEENABLE);
  Multiplexer #(.enable("false")) multiplexer_11 (.in0(1'b0), .in1(TTX), .out(TX), .sel(not_8_out));
  not not_8 (not_8_out, TIDLE);
  Register u_BRD (.D(UPDATE_VALS), .en(BRD_WRITEENABLE), .Q(BRD), .clk(CLK_t));  // open: clr
  nand nand_1 (nand_1_out, O, WRITE);
  D_Flip_Flop d_ff_6 (.clk(CLK_t), .D(not_8_out), .Qn(TXIO), .reset(not_8_out));  // open: Q, preset, en
  Multiplexer #(.select(4), .width(8)) multiplexer_12 (
    .in1({FE_W, SC_W[6], OR_W, NF_W, SC[3:2], DR, ENA_IN}), .in2({FE, SC[6], OR, NF, SC[3:2], DR, ENA}),
    .in5(IM_W), .in6({FEIM, IM[6:2], DRIM, IM[0]}), .in9(DATA_W), .in10(DATA_FROM_RX), .in13(BRD_W),
    .in14(BRD), .out(UPDATE_VALS), .sel({ADDR, O, WRITE}), .en(nand_2_out));  // open: in0, in3, in4, in7, in8, in11, in12, in15
  nand nand_2 (nand_2_out, O, WRITE);
  Demultiplexer #(.select(4)) demultiplexer_2 (
    .out1(SC_WRITEENABLE), .out5(IM_WRITEENABLE), .out9(DATA_WRITEENABLE), .out13(demultiplexer_2_out13),
    .in(1'b1), .sel({ADDR, O, WRITE}), .en(nand_1_out));  // open: out0, out2, out3, out4, out6, out7, out8, out10, out11, out12, out14, out15
  Comparator #(.mode("unsigned")) comparator_1 (.a(UPDATE_VALS), .b(8'h3), .lt(comparator_1_lt));  // open: gt, eq
  Comparator #(.mode("unsigned")) comparator_2 (.a(UPDATE_VALS), .b(8'hf), .gt(comparator_2_gt));  // open: eq, lt
  and and_11 (BRD_WRITEENABLE, demultiplexer_2_out13, ~comparator_1_lt, ~comparator_2_gt, ~ENA);  // AND_Gate

  // Other names for the same wires on the sheet: READ = O; BRDIN[7:0] = BRD_W; IM (some bits) = {FEIM, DRIM};
  //   TBNFIM = IM[2]; TXIIM = IM[3]; NIM = IM[4]; ORIM = IM[5]; SDEIM = IM[6]; IMIN[7:0] = IM_W;
  //   SC (some bits) = {FE, OR, NF, DR, ENA}; SDE = SC[6]; SC_W (some bits) = {FE_W, OR_W, NF_W, SC[3:2], DR, ENA_IN};
  //   TBNF = SC[2]; TXI = SC[3]; SDE_W = SC_W[6]; ENA_W = ENA_IN; SCIN (some bits) = {FEC, ORC, NFC, ENA_IN};
  //   TF_IN = SCIN[1]; SDEC = SCIN[6]; TXIN[7:0] = DATA_W; WORDIN[7:0] = TXBUFFER
endmodule

module NoisyChannel (
  input  [15:0] Rate,
  input  In,
  input  CLK,
  output Out
);

  wire Flip;
  wire [15:0] RNG;
  wire [31:0] adder_1_out, multiplier_1_out, SEED;

  xor xor_1 (Out, In, Flip);
  Multiplier #(.width(32)) multiplier_1 (.a(SEED), .b(32'h15a4e35), .out(multiplier_1_out));  // open: cin, cout
  Adder #(.width(32)) adder_1 (.a(multiplier_1_out), .b(32'h1), .out(adder_1_out));  // open: cin, cout
  Comparator #(.width(16), .mode("unsigned")) comparator_1 (.a(RNG), .b(Rate), .lt(Flip));  // open: gt, eq
  Register #(.width(32)) register_1 (.D(adder_1_out), .Q(SEED), .clk(CLK));  // open: en, clr
  assign RNG = SEED[15:0] ^ SEED[31:16];  // XOR_Gate xor_2, 16 bits wide
endmodule

module BRD (
  input  [3:0] BRD,
  input  Clock,
  input  in_3,
  input  [3:0] ADVANCE_VAL,
  input  in_5,
  output [3:0] BRD_2,
  output [3:0] BRD_COUNT,
  output BRDO,
  output BRD_is0,
  output [3:0] B
);

  wire CLK, comparator_1_eq, d_ff_1_q, DELAYED, InputCLK, multiplexer_4_out, or_1_out, undriven;
  wire [3:0] adder_1_out, BRD_1, C, C_1, multiplexer_1_out, multiplexer_2_out, multiplexer_3_out,
       subtractor_3_out;

  Clock clock_1 (.out(InputCLK));
  Multiplexer #(.width(4), .enable("false")) multiplexer_1 (
    .in0(C_1), .in1(BRD_1), .out(multiplexer_1_out), .sel(BRD_is0));
  nor nor_1 (BRD_is0, C[0], C[1], C[2], C[3]);
  Subtractor #(.width(4)) subtractor_1 (.a(C), .b(4'b0000), .out(C_1), .bin(1'b1));  // open: bout
  Subtractor #(.width(4)) subtractor_2 (.a(BRD), .b(4'b0000), .out(BRD_1), .bin(1'b1));  // open: bout
  Subtractor #(.width(4)) subtractor_3 (.a(BRD), .b(ADVANCE_VAL), .out(subtractor_3_out), .bin(1'b1));  // open: bout
  Multiplexer #(.width(4), .enable("false")) multiplexer_2 (
    .in0(multiplexer_1_out), .in1(subtractor_3_out), .out(multiplexer_2_out), .sel(in_3));
  Adder #(.width(4)) adder_1 (.a(B), .b(4'b0001), .out(adder_1_out));  // open: cin, cout
  Comparator #(.width(4), .mode("unsigned")) comparator_1 (.a(BRD), .b(B), .eq(comparator_1_eq));  // open: gt, lt
  Subtractor #(.width(4)) subtractor_4 (.a(BRD), .b(C), .out(BRD_COUNT), .bin(1'b1));  // open: bout
  // Probe on BRD_COUNT
  and and_1 (CLK, ~DELAYED, InputCLK);  // AND_Gate
  Register #(.width(4)) register_1 (.D(multiplexer_2_out), .Q(C), .clk(CLK), .clr(undriven));  // open: en
  Multiplexer #(.width(4), .enable("false")) multiplexer_3 (
    .in0(adder_1_out), .in1(ADVANCE_VAL), .out(multiplexer_3_out), .sel(in_3));
  Register #(.width(4)) register_2 (.D(multiplexer_3_out), .Q(B), .clk(CLK), .clr(or_1_out));  // open: en
  or or_1 (or_1_out, comparator_1_eq, DELAYED);
  // Probe on B
  Multiplexer #(.enable("false")) multiplexer_4 (.in0(in_5), .in1(1'b0), .out(multiplexer_4_out), .sel(DELAYED));
  D_Flip_Flop d_ff_1 (.clk(InputCLK), .D(multiplexer_4_out), .Q(d_ff_1_q));  // open: Qn, preset, en, reset
  D_Flip_Flop d_ff_2 (.clk(InputCLK), .D(d_ff_1_q), .Q(DELAYED));  // open: Qn, preset, en, reset

  assign BRD_2 = BRD;
  assign BRDO = BRD_is0;

  // Other names for the same wires on the sheet: ADVANCE = in_3; DELAY = in_5; is0 = BRD_is0; O = BRD_is0

  // Notes on the sheet:
  //   BRD: pull=down
  //   in_3: pull=down
  //   ADVANCE_VAL: pull=down
  //   in_5: pull=down
endmodule

module bit_stuffer (
  input  BRD_CLK,
  input  new_data_bit,
  input  Special_flag,
  input  BRD_is0,
  input  Enable,
  output TX,
  output STUFF_E
);

  wire and_1_out, and_2_out, and_3_out, and_4_out, and_5_out, and_6_out, and_7_out, clock_1_out, D, InpB,
       nor_1_out, nor_2_out, nor_3_out, not_4_out, nTE, OLDB, or_3_out, or_5_out, SS, SS_previous, undriven,
       undriven_2, xor_1_out;
  wire [2:0] _0C, _0C_star, _1C, _1C_star, multiplexer_1_out, multiplexer_2_out, xnor_1_out, xnor_2_out;

  // NOT_Gate not_1 has open pins: in=Special_flag, out=open
  and and_1 (and_1_out, D, nor_1_out);
  nor nor_1 (nor_1_out, Special_flag, SS);
  Multiplexer #(.width(3), .enable("false")) multiplexer_1 (
    .in0(3'b000), .in1(_1C_star), .out(multiplexer_1_out), .sel(and_1_out));
  Register #(.width(3)) register_1 (.D(multiplexer_1_out), .en(undriven), .Q(_1C), .clk(BRD_CLK), .clr(nTE));
  Adder #(.width(3)) adder_1 (.a(_1C), .b(3'b001), .out(_1C_star));  // open: cin, cout
  Adder #(.width(3)) adder_2 (.a(_0C), .b(3'b001), .out(_0C_star));  // open: cin, cout
  not not_2 (nTE, Enable);
  // NOT_Gate not_3 has open pins: in=Special_flag, out=open
  and and_2 (and_2_out, SS_previous, BRD_is0);
  // OR_Gate or_1 has open pins: in0=and_2_out, in1=and_3_out, out=open
  and and_3 (and_3_out, ~BRD_is0, SS_previous);  // AND_Gate
  Multiplexer #(.width(3), .enable("false")) multiplexer_2 (
    .in0(_0C_star), .in1(3'b000), .out(multiplexer_2_out), .sel(or_3_out));
  Register #(.width(3)) register_2 (.D(multiplexer_2_out), .Q(_0C), .clk(BRD_CLK), .clr(nTE));  // open: en
  // OR_Gate or_2 has open pins: in0=Special_flag, in1=SS, out=open
  nor nor_2 (nor_2_out, _1C[0], _1C[1], _1C[2]);
  assign xnor_1_out = ~(3'b101 ^ _0C);  // XNOR_Gate xnor_1, 3 bits wide
  assign xnor_2_out = ~(3'b101 ^ _1C);  // XNOR_Gate xnor_2, 3 bits wide
  and and_4 (and_4_out, ~SS, D);  // AND_Gate
  and and_5 (and_5_out, ~InpB, SS);  // AND_Gate
  or or_3 (or_3_out, Special_flag, SS, D);
  xor xor_1 (xor_1_out, nor_2_out, nor_3_out);
  nor nor_3 (nor_3_out, _0C[0], _0C[1], _0C[2]);
  and and_6 (and_6_out, xnor_1_out[0], xnor_1_out[1], xnor_1_out[2]);
  and and_7 (and_7_out, xnor_2_out[0], xnor_2_out[1], xnor_2_out[2]);
  or or_4 (TX, and_4_out, and_5_out);
  Register #(.width(1)) register_3 (.D(D), .en(undriven_2), .Q(InpB), .clk(BRD_CLK), .clr(nTE));
  and and_8 (SS, xor_1_out, or_5_out);
  or or_5 (or_5_out, and_6_out, and_7_out);
  D_Flip_Flop #(.trigger("high")) d_ff_1 (.clk(BRD_CLK), .D(new_data_bit), .Q(OLDB));  // open: Qn, preset, en, reset
  Multiplexer #(.enable("false")) multiplexer_3 (.in0(OLDB), .in1(new_data_bit), .out(D), .sel(STUFF_E));
  not not_4 (not_4_out, SS);
  and and_9 (STUFF_E, not_4_out, BRD_is0);
  Clock clock_1 (.out(clock_1_out));
  D_Flip_Flop d_ff_2 (.clk(clock_1_out), .D(SS), .Q(SS_previous), .reset(nTE));  // open: Qn, preset, en

  // Other names for the same wires on the sheet: BRD = BRD_CLK; E = STUFF_E; NEWDB = new_data_bit; SF = Special_flag;
  //   TE = Enable

  // Notes on the sheet:
  //   Enable: pull=down
  //   SS = should stuff
endmodule

// updater
module PLComp (
  input  f,
  input  p,
  input  [9:0] index,
  output [9:0] index_1,
  output f_star
);

  wire and_1_out, and_2_out, comparator_1_eq, comparator_1_gt, comparator_1_lt, or_1_out;

  Comparator #(.width(5), .mode("unsigned")) comparator_1 (
    .a(index[9:5]), .b(index[4:0]), .gt(comparator_1_gt), .eq(comparator_1_eq), .lt(comparator_1_lt));
  Subtractor #(.width(5)) subtractor_1 (.a(index[9:5]), .b(5'b00001), .out(index_1[9:5]));  // open: bin, bout
  or or_1 (or_1_out, comparator_1_eq, comparator_1_lt);
  and and_1 (and_1_out, or_1_out, p);
  or or_2 (f_star, and_2_out, and_1_out);
  and and_2 (and_2_out, comparator_1_gt, f);

  assign index_1[4:0] = index[4:0];

  // Other names for the same wires on the sheet: index_t[4:0] = index[9:5]; tunnel[4:0] = index[4:0]

  // Notes on the sheet:
  //   f: pull=down
  //   p: pull=down
endmodule

module P_Loader (
  input  [21:0] FIFO,
  input  [21:0] PIN,
  input  [4:0] Count,
  output [21:0] out_4
);

  wire [9:0] plcomp_2_index_1, plcomp_3_index_1, plcomp_4_index_1, plcomp_5_index_1, plcomp_6_index_1,
       plcomp_7_index_1, plcomp_8_index_1, plcomp_9_index_1, plcomp_10_index_1, plcomp_11_index_1,
       plcomp_12_index_1, plcomp_13_index_1, plcomp_14_index_1, plcomp_15_index_1, plcomp_16_index_1,
       plcomp_17_index_1, plcomp_18_index_1, plcomp_19_index_1, plcomp_20_index_1, plcomp_21_index_1,
       plcomp_22_index_1;

  // Probe on Count
  PLComp plcomp_1 (.f_star(out_4[0]), .index(plcomp_2_index_1), .f(FIFO[0]), .p(PIN[0]));  // open: index_1
  PLComp plcomp_2 (.index_1(plcomp_2_index_1), .f_star(out_4[1]), .index(plcomp_3_index_1), .f(FIFO[1]), .p(PIN[1]));
  PLComp plcomp_3 (.index_1(plcomp_3_index_1), .f_star(out_4[2]), .index(plcomp_4_index_1), .f(FIFO[2]), .p(PIN[2]));
  PLComp plcomp_4 (.index_1(plcomp_4_index_1), .f_star(out_4[3]), .index(plcomp_5_index_1), .f(FIFO[3]), .p(PIN[3]));
  PLComp plcomp_5 (.index_1(plcomp_5_index_1), .f_star(out_4[4]), .index(plcomp_6_index_1), .f(FIFO[4]), .p(PIN[4]));
  PLComp plcomp_6 (.index_1(plcomp_6_index_1), .f_star(out_4[5]), .index(plcomp_7_index_1), .f(FIFO[5]), .p(PIN[5]));
  PLComp plcomp_7 (.index_1(plcomp_7_index_1), .f_star(out_4[6]), .index(plcomp_8_index_1), .f(FIFO[6]), .p(PIN[6]));
  PLComp plcomp_8 (.index_1(plcomp_8_index_1), .f_star(out_4[7]), .index(plcomp_9_index_1), .f(FIFO[7]), .p(PIN[7]));
  PLComp plcomp_9 (.index_1(plcomp_9_index_1), .f_star(out_4[8]), .index(plcomp_10_index_1), .f(FIFO[8]), .p(PIN[8]));
  PLComp plcomp_10 (.index_1(plcomp_10_index_1), .f_star(out_4[9]), .index(plcomp_11_index_1), .f(FIFO[9]), .p(PIN[9]));
  PLComp plcomp_11 (
    .index_1(plcomp_11_index_1), .f_star(out_4[10]), .index(plcomp_12_index_1), .f(FIFO[10]), .p(PIN[10]));
  PLComp plcomp_12 (
    .index_1(plcomp_12_index_1), .f_star(out_4[11]), .index(plcomp_13_index_1), .f(FIFO[11]), .p(PIN[11]));
  PLComp plcomp_13 (
    .index_1(plcomp_13_index_1), .f_star(out_4[12]), .index(plcomp_14_index_1), .f(FIFO[12]), .p(PIN[12]));
  PLComp plcomp_14 (
    .index_1(plcomp_14_index_1), .f_star(out_4[13]), .index(plcomp_15_index_1), .f(FIFO[13]), .p(PIN[13]));
  PLComp plcomp_15 (
    .index_1(plcomp_15_index_1), .f_star(out_4[14]), .index(plcomp_16_index_1), .f(FIFO[14]), .p(PIN[14]));
  PLComp plcomp_16 (
    .index_1(plcomp_16_index_1), .f_star(out_4[15]), .index(plcomp_17_index_1), .f(FIFO[15]), .p(PIN[15]));
  PLComp plcomp_17 (
    .index_1(plcomp_17_index_1), .f_star(out_4[16]), .index(plcomp_18_index_1), .f(FIFO[16]), .p(PIN[16]));
  PLComp plcomp_18 (
    .index_1(plcomp_18_index_1), .f_star(out_4[17]), .index(plcomp_19_index_1), .f(FIFO[17]), .p(PIN[17]));
  PLComp plcomp_19 (
    .index_1(plcomp_19_index_1), .f_star(out_4[18]), .index(plcomp_20_index_1), .f(FIFO[18]), .p(PIN[18]));
  PLComp plcomp_20 (
    .index_1(plcomp_20_index_1), .f_star(out_4[19]), .index(plcomp_21_index_1), .f(FIFO[19]), .p(PIN[19]));
  PLComp plcomp_21 (
    .index_1(plcomp_21_index_1), .f_star(out_4[20]), .index(plcomp_22_index_1), .f(FIFO[20]), .p(PIN[20]));
  PLComp plcomp_22 (
    .index_1(plcomp_22_index_1), .f_star(out_4[21]), .index({5'b10110, Count}), .f(FIFO[21]), .p(PIN[21]));

  // Other names for the same wires on the sheet: tunnel[4:0] = Count; f0 = FIFO[0]; f1 = FIFO[1]; f2 = FIFO[2];
  //   f3 = FIFO[3]; f4 = FIFO[4]; f5 = FIFO[5]; f6 = FIFO[6]; f7 = FIFO[7]; f8 = FIFO[8]; f9 = FIFO[9];
  //   f10 = FIFO[10]; f11 = FIFO[11]; f12 = FIFO[12]; f13 = FIFO[13]; f14 = FIFO[14]; f15 = FIFO[15]; f16 = FIFO[16];
  //   f17 = FIFO[17]; f18 = FIFO[18]; f19 = FIFO[19]; f20 = FIFO[20]; f21 = FIFO[21]; f0_star = out_4[0];
  //   FIFO_star[21:0] = out_4; f1_star = out_4[1]; f2_star = out_4[2]; f3_star = out_4[3]; f4_star = out_4[4];
  //   f5_star = out_4[5]; f6_star = out_4[6]; f7_star = out_4[7]; f8_star = out_4[8]; f9_star = out_4[9];
  //   f10_star = out_4[10]; f11_star = out_4[11]; f12_star = out_4[12]; f13_star = out_4[13]; f14_star = out_4[14];
  //   f15_star = out_4[15]; f16_star = out_4[16]; f17_star = out_4[17]; f18_star = out_4[18]; f19_star = out_4[19];
  //   f20_star = out_4[20]; f21_star = out_4[21]; _0 = PIN[0]; _1 = PIN[1]; _2 = PIN[2]; _3 = PIN[3]; _4 = PIN[4];
  //   _5 = PIN[5]; _6 = PIN[6]; _7 = PIN[7]; _8 = PIN[8]; _9 = PIN[9]; _10 = PIN[10]; _11 = PIN[11]; _12 = PIN[12];
  //   _13 = PIN[13]; _14 = PIN[14]; _15 = PIN[15]; _16 = PIN[16]; _17 = PIN[17]; _18 = PIN[18]; _19 = PIN[19];
  //   _20 = PIN[20]; _21 = PIN[21]

  // Notes on the sheet:
  //   FIFO: pull=up
  //   out_4: pull=up
endmodule

module _5bSUB1 (
  input  [4:0] in_1,
  output [4:0] out_2
);

  Subtractor #(.width(5)) subtractor_1 (.a(in_1), .b(5'b00001), .out(out_2));  // open: bin, bout
endmodule

module _5bADD1 (
  input  [4:0] in_1,
  output [4:0] out_2
);

  Adder #(.width(5)) adder_1 (.a(in_1), .b(5'b00001), .out(out_2));  // open: cin, cout
endmodule

module _22FIFO (
  input  CLK,
  input  Serial_In,
  input  Serial_In_Signal,
  input  Serial_Out_Signal,
  input  Parallel_Signal,
  input  Parallel_Unload,
  input  [4:0] Paralell_In_Count,
  input  [21:0] Parallel_In,
  output Serial_Out,
  output [4:0] FIFO_count,
  output [21:0] Parallel_Out
);

  wire _21, and_1_out, and_2_out, and_3_out, and_4_out, and_5_out, comparator_1_gt, comparator_2_eq,
       comparator_3_eq, comparator_4_eq, comparator_5_eq, multiplexer_8_out, nor_1_out, not_1_out, not_2_out,
       or_1_out, or_2_out, SIOO, SOO, SXO_star, SXO_star_star;
  wire [4:0] _5bSUB1_2_out_2, _5bSUB1_3_out_2, _5bSUB1_4_out_2, _5bSUB1_out_2, adder_1_out, FRONT_P,
       FRONT_PL, FRONT_S, FRONT_SI, FRONT_SO, FRONT_star, total_num;
  wire [20:0] FIFO_S;
  wire [21:0] FIFO, FIFO_PL, FIFO_star, PXO;

  P_Loader P_Load (.FIFO(FIFO), .PIN(Parallel_In), .Count(Paralell_In_Count), .out_4(FIFO_PL));
  Comparator #(.width(5), .mode("unsigned")) comparator_1 (
    .a(Paralell_In_Count), .b(FRONT_PL), .gt(comparator_1_gt));  // open: eq, lt
  Multiplexer #(.width(22), .enable("false")) multiplexer_1 (
    .in0(FIFO), .in1(FIFO_PL), .out({_21, FIFO_S}), .sel(Parallel_Signal));
  Multiplexer #(.width(5), .enable("false")) multiplexer_2 (
    .in0(FRONT_PL), .in1(Paralell_In_Count), .out(FRONT_P), .sel(comparator_1_gt));
  Multiplexer #(.width(5), .enable("false")) multiplexer_3 (
    .in0(FIFO_count), .in1({5{1'b0}}), .out(FRONT_PL), .sel(Parallel_Unload));
  // Probe on {_21, FIFO_S}
  Adder #(.width(5)) adder_1 (.a(FRONT_S), .b(5'b00001), .out(adder_1_out));  // open: cin, cout
  Comparator #(.width(5), .mode("unsigned")) comparator_2 (
    .a(FRONT_S), .b(5'b10110), .eq(comparator_2_eq));  // open: gt, lt
  Multiplexer #(.width(5), .enable("false")) multiplexer_4 (
    .in0(FRONT_PL), .in1(FRONT_P), .out(FRONT_S), .sel(Parallel_Signal));
  Multiplexer #(.width(5), .enable("false")) multiplexer_5 (
    .in0(adder_1_out), .in1(5'b10110), .out(FRONT_SI), .sel(comparator_2_eq));
  Register #(.width(5)) register_1 (
    .D(Paralell_In_Count), .en(Parallel_Signal), .Q(total_num), .clk(CLK));  // open: clr
  // Probe on FIFO_star
  // Probe on FIFO
  Register #(.width(22)) u_FIFO (.D(FIFO_star), .Q(FIFO), .clk(CLK));  // open: en, clr
  assign Parallel_Out = Parallel_Unload ? FIFO : 22'bz;  // Controlled_Buffer controlled_buffer_1
  Multiplexer #(.select(5), .enable("false")) multiplexer_6 (
    .in0(Serial_In), .in1(FIFO_S[0]), .in2(FIFO_S[1]), .in3(FIFO_S[2]), .in4(FIFO_S[3]), .in5(FIFO_S[4]),
    .in6(FIFO_S[5]), .in7(FIFO_S[6]), .in8(FIFO_S[7]), .in9(FIFO_S[8]), .in10(FIFO_S[9]), .in11(FIFO_S[10]),
    .in12(FIFO_S[11]), .in13(FIFO_S[12]), .in14(FIFO_S[13]), .in15(FIFO_S[14]), .in16(FIFO_S[15]),
    .in17(FIFO_S[16]), .in18(FIFO_S[17]), .in19(FIFO_S[18]), .in20(FIFO_S[19]), .in21(FIFO_S[20]),
    .out(SIOO), .sel(_5bSUB1_out_2));  // open: in22, in23, in24, in25, in26, in27, in28, in29, in30, in31
  _5bSUB1 _5bSUB1 (.in_1(FRONT_SI), .out_2(_5bSUB1_out_2));
  // Probe on FRONT_star
  Register #(.width(5)) FRONT (.D(FRONT_star), .Q(FIFO_count), .clk(CLK));  // open: en, clr
  // Probe on _5bSUB1_2_out_2
  // Probe on FIFO_count
  Multiplexer #(.select(5), .enable("false")) multiplexer_7 (
    .in0(FIFO_S[0]), .in1(FIFO_S[1]), .in2(FIFO_S[2]), .in3(FIFO_S[3]), .in4(FIFO_S[4]), .in5(FIFO_S[5]),
    .in6(FIFO_S[6]), .in7(FIFO_S[7]), .in8(FIFO_S[8]), .in9(FIFO_S[9]), .in10(FIFO_S[10]), .in11(FIFO_S[11]),
    .in12(FIFO_S[12]), .in13(FIFO_S[13]), .in14(FIFO_S[14]), .in15(FIFO_S[15]), .in16(FIFO_S[16]),
    .in17(FIFO_S[17]), .in18(FIFO_S[18]), .in19(FIFO_S[19]), .in20(FIFO_S[20]), .in21(_21), .out(SOO),
    .sel(_5bSUB1_2_out_2));  // open: in22, in23, in24, in25, in26, in27, in28, in29, in30, in31
  _5bSUB1 _5bSUB1_2 (.in_1(FRONT_S), .out_2(_5bSUB1_2_out_2));
  Multiplexer #(.enable("false")) multiplexer_8 (.in0(SIOO), .in1(_21), .out(multiplexer_8_out), .sel(comparator_3_eq));
  Comparator #(.width(5), .mode("unsigned")) comparator_3 (
    .a(FRONT_star), .b(5'b10110), .eq(comparator_3_eq));  // open: gt, lt
  D_Flip_Flop d_ff_1 (.clk(CLK), .D(SXO_star), .Q(SXO_star_star));  // open: Qn, preset, en, reset
  Register #(.width(22)) register_2 (.D(Parallel_Out), .Q(PXO), .clk(CLK));  // open: en, clr
  // Probe on {_21, FIFO_S}
  _5bSUB1 _5bSUB1_3 (.in_1(FRONT_S), .out_2(_5bSUB1_3_out_2));
  Multiplexer #(.width(5), .enable("false")) multiplexer_9 (
    .in0(_5bSUB1_3_out_2), .in1(_5bSUB1_4_out_2), .out(FRONT_SO), .sel(Serial_In_Signal));
  _5bSUB1 _5bSUB1_4 (.in_1(FRONT_SI), .out_2(_5bSUB1_4_out_2));
  and and_1 (and_1_out, and_3_out, ~comparator_4_eq);  // AND_Gate
  or or_1 (or_1_out, and_2_out, and_1_out);
  and and_2 (and_2_out, and_4_out, comparator_5_eq);
  Multiplexer #(.select(2)) multiplexer_10 (
    .in2(SOO), .in3(multiplexer_8_out), .out(SXO_star), .sel({Serial_Out_Signal, Serial_In_Signal}),
    .en(not_1_out));  // open: in0, in1
  Multiplexer #(.select(2), .width(5)) multiplexer_11 (
    .in0(FRONT_S), .in1(FRONT_SI), .in2(FRONT_SO), .in3(FRONT_S), .out(FRONT_star),
    .sel({Serial_Out_Signal, Serial_In_Signal}), .en(not_2_out));
  Multiplexer #(.select(2), .width(22), .enable("false")) multiplexer_12 (
    .in0({_21, FIFO_S}), .in1({FIFO_S, Serial_In}), .in2({_21, FIFO_S}), .in3({FIFO_S, Serial_In}),
    .out(FIFO_star), .sel({Serial_Out_Signal, Serial_In_Signal}));
  Multiplexer #(.enable("false")) multiplexer_13 (.in0(SXO_star), .in1(SOO), .out(Serial_Out), .sel(or_1_out));
  and and_3 (and_3_out, Parallel_Signal, ~Serial_Out_Signal);  // AND_Gate
  Comparator #(.width(5), .mode("unsigned")) comparator_4 (
    .a(FIFO_count), .b({5{1'b0}}), .eq(comparator_4_eq));  // open: gt, lt
  and and_4 (and_4_out, Serial_Out_Signal, ~Parallel_Signal);  // AND_Gate
  Comparator #(.width(5), .mode("unsigned")) comparator_5 (
    .a(FIFO_count), .b(total_num), .eq(comparator_5_eq));  // open: gt, lt
  or or_2 (or_2_out, Parallel_Unload, and_5_out);
  not not_1 (not_1_out, or_2_out);
  not not_2 (not_2_out, and_5_out);
  // Probe on FRONT_star
  nor nor_1 (nor_1_out, FIFO_count[0], FIFO_count[1], FIFO_count[2], FIFO_count[3], FIFO_count[4]);
  and and_5 (and_5_out, nor_1_out, ~Serial_In_Signal, ~Parallel_Signal);  // AND_Gate

  // Other names for the same wires on the sheet: SIS = Serial_In_Signal; SOS = Serial_Out_Signal; FIFO_S[21] = _21;
  //   FIFO_SI[21:0] = {FIFO_S, Serial_In}; SI = Serial_In; FC[4:0] = FIFO_count; FRONT[4:0] = FIFO_count;
  //   PS = Parallel_Signal; PU = Parallel_Unload; PX[21:0] = Parallel_In; PXC[4:0] = Paralell_In_Count;
  //   PXO_star[21:0] = Parallel_Out; SXO = Serial_Out

  // Notes on the sheet:
  //   Serial_Out_Signal: pull=down
  //   Serial_In: pull=down
  //   Parallel_Out: pull=down
  //   Serial_Out: pull=down
  //   Parallel_Unload: pull=down
  //   Serial_In_Signal: pull=down
  //   Parallel_Signal: pull=down
  //   when count is greater than front from p, then front will change, otherwise it wont
endmodule

module _16FIFO (
  input  CLK,
  input  [21:0] Word_In,
  input  Word_In_Signal,
  input  Word_Out_Signal,
  input  Parallel_load_signal,
  input  Parallel_Unload_Signal,
  input  [4:0] Paralell_In_Count,
  input  [21:0] Parallel_In_0,
  input  [21:0] Parallel_In_1,
  input  [21:0] Parallel_In_2,
  input  [21:0] Parallel_In_3,
  input  [21:0] Parallel_In_4,
  input  [21:0] Parallel_In_5,
  input  [21:0] Parallel_In_6,
  input  [21:0] Parallel_In_7,
  input  [21:0] Parallel_In_8,
  input  [21:0] Parallel_In_9,
  input  [21:0] Parallel_In_10,
  input  [21:0] Parallel_In_11,
  input  [21:0] Parallel_In_12,
  input  [21:0] Parallel_In_13,
  input  [21:0] Parallel_In_14,
  input  [21:0] Parallel_In_15,
  output [21:0] Word_Out,
  output [4:0] FIFO_count,
  output [21:0] Parallel_out_0,
  output [21:0] Parallel_out_1,
  output [21:0] Parallel_out_2,
  output [21:0] Parallel_out_3,
  output [21:0] Parallel_out_4,
  output [21:0] Parallel_out_5,
  output [21:0] Parallel_out_6,
  output [21:0] Parallel_out_7,
  output [21:0] Parallel_out_8,
  output [21:0] Parallel_out_9,
  output [21:0] Parallel_out_10,
  output [21:0] Parallel_out_11,
  output [21:0] Parallel_out_12,
  output [21:0] Parallel_out_13,
  output [21:0] Parallel_out_14,
  output [21:0] Parallel_out_15
);

  wire and_1_out, and_2_out, and_3_out, and_4_out, comparator_1_gt, comparator_2_eq, comparator_3_eq,
       comparator_4_eq, not_1_out, or_1_out, or_2_out, or_3_out, or_4_out, or_5_out, or_6_out, or_7_out,
       or_8_out, or_9_out, or_10_out, or_11_out, or_12_out, or_13_out, or_14_out, or_15_out, or_16_out,
       or_17_out, or_18_out, or_19_out, or_20_out, or_21_out, or_22_out, or_23_out, or_24_out, or_25_out,
       or_26_out, or_27_out, or_28_out, or_29_out, or_30_out, or_31_out, or_32_out, or_33_out;
  wire [4:0] FRONT_AL, FRONT_ASI, FRONT_ASO, FRONT_AU, FRONT_P, n5badd1_1_out_2, n5bsub1_1_out_2;
  wire [21:0] multiplexer_1_out, multiplexer_2_out, multiplexer_3_out, multiplexer_4_out, multiplexer_5_out,
       multiplexer_6_out, multiplexer_7_out, multiplexer_8_out, multiplexer_9_out, multiplexer_10_out,
       multiplexer_11_out, multiplexer_12_out, multiplexer_13_out, multiplexer_14_out, multiplexer_15_out,
       multiplexer_16_out;

  or or_1 (or_1_out, Word_Out_Signal, Word_In_Signal, Parallel_Unload_Signal);
  or or_2 (or_2_out, Word_Out_Signal, Word_In_Signal, Parallel_Unload_Signal);
  or or_3 (or_3_out, Word_Out_Signal, Word_In_Signal, Parallel_Unload_Signal);
  or or_4 (or_4_out, Word_Out_Signal, Word_In_Signal, Parallel_Unload_Signal);
  or or_5 (or_5_out, Word_Out_Signal, Word_In_Signal, Parallel_Unload_Signal);
  or or_6 (or_6_out, Word_Out_Signal, Word_In_Signal, Parallel_Unload_Signal);
  or or_7 (or_7_out, Word_Out_Signal, Word_In_Signal, Parallel_Unload_Signal);
  or or_8 (or_8_out, Word_Out_Signal, Word_In_Signal, Parallel_Unload_Signal);
  or or_9 (or_9_out, Word_Out_Signal, Word_In_Signal, Parallel_Unload_Signal);
  or or_10 (or_10_out, Word_Out_Signal, Word_In_Signal, Parallel_Unload_Signal);
  or or_11 (or_11_out, Word_Out_Signal, Word_In_Signal, Parallel_Unload_Signal);
  or or_12 (or_12_out, Word_Out_Signal, Word_In_Signal, Parallel_Unload_Signal);
  or or_13 (or_13_out, Word_In_Signal, Parallel_load_signal);
  Multiplexer #(.width(22), .enable("false")) multiplexer_1 (
    .in0(Parallel_In_0), .in1(Word_In), .out(multiplexer_1_out), .sel(Word_In_Signal));
  or or_14 (or_14_out, Word_In_Signal, Parallel_load_signal);
  Multiplexer #(.width(22), .enable("false")) multiplexer_2 (
    .in0(Parallel_In_1), .in1(Parallel_out_0), .out(multiplexer_2_out), .sel(Word_In_Signal));
  or or_15 (or_15_out, Word_In_Signal, Parallel_load_signal);
  Multiplexer #(.width(22), .enable("false")) multiplexer_3 (
    .in0(Parallel_In_2), .in1(Parallel_out_1), .out(multiplexer_3_out), .sel(Word_In_Signal));
  or or_16 (or_16_out, Word_In_Signal, Parallel_load_signal);
  Multiplexer #(.width(22), .enable("false")) multiplexer_4 (
    .in0(Parallel_In_3), .in1(Parallel_out_2), .out(multiplexer_4_out), .sel(Word_In_Signal));
  or or_17 (or_17_out, Word_In_Signal, Parallel_load_signal);
  Multiplexer #(.width(22), .enable("false")) multiplexer_5 (
    .in0(Parallel_In_4), .in1(Parallel_out_3), .out(multiplexer_5_out), .sel(Word_In_Signal));
  or or_18 (or_18_out, Word_In_Signal, Parallel_load_signal);
  or or_19 (or_19_out, Word_In_Signal, Parallel_load_signal);
  or or_20 (or_20_out, Word_Out_Signal, Word_In_Signal, Parallel_Unload_Signal);
  or or_21 (or_21_out, Word_Out_Signal, Word_In_Signal, Parallel_Unload_Signal);
  or or_22 (or_22_out, Word_In_Signal, Parallel_load_signal);
  or or_23 (or_23_out, Word_Out_Signal, Word_In_Signal, Parallel_Unload_Signal);
  or or_24 (or_24_out, Word_Out_Signal, Word_In_Signal, Parallel_Unload_Signal);
  or or_25 (or_25_out, Word_In_Signal, Parallel_load_signal);
  or or_26 (or_26_out, Word_In_Signal, Parallel_load_signal);
  or or_27 (or_27_out, Word_In_Signal, Parallel_load_signal);
  Multiplexer #(.width(22), .enable("false")) multiplexer_6 (
    .in0(Parallel_In_14), .in1(Parallel_out_13), .out(multiplexer_6_out), .sel(Word_In_Signal));
  or or_28 (or_28_out, Word_In_Signal, Parallel_load_signal);
  _22FIFO u_22fifo_1 (
    .CLK(CLK), .Parallel_Signal(or_13_out), .Parallel_Unload(or_1_out), .Paralell_In_Count(5'b10110),
    .Parallel_In(multiplexer_1_out), .Parallel_Out(Parallel_out_0));  // open: Serial_In, Serial_In_Signal, Serial_Out_Signal, Serial_Out, FIFO_count
  _22FIFO u_22fifo_2 (
    .CLK(CLK), .Parallel_Signal(or_14_out), .Parallel_Unload(or_2_out), .Paralell_In_Count(5'b10110),
    .Parallel_In(multiplexer_2_out), .Parallel_Out(Parallel_out_1));  // open: Serial_In, Serial_In_Signal, Serial_Out_Signal, Serial_Out, FIFO_count
  _22FIFO u_22fifo_3 (
    .CLK(CLK), .Parallel_Signal(or_15_out), .Parallel_Unload(or_3_out), .Paralell_In_Count(5'b10110),
    .Parallel_In(multiplexer_3_out), .Parallel_Out(Parallel_out_2));  // open: Serial_In, Serial_In_Signal, Serial_Out_Signal, Serial_Out, FIFO_count
  _22FIFO u_22fifo_4 (
    .CLK(CLK), .Parallel_Signal(or_16_out), .Parallel_Unload(or_4_out), .Paralell_In_Count(5'b10110),
    .Parallel_In(multiplexer_4_out), .Parallel_Out(Parallel_out_3));  // open: Serial_In, Serial_In_Signal, Serial_Out_Signal, Serial_Out, FIFO_count
  _22FIFO u_22fifo_5 (
    .CLK(CLK), .Parallel_Signal(or_17_out), .Parallel_Unload(or_5_out), .Paralell_In_Count(5'b10110),
    .Parallel_In(multiplexer_5_out), .Parallel_Out(Parallel_out_4));  // open: Serial_In, Serial_In_Signal, Serial_Out_Signal, Serial_Out, FIFO_count
  _22FIFO u_22fifo_6 (
    .CLK(CLK), .Parallel_Signal(or_18_out), .Parallel_Unload(or_6_out), .Paralell_In_Count(5'b10110),
    .Parallel_In(multiplexer_7_out), .Parallel_Out(Parallel_out_5));  // open: Serial_In, Serial_In_Signal, Serial_Out_Signal, Serial_Out, FIFO_count
  Multiplexer #(.width(22), .enable("false")) multiplexer_7 (
    .in0(Parallel_In_5), .in1(Parallel_out_4), .out(multiplexer_7_out), .sel(Word_In_Signal));
  _22FIFO u_22fifo_7 (
    .CLK(CLK), .Parallel_Signal(or_19_out), .Parallel_Unload(or_7_out), .Paralell_In_Count(5'b10110),
    .Parallel_In(multiplexer_8_out), .Parallel_Out(Parallel_out_6));  // open: Serial_In, Serial_In_Signal, Serial_Out_Signal, Serial_Out, FIFO_count
  Multiplexer #(.width(22), .enable("false")) multiplexer_8 (
    .in0(Parallel_In_6), .in1(Parallel_out_5), .out(multiplexer_8_out), .sel(Word_In_Signal));
  _22FIFO u_22fifo_8 (
    .CLK(CLK), .Parallel_Signal(or_29_out), .Parallel_Unload(or_8_out), .Paralell_In_Count(5'b10110),
    .Parallel_In(multiplexer_9_out), .Parallel_Out(Parallel_out_7));  // open: Serial_In, Serial_In_Signal, Serial_Out_Signal, Serial_Out, FIFO_count
  or or_29 (or_29_out, Word_In_Signal, Parallel_load_signal);
  Multiplexer #(.width(22), .enable("false")) multiplexer_9 (
    .in0(Parallel_In_7), .in1(Parallel_out_6), .out(multiplexer_9_out), .sel(Word_In_Signal));
  or or_30 (or_30_out, Word_In_Signal, Parallel_load_signal);
  Multiplexer #(.width(22), .enable("false")) multiplexer_10 (
    .in0(Parallel_In_8), .in1(Parallel_out_7), .out(multiplexer_10_out), .sel(Word_In_Signal));
  or or_31 (or_31_out, Word_In_Signal, Parallel_load_signal);
  Multiplexer #(.width(22), .enable("false")) multiplexer_11 (
    .in0(Parallel_In_9), .in1(Parallel_out_8), .out(multiplexer_11_out), .sel(Word_In_Signal));
  _22FIFO u_22fifo_9 (
    .CLK(CLK), .Parallel_Signal(or_22_out), .Parallel_Unload(or_23_out), .Paralell_In_Count(5'b10110),
    .Parallel_In(multiplexer_12_out), .Parallel_Out(Parallel_out_10));  // open: Serial_In, Serial_In_Signal, Serial_Out_Signal, Serial_Out, FIFO_count
  Multiplexer #(.width(22), .enable("false")) multiplexer_12 (
    .in0(Parallel_In_10), .in1(Parallel_out_9), .out(multiplexer_12_out), .sel(Word_In_Signal));
  or or_32 (or_32_out, Word_In_Signal, Parallel_load_signal);
  Multiplexer #(.width(22), .enable("false")) multiplexer_13 (
    .in0(Parallel_In_11), .in1(Parallel_out_10), .out(multiplexer_13_out), .sel(Word_In_Signal));
  _22FIFO u_22fifo_10 (
    .CLK(CLK), .Parallel_Signal(or_25_out), .Parallel_Unload(or_9_out), .Paralell_In_Count(5'b10110),
    .Parallel_In(multiplexer_14_out), .Parallel_Out(Parallel_out_12));  // open: Serial_In, Serial_In_Signal, Serial_Out_Signal, Serial_Out, FIFO_count
  Multiplexer #(.width(22), .enable("false")) multiplexer_14 (
    .in0(Parallel_In_12), .in1(Parallel_out_11), .out(multiplexer_14_out), .sel(Word_In_Signal));
  // Probe on Parallel_out_13
  _22FIFO u_22fifo_11 (
    .CLK(CLK), .Parallel_Signal(or_26_out), .Parallel_Unload(or_10_out), .Paralell_In_Count(5'b10110),
    .Parallel_In(multiplexer_15_out), .Parallel_Out(Parallel_out_13));  // open: Serial_In, Serial_In_Signal, Serial_Out_Signal, Serial_Out, FIFO_count
  Multiplexer #(.width(22), .enable("false")) multiplexer_15 (
    .in0(Parallel_In_13), .in1(Parallel_out_12), .out(multiplexer_15_out), .sel(Word_In_Signal));
  _22FIFO u_22fifo_12 (
    .CLK(CLK), .Parallel_Signal(or_27_out), .Parallel_Unload(or_11_out), .Paralell_In_Count(5'b10110),
    .Parallel_In(multiplexer_6_out), .Parallel_Out(Parallel_out_14));  // open: Serial_In, Serial_In_Signal, Serial_Out_Signal, Serial_Out, FIFO_count
  // Probe on Parallel_out_15
  _22FIFO u_22fifo_13 (
    .CLK(CLK), .Parallel_Signal(or_28_out), .Parallel_Unload(or_12_out), .Paralell_In_Count(5'b10110),
    .Parallel_In(multiplexer_16_out), .Parallel_Out(Parallel_out_15));  // open: Serial_In, Serial_In_Signal, Serial_Out_Signal, Serial_Out, FIFO_count
  // Probe on multiplexer_16_out
  Multiplexer #(.width(22), .enable("false")) multiplexer_16 (
    .in0(Parallel_In_15), .in1(Parallel_out_14), .out(multiplexer_16_out), .sel(Word_In_Signal));
  // Probe on FIFO_count
  Register #(.width(5)) FRONT (.D(FRONT_ASO), .Q(FIFO_count), .clk(CLK));  // open: en, clr
  _22FIFO u_22fifo_14 (
    .CLK(CLK), .Parallel_Signal(or_30_out), .Parallel_Unload(or_20_out), .Paralell_In_Count(5'b10110),
    .Parallel_In(multiplexer_10_out), .Parallel_Out(Parallel_out_8));  // open: Serial_In, Serial_In_Signal, Serial_Out_Signal, Serial_Out, FIFO_count
  _22FIFO u_22fifo_15 (
    .CLK(CLK), .Parallel_Signal(or_31_out), .Parallel_Unload(or_21_out), .Paralell_In_Count(5'b10110),
    .Parallel_In(multiplexer_11_out), .Parallel_Out(Parallel_out_9));  // open: Serial_In, Serial_In_Signal, Serial_Out_Signal, Serial_Out, FIFO_count
  _22FIFO u_22fifo_16 (
    .CLK(CLK), .Parallel_Signal(or_32_out), .Parallel_Unload(or_24_out), .Paralell_In_Count(5'b10110),
    .Parallel_In(multiplexer_13_out), .Parallel_Out(Parallel_out_11));  // open: Serial_In, Serial_In_Signal, Serial_Out_Signal, Serial_Out, FIFO_count
  // Probe on Parallel_out_15
  // Probe on Word_Out
  Multiplexer #(.select(5), .width(22)) multiplexer_17 (
    .in0(Parallel_out_0), .in1(Parallel_out_1), .in2(Parallel_out_2), .in3(Parallel_out_3),
    .in4(Parallel_out_4), .in5(Parallel_out_5), .in6(Parallel_out_6), .in7(Parallel_out_7),
    .in8(Parallel_out_8), .in9(Parallel_out_9), .in10(Parallel_out_10), .in11(Parallel_out_11),
    .in12(Parallel_out_12), .in13(Parallel_out_13), .in14(Parallel_out_14), .in15(Parallel_out_15),
    .out(Word_Out), .sel(FRONT_ASO), .en(Word_Out_Signal));  // open: in16, in17, in18, in19, in20, in21, in22, in23, in24, in25, in26, in27, in28, in29, in30, in31
  // Probe on FRONT_ASO
  Multiplexer #(.width(5), .enable("false")) multiplexer_18 (
    .in0(FIFO_count), .in1({5{1'b0}}), .out(FRONT_AU), .sel(Parallel_Unload_Signal));
  Multiplexer #(.width(5), .enable("false")) multiplexer_19 (
    .in0(FRONT_AU), .in1(FRONT_P), .out(FRONT_AL), .sel(Parallel_load_signal));
  Multiplexer #(.width(5), .enable("false")) multiplexer_20 (
    .in0(FRONT_AU), .in1(Paralell_In_Count), .out(FRONT_P), .sel(comparator_1_gt));
  Comparator #(.width(5), .mode("unsigned")) comparator_1 (
    .a(Paralell_In_Count), .b(FRONT_AU), .gt(comparator_1_gt));  // open: eq, lt
  Comparator #(.width(5)) comparator_2 (.a(FRONT_AL), .b(5'b10000), .eq(comparator_2_eq));  // open: gt, lt
  not not_1 (not_1_out, comparator_2_eq);
  Multiplexer #(.width(5), .enable("false")) multiplexer_21 (
    .in0(FRONT_AL), .in1(n5badd1_1_out_2), .out(FRONT_ASI), .sel(and_1_out));
  _5bADD1 u_5badd1_1 (.in_1(FRONT_AL), .out_2(n5badd1_1_out_2));
  and and_1 (and_1_out, not_1_out, Word_In_Signal);
  Comparator #(.width(5)) comparator_3 (.a(FRONT_ASI), .b(5'b10000), .eq(comparator_3_eq));  // open: gt, lt
  // Probe on FRONT_ASI
  _5bSUB1 u_5bsub1_1 (.in_1(FRONT_ASI), .out_2(n5bsub1_1_out_2));
  and and_2 (and_2_out, or_33_out, ~comparator_4_eq);  // AND_Gate
  and and_3 (and_3_out, Word_Out_Signal, ~Word_In_Signal);  // AND_Gate
  and and_4 (and_4_out, Word_Out_Signal, Word_In_Signal, ~comparator_3_eq);  // AND_Gate
  Multiplexer #(.width(5), .enable("false")) multiplexer_22 (
    .in0(FRONT_ASI), .in1(n5bsub1_1_out_2), .out(FRONT_ASO), .sel(and_2_out));
  or or_33 (or_33_out, and_3_out, and_4_out);
  Comparator #(.width(5)) comparator_4 (.a(FRONT_ASI), .b({5{1'b0}}), .eq(comparator_4_eq));  // open: gt, lt

  // Other names for the same wires on the sheet: FC[4:0] = FIFO_count; FRONT[4:0] = FIFO_count;
  //   PLS = Parallel_load_signal; PUS = Parallel_Unload_Signal; PX0[21:0] = Parallel_In_0; PX1[21:0] = Parallel_In_1;
  //   PX2[21:0] = Parallel_In_2; PX3[21:0] = Parallel_In_3; PX4[21:0] = Parallel_In_4; PX5[21:0] = Parallel_In_5;
  //   PX6[21:0] = Parallel_In_6; PX7[21:0] = Parallel_In_7; PX8[21:0] = Parallel_In_8; PX9[21:0] = Parallel_In_9;
  //   PX10[21:0] = Parallel_In_10; PX11[21:0] = Parallel_In_11; PX12[21:0] = Parallel_In_12;
  //   PX13[21:0] = Parallel_In_13; PX14[21:0] = Parallel_In_14; PX15[21:0] = Parallel_In_15;
  //   PXC[4:0] = Paralell_In_Count; PXO0[21:0] = Parallel_out_0; PXO1[21:0] = Parallel_out_1;
  //   PXO2[21:0] = Parallel_out_2; PXO3[21:0] = Parallel_out_3; PXO4[21:0] = Parallel_out_4;
  //   PXO5[21:0] = Parallel_out_5; PXO6[21:0] = Parallel_out_6; PXO7[21:0] = Parallel_out_7;
  //   PXO8[21:0] = Parallel_out_8; PXO9[21:0] = Parallel_out_9; PXO10[21:0] = Parallel_out_10;
  //   PXO11[21:0] = Parallel_out_11; PXO12[21:0] = Parallel_out_12; PXO13[21:0] = Parallel_out_13;
  //   PXO14[21:0] = Parallel_out_14; PXO15[21:0] = Parallel_out_15; WI[21:0] = Word_In; WIS = Word_In_Signal;
  //   WO[21:0] = Word_Out; WOS = Word_Out_Signal

  // Notes on the sheet:
  //   Paralell_In_Count: pull=down
  //   Word_Out: pull=down
  //   Parallel_Unload_Signal: pull=down
  //   Parallel_load_signal: pull=down
  //   front is the current front
  //   front* is the next rising edge front
  //   FRONT-AU= front after unload
  //   FRONT-AL = front after load
  //   FRONT-ASI = front after shift in
  //   FRONT-ASO = front after shift out
endmodule

module SECDED (
  input  [15:0] in_1,
  output [21:0] out_2
);

  xor odd_parity_1 (out_2[1], in_1[0], in_1[1], in_1[3], in_1[4], in_1[6], in_1[8], in_1[10], in_1[11], in_1[13], in_1[15]);
  xor odd_parity_2 (out_2[8], in_1[4], in_1[5], in_1[6], in_1[7], in_1[8], in_1[9], in_1[10]);
  xor odd_parity_3 (out_2[2], in_1[0], in_1[2], in_1[3], in_1[5], in_1[6], in_1[9], in_1[10], in_1[12], in_1[13]);
  xor odd_parity_4 (out_2[16], in_1[11], in_1[12], in_1[13], in_1[14], in_1[15]);
  xor odd_parity_5 (out_2[4], in_1[1], in_1[2], in_1[3], in_1[7], in_1[8], in_1[9], in_1[10], in_1[14], in_1[15]);
  xor odd_parity_6 (out_2[0], out_2[1], out_2[2], in_1[0], out_2[4], in_1[1], in_1[2], in_1[3], out_2[8], in_1[4], in_1[5], in_1[6], in_1[7], in_1[8], in_1[9], in_1[10], out_2[16], in_1[11], in_1[12], in_1[13], in_1[14], in_1[15]);

  assign {out_2[21:17], out_2[15:9], out_2[7:5], out_2[3]} = in_1;

  // Other names for the same wires on the sheet: C0 = out_2[0];
  //   OUT[21:0] = {in_1[15:11], out_2[16], in_1[10:4], out_2[8], in_1[3:1], out_2[4], in_1[0], out_2[2:0]};
  //   C1 = out_2[1];
  //   INT[20:0] = {in_1[15:11], out_2[16], in_1[10:4], out_2[8], in_1[3:1], out_2[4], in_1[0], out_2[2:1]};
  //   C2 = out_2[2]; IN[15:0] = in_1; C3 = out_2[4]; C4 = out_2[8]; C5 = out_2[16]
endmodule

// 32
module Transmitter (
  input  CLK,
  input  [7:0] BRD,
  input  E,
  input  [15:0] WI,
  input  WIS,
  input  BTS,
  output FULL,
  output IDLE,
  output TX,
  output BUFFER_EMPTY
);

  wire and_1_out, and_2_out, and_3_out, and_4_out, and_5_out, and_6_out, and_10_out, and_11_out, BRD_CLK,
       BRD_is0, clock_1_out, comparator_1_eq, comparator_5_eq, comparator_6_lt, comparator_7_gt,
       comparator_8_eq, comparator_9_eq, comparator_10_eq, comparator_11_eq, LAST_BRD_CYCLE,
       multiplexer_5_out, multiplexer_8_out, multiplexer_11_out, multiplexer_14_out, No_Stuffing, not_1_out,
       or_1_out, or_2_out, PL, PWO_E, StartFO_E, StopFO_E, STUFF_done, STUFF_TX, T_idle, TRANS, TSO, WO_E;
  wire [3:0] BRD_COUNT;
  wire [4:0] BufferFIFO_count, fifo_count, multiplexer_4_out, multiplexer_7_out, multiplexer_10_out,
       n5badd1_1_out_2, n5badd1_2_out_2, n5badd1_3_out_2, n5badd1_4_out_2, Par_count, T_count, TOTAL_Words,
       TRANSMIT_COUNT;
  wire [6:0] multiplexer_1_out;
  wire [7:0] subtractor_1_out;
  wire [21:0] EWI, multiplexer_2_out, multiplexer_3_out, multiplexer_6_out, multiplexer_9_out, ParW, Start,
       Stop, TRANSMIT, word_out, xor_1_out;

  Multiplexer #(.width(7)) multiplexer_1 (
    .in0(7'b0110000), .in1(7'b0110001), .out(multiplexer_1_out), .sel(TX));  // open: en
  Clock clock_1 (.out(clock_1_out));
  TTY #(.rows(45), .cols(6)) tty_1 (.data(multiplexer_1_out), .clk(clock_1_out));  // open: we, clr
  and and_1 (and_1_out, E, IDLE, WIS);
  assign xor_1_out = EWI ^ ParW;  // XOR_Gate xor_1, 22 bits wide
  and and_2 (and_2_out, TRANS, STUFF_done);
  Subtractor subtractor_1 (.a(BRD), .b(8'h1), .out(subtractor_1_out));  // open: bin, bout
  or or_1 (or_1_out, PWO_E, and_1_out);
  Multiplexer #(.width(22), .enable("false")) multiplexer_2 (
    .in0(xor_1_out), .in1({22{1'b0}}), .out(multiplexer_2_out), .sel(StopFO_E));
  // Probe on Start
  _22FIFO u_22fifo_1 (
    .CLK(CLK), .Parallel_Signal(IDLE), .Parallel_Unload(StartFO_E), .Paralell_In_Count(5'b00111),
    .Parallel_In(22'h3f), .Parallel_Out(Start));  // open: Serial_In, Serial_In_Signal, Serial_Out_Signal, Serial_Out, FIFO_count
  _22FIFO Transmit_buffer_fifo (
    .CLK(CLK), .Serial_Out_Signal(and_2_out), .Parallel_Signal(PL), .Paralell_In_Count(TRANSMIT_COUNT),
    .Parallel_In(TRANSMIT), .Serial_Out(TSO), .FIFO_count(BufferFIFO_count));  // open: Serial_In, Serial_In_Signal, Parallel_Unload, Parallel_Out
  Comparator #(.width(5), .mode("unsigned")) comparator_1 (
    .a(BufferFIFO_count), .b(5'b00001), .eq(comparator_1_eq));  // open: gt, lt
  Comparator #(.width(4), .mode("unsigned")) comparator_2 (
    .a(BRD_COUNT), .b(subtractor_1_out[3:0]), .eq(LAST_BRD_CYCLE));  // open: gt, lt
  // Probe on EWI
  SECDED SECDED (.in_1(WI), .out_2(EWI));
  _22FIFO Parity_word_fifo (
    .CLK(CLK), .Parallel_Signal(and_1_out), .Parallel_Unload(or_1_out), .Paralell_In_Count(5'b10110),
    .Parallel_In(multiplexer_2_out), .FIFO_count(Par_count), .Parallel_Out(ParW));  // open: Serial_In, Serial_In_Signal, Serial_Out_Signal, Serial_Out
  // Probe on multiplexer_2_out
  // Probe on BufferFIFO_count
  _5bADD1 u_5badd1_1 (.in_1(T_count), .out_2(n5badd1_1_out_2));
  and and_3 (and_3_out, comparator_1_eq, STUFF_done, LAST_BRD_CYCLE);
  T_Flip_Flop t_ff_1 (.clk(CLK), .T(1'b1), .Q(TRANS), .Qn(IDLE), .en(and_4_out));  // open: preset, reset
  and and_4 (and_4_out, T_idle, E);
  and and_5 (and_5_out, E, IDLE, WIS);
  // Probe on Par_count
  // Probe on Stop
  _22FIFO u_22fifo_2 (
    .CLK(CLK), .Parallel_Signal(IDLE), .Parallel_Unload(StopFO_E), .Paralell_In_Count(5'b00110),
    .Parallel_In({22{1'b0}}), .Parallel_Out(Stop));  // open: Serial_In, Serial_In_Signal, Serial_Out_Signal, Serial_Out, FIFO_count
  Register #(.width(5)) register_1 (.D(n5badd1_1_out_2), .en(and_3_out), .Q(T_count), .clk(CLK), .clr(IDLE));
  assign TX = TRANS ? STUFF_TX : 1'bz;  // Controlled_Buffer controlled_buffer_1
  _16FIFO _22_bit_word_fifo (
    .CLK(CLK), .Word_In(EWI), .Word_In_Signal(and_5_out), .Word_Out_Signal(WO_E), .Word_Out(word_out),
    .FIFO_count(fifo_count));  // open: Parallel_load_signal, Parallel_Unload_Signal, Paralell_In_Count, Parallel_In_0, Parallel_In_1, Parallel_In_2, Parallel_In_3, Parallel_In_4, Parallel_In_5, Parallel_In_6, Parallel_In_7, Parallel_In_8, Parallel_In_9, Parallel_In_10, Parallel_In_11, Parallel_In_12, Parallel_In_13, Parallel_In_14, Parallel_In_15, Parallel_out_0, Parallel_out_1, Parallel_out_2, Parallel_out_3, Parallel_out_4, Parallel_out_5, Parallel_out_6, Parallel_out_7, Parallel_out_8, Parallel_out_9, Parallel_out_10, Parallel_out_11, Parallel_out_12, Parallel_out_13, Parallel_out_14, Parallel_out_15
  // Probe on fifo_count
  // Probe on BRD_COUNT
  BRD u_BRD (
    .BRD(BRD[3:0]), .Clock(and_6_out), .BRD_COUNT(BRD_COUNT), .BRDO(BRD_CLK), .BRD_is0(BRD_is0));  // open: in_3, ADVANCE_VAL, in_5, BRD_2, B
  and and_6 (and_6_out, CLK, TRANS);
  Comparator #(.width(5)) comparator_3 (.a(fifo_count), .b({5{1'b0}}), .eq(BUFFER_EMPTY));  // open: gt, lt
  Comparator #(.width(5)) comparator_4 (.a(fifo_count), .b(5'b10000), .eq(FULL));  // open: gt, lt
  bit_stuffer bit_stuffer_1 (
    .new_data_bit(TSO), .TX(STUFF_TX), .Special_flag(No_Stuffing), .STUFF_E(STUFF_done), .BRD_CLK(BRD_CLK),
    .BRD_is0(BRD_is0), .Enable(not_1_out));
  not not_1 (not_1_out, PL);
  Multiplexer #(.width(22), .enable("false")) multiplexer_3 (
    .in1(Start), .out(multiplexer_3_out), .sel(StartFO_E));  // open: in0
  Multiplexer #(.width(5), .enable("false")) multiplexer_4 (
    .in1(5'b00111), .out(multiplexer_4_out), .sel(StartFO_E));  // open: in0
  Multiplexer #(.enable("false")) multiplexer_5 (.in1(1'b1), .out(multiplexer_5_out), .sel(StartFO_E));  // open: in0
  _5bADD1 u_5badd1_2 (.in_1(TOTAL_Words), .out_2(n5badd1_2_out_2));
  _5bADD1 u_5badd1_3 (.in_1(n5badd1_2_out_2), .out_2(n5badd1_3_out_2));
  _5bADD1 u_5badd1_4 (.in_1(n5badd1_3_out_2), .out_2(n5badd1_4_out_2));
  Register #(.width(5)) register_2 (.D(fifo_count), .en(IDLE), .Q(TOTAL_Words), .clk(CLK));  // open: clr
  Multiplexer #(.width(22), .enable("false")) multiplexer_6 (
    .in0(multiplexer_3_out), .in1(word_out), .out(multiplexer_6_out), .sel(WO_E));
  Multiplexer #(.width(5), .enable("false")) multiplexer_7 (
    .in0(multiplexer_4_out), .in1(5'b10110), .out(multiplexer_7_out), .sel(WO_E));
  Multiplexer #(.enable("false")) multiplexer_8 (
    .in0(multiplexer_5_out), .in1(1'b0), .out(multiplexer_8_out), .sel(WO_E));
  Comparator #(.width(5), .mode("unsigned")) comparator_5 (
    .a(T_count), .b({5{1'b0}}), .eq(comparator_5_eq));  // open: gt, lt
  Comparator #(.width(5), .mode("unsigned")) comparator_6 (
    .a(T_count), .b(5'b00001), .lt(comparator_6_lt));  // open: gt, eq
  Comparator #(.width(5), .mode("unsigned")) comparator_7 (
    .a(T_count), .b(TOTAL_Words), .gt(comparator_7_gt));  // open: eq, lt
  Comparator #(.width(5), .mode("unsigned")) comparator_8 (
    .a(T_count), .b(n5badd1_2_out_2), .eq(comparator_8_eq));  // open: gt, lt
  Comparator #(.width(5), .mode("unsigned")) comparator_9 (
    .a(T_count), .b(n5badd1_3_out_2), .eq(comparator_9_eq));  // open: gt, lt
  Comparator #(.width(5), .mode("unsigned")) comparator_10 (
    .a(T_count), .b(n5badd1_4_out_2), .eq(comparator_10_eq));  // open: gt, lt
  or or_2 (or_2_out, StartFO_E, WO_E, PWO_E, StopFO_E);
  and and_7 (PL, or_2_out, comparator_11_eq);
  Comparator #(.width(5), .mode("unsigned")) comparator_11 (
    .a(BufferFIFO_count), .b({5{1'b0}}), .eq(comparator_11_eq));  // open: gt, lt
  Multiplexer #(.width(22), .enable("false")) multiplexer_9 (
    .in0(multiplexer_6_out), .in1(ParW), .out(multiplexer_9_out), .sel(PWO_E));
  Multiplexer #(.width(5), .enable("false")) multiplexer_10 (
    .in0(multiplexer_7_out), .in1(5'b10110), .out(multiplexer_10_out), .sel(PWO_E));
  Multiplexer #(.enable("false")) multiplexer_11 (
    .in0(multiplexer_8_out), .in1(1'b0), .out(multiplexer_11_out), .sel(PWO_E));
  and and_8 (WO_E, ~comparator_6_lt, TRANS, ~comparator_7_gt);  // AND_Gate
  and and_9 (PWO_E, comparator_8_eq, TRANS);
  and and_10 (and_10_out, BTS, IDLE);
  and and_11 (and_11_out, comparator_10_eq, TRANS, STUFF_done);
  // Probe on TRANSMIT
  Multiplexer #(.width(22), .enable("false")) multiplexer_12 (
    .in0(multiplexer_9_out), .in1(Stop), .out(TRANSMIT), .sel(StopFO_E));
  // Probe on TRANSMIT_COUNT
  Multiplexer #(.width(5), .enable("false")) multiplexer_13 (
    .in0(multiplexer_10_out), .in1(5'b00110), .out(TRANSMIT_COUNT), .sel(StopFO_E));
  D_Flip_Flop d_ff_1 (.clk(CLK), .D(multiplexer_14_out), .Q(No_Stuffing));  // open: Qn, preset, en, reset
  Multiplexer #(.enable("false")) multiplexer_14 (
    .in0(multiplexer_11_out), .in1(1'b1), .out(multiplexer_14_out), .sel(StopFO_E));
  and and_12 (StartFO_E, comparator_5_eq, TRANS);
  and and_13 (StopFO_E, comparator_9_eq, TRANS);
  or or_3 (T_idle, and_10_out, and_11_out);

  // Other names for the same wires on the sheet: is0 = BUFFER_EMPTY

  // Notes on the sheet:
  //   BIT STUFFER
endmodule

module testing (
  input  in_1
);

  wire _7ZEROS, and_1_out, and_2_out, and_3_out, CERROR, CLK, d_ff_1_q, d_ff_4_q, DE1, DE2, ENABLE, ERROR,
       IDLE, NOT_STARTED, or_1_out, or_2_out, or_3_out, or_4_out, START_FRAME, STARTED, t_ff_1_q;
  wire [2:0] adder_1_out, adder_2_out, CONS_0, CONS_1, multiplexer_1_out, multiplexer_2_out;
  wire [4:0] multiplexer_3_out, multiplexer_4_out, START_FRAME_FIFO_fifo_count;
  wire [21:0] START_FRAME_FIFO_parallel_out, undriven;

  Clock clock_1 (.out(CLK));
  or or_1 (or_1_out, DE2, DE1);
  Multiplexer #(.width(3), .enable("false")) multiplexer_1 (
    .in1(adder_1_out), .out(multiplexer_1_out), .sel(in_1));  // open: in0
  Adder #(.width(3)) adder_1 (.a(CONS_1), .b(3'b001), .out(adder_1_out));  // open: cin, cout
  Comparator #(.width(3)) comparator_1 (.a(multiplexer_1_out), .b(3'b111), .eq(CERROR));  // open: gt, lt
  D_Flip_Flop d_ff_1 (.clk(CLK), .D(or_1_out), .Q(d_ff_1_q), .en(or_1_out), .reset(START_FRAME));  // open: Qn, preset
  // Probe on multiplexer_1_out
  Register #(.width(3)) register_1 (.D(multiplexer_1_out), .en(ENABLE), .Q(CONS_1), .clk(CLK));  // open: clr
  or or_2 (or_2_out, CERROR, ERROR);
  and and_1 (and_1_out, ~in_1, ENABLE);  // AND_Gate
  or or_3 (or_3_out, ~in_1, in_1);  // OR_Gate
  D_Flip_Flop d_ff_2 (.clk(CLK), .D(or_2_out), .Q(ERROR), .en(ENABLE), .reset(and_1_out));  // open: Qn, preset
  T_Flip_Flop t_ff_1 (.clk(CLK), .T(or_3_out), .Q(t_ff_1_q));  // open: Qn, preset, reset, en
  // Probe on multiplexer_2_out
  Adder #(.width(3)) adder_2 (.a(CONS_0), .b(3'b001), .out(adder_2_out));  // open: cin, cout
  D_Flip_Flop d_ff_3 (.clk(CLK), .D(or_4_out), .Q(IDLE), .en(ENABLE), .reset(and_2_out));  // open: Qn, preset
  and and_2 (and_2_out, in_1, ENABLE);
  or or_4 (or_4_out, IDLE, _7ZEROS);
  Multiplexer #(.width(3), .enable("false")) multiplexer_2 (
    .in0(adder_2_out), .out(multiplexer_2_out), .sel(in_1));  // open: in1
  D_Flip_Flop d_ff_4 (.clk(CLK), .D(t_ff_1_q), .Q(d_ff_4_q));  // open: Qn, preset, en, reset
  Comparator #(.width(3)) comparator_2 (.a(3'b111), .b(multiplexer_2_out), .eq(_7ZEROS));  // open: gt, lt
  Register #(.width(3)) register_2 (.D(multiplexer_2_out), .en(ENABLE), .Q(CONS_0), .clk(CLK));  // open: clr
  _22FIFO DATA_FIFO (.CLK(CLK));  // open: Serial_In, Serial_In_Signal, Serial_Out_Signal, Parallel_Signal, Parallel_Unload, Paralell_In_Count, Parallel_In, Serial_Out, FIFO_count, Parallel_Out
  and and_3 (and_3_out, NOT_STARTED, CERROR, ~IDLE);  // AND_Gate
  _22FIFO START_FRAME_FIFO (
    .CLK(CLK), .Serial_In(and_3_out), .Serial_In_Signal(in_1), .Parallel_Signal(1'b1),
    .Parallel_Unload(1'b1), .Paralell_In_Count(multiplexer_3_out), .Parallel_In(undriven),
    .FIFO_count(START_FRAME_FIFO_fifo_count), .Parallel_Out(START_FRAME_FIFO_parallel_out));  // open: Serial_Out_Signal, Serial_Out
  Multiplexer #(.width(5), .enable("false")) multiplexer_3 (
    .in0(START_FRAME_FIFO_fifo_count), .in1({5{1'b0}}), .out(multiplexer_3_out), .sel(CERROR));
  D_Flip_Flop d_ff_5 (.clk(CLK), .Q(STARTED), .Qn(NOT_STARTED), .en(ENABLE));  // open: D, preset, reset
  Multiplexer #(.width(5), .enable("false")) multiplexer_4 (
    .in1({5{1'b0}}), .out(multiplexer_4_out), .sel(CERROR));  // open: in0
  _22FIFO u_22fifo_1 ();  // open: CLK, Serial_In, Serial_In_Signal, Serial_Out_Signal, Parallel_Signal, Parallel_Unload, Paralell_In_Count, Parallel_In, Serial_Out, FIFO_count, Parallel_Out

  // Other names for the same wires on the sheet: RX = in_1
endmodule

module myNIC (
  input  minus_CS,
  input  minus_O,
  input  minus_W,
  input  RX,
  input  [1:0] ADDR,
  input  [7:0] DATAIN,
  input  CLK,
  output minus_INT,
  output TX,
  output [7:0] DATAOUT
);

  wire and_2_out, and_3_out, and_4_out, and_5_out, and_6_out, and_7_out, and_8_out, and_9_out, and_10_out,
       BRD_WRITEENABLE, BYTECOUNT, CLK_t, comparator_1_lt, comparator_2_gt, CS, d_ff_1_qn, d_ff_2_qn,
       DATA_WRITEENABLE, demultiplexer_2_out13, DR, DRIM, ENA, ENA_IN, FE, FE_W, FEC, FEIM, IM_WRITEENABLE,
       INT, multiplexer_8_out, nand_1_out, nand_2_out, NF, NF_W, NFC, not_1_out, O, OR, or_2_out, or_3_out,
       or_4_out, or_5_out, or_6_out, or_7_out, OR_W, ORC, READ, SC_WRITEENABLE, SHOULDTRANSMIT, TBF, TF,
       TF_W, TIDLE, TXBUFFEREMPTY, undriven, W, WRITE;
  wire [6:0] IM;
  wire [6:1] SCIN;
  wire [6:2] SC;
  wire [6:6] SC_W;
  wire [7:0] and_1_out, BRD, BRD_W, DATA_FROM_RX, DATA_W, edit_register_1_updated_8_bits, IM_star, IM_W,
       INTERRUPT_MASKS_q, multiplexer_2_out, not_7_out, SC_star, TXBUFFER, UPDATE_VALS;
  wire [15:8] WORDIN;

  Demultiplexer #(.select(2), .width(8), .enable("false")) demultiplexer_1 (
    .out0({FEC, SCIN[6], ORC, NFC, SCIN[3:1], ENA_IN}), .out1(IM_W), .out2(DATA_W), .out3(BRD_W),
    .in(DATAIN), .sel(ADDR));
  Multiplexer #(.width(8), .enable("false")) multiplexer_1 (.in1(UPDATE_VALS), .out(DATAOUT), .sel(READ));  // open: in0
  Multiplexer #(.width(8), .enable("false")) multiplexer_2 (
    .in0({FE, SC[6], OR, NF, SC[3:2], DR, ENA}), .in1({FE_W, SC_W[6], OR_W, NF_W, SC[3:2], DR, ENA_IN}),
    .out(multiplexer_2_out), .sel(SC_WRITEENABLE));
  assign and_1_out = {FEIM, IM[6:2], DRIM, IM[0]} & {FE, SC[6], OR, NF, SC[3:2], DR, ENA};  // AND_Gate and_1, 8 bits wide
  Clock clock_1 (.out(CLK_t));
  edit_register edit_register_1 (
    ._8_bit(multiplexer_2_out), .BIT(3'b011), .V(TIDLE), .Enable(1'b1),
    .updated_8_bits(edit_register_1_updated_8_bits));
  not not_1 (not_1_out, TBF);
  edit_register edit_register_2 (
    ._8_bit(IM_star), .BIT(3'b000), .V(1'b0), .Enable(1'b1), .updated_8_bits({FEIM, IM[6:2], DRIM, IM[0]}));
  not not_2 (minus_INT, INT);
  not not_3 (CS, minus_CS);
  not not_4 (O, minus_O);
  not not_5 (W, minus_W);
  edit_register edit_register_3 (
    ._8_bit(edit_register_1_updated_8_bits), .BIT(3'b010), .V(not_1_out), .Enable(1'b1),
    .updated_8_bits(SC_star));
  or or_1 (INT, and_1_out[0], and_1_out[1], and_1_out[2], and_1_out[3], and_1_out[4], and_1_out[5], and_1_out[6], and_1_out[7]);
  Register STATUS_COMMAND (
    .D(SC_star), .en(undriven), .Q({FE, SC[6], OR, NF, SC[3:2], DR, ENA}), .clk(CLK_t));  // open: clr
  Multiplexer #(.enable("false")) multiplexer_3 (.in0(TF), .in1(1'b0), .out(TF_W), .sel(TXBUFFEREMPTY));
  Multiplexer #(.enable("false")) multiplexer_4 (.in0(NF), .in1(1'b0), .out(NF_W), .sel(or_2_out));
  or or_2 (or_2_out, NFC, ~ENA_IN);  // OR_Gate
  Multiplexer #(.enable("false")) multiplexer_5 (.in0(OR), .in1(1'b0), .out(OR_W), .sel(or_3_out));
  or or_3 (or_3_out, ORC, ~ENA_IN);  // OR_Gate
  Multiplexer #(.enable("false")) multiplexer_6 (.in0(SC[6]), .in1(1'b0), .out(SC_W[6]), .sel(or_4_out));
  or or_4 (or_4_out, SCIN[6], ~ENA_IN);  // OR_Gate
  Multiplexer #(.enable("false")) multiplexer_7 (.in0(FE), .in1(1'b0), .out(FE_W), .sel(or_5_out));
  or or_5 (or_5_out, FEC, ~ENA_IN);  // OR_Gate
  D_Flip_Flop d_ff_1 (.clk(CLK_t), .D(W), .Qn(d_ff_1_qn), .en(CS), .reset(minus_CS));  // open: Q, preset
  D_Flip_Flop d_ff_2 (.clk(CLK_t), .D(O), .Qn(d_ff_2_qn), .en(CS), .reset(minus_CS));  // open: Q, preset
  and and_2 (and_2_out, W, d_ff_1_qn);
  and and_3 (and_3_out, O, d_ff_2_qn);
  D_Flip_Flop d_ff_3 (.clk(CLK_t), .D(and_2_out), .Q(WRITE), .en(CS), .reset(minus_CS));  // open: Qn, preset
  D_Flip_Flop d_ff_4 (.clk(CLK_t), .D(and_3_out), .Q(READ), .en(CS), .reset(minus_CS));  // open: Qn, preset
  assign IM_star = ~INTERRUPT_MASKS_q;  // NOT_Gate not_6, 8 bits wide
  Register INTERRUPT_MASKS (.D(not_7_out), .en(IM_WRITEENABLE), .Q(INTERRUPT_MASKS_q), .clk(CLK_t));  // open: clr
  assign not_7_out = ~UPDATE_VALS;  // NOT_Gate not_7, 8 bits wide
  and and_4 (and_4_out, BYTECOUNT, DATA_WRITEENABLE);
  or or_6 (or_6_out, and_4_out, and_5_out);
  and and_5 (and_5_out, SCIN[1], BYTECOUNT);
  Multiplexer #(.disabled(0), .enable("false")) multiplexer_8 (
    .in0(1'b0), .in1(1'b1), .out(multiplexer_8_out), .sel(and_6_out));
  and and_6 (and_6_out, SCIN[1], BYTECOUNT);
  and and_7 (and_7_out, ~BYTECOUNT, DATA_WRITEENABLE);  // AND_Gate
  and and_8 (and_8_out, ~TXBUFFEREMPTY, WRITE, or_7_out);  // AND_Gate
  or or_7 (or_7_out, and_9_out, SHOULDTRANSMIT);
  D_Flip_Flop d_ff_5 (.clk(CLK_t), .D(multiplexer_8_out), .Q(SHOULDTRANSMIT));  // open: Qn, preset, en, reset
  // Probe on TXBUFFER
  Register u_TXBUFFER (.D(UPDATE_VALS), .en(and_7_out), .Q(TXBUFFER), .clk(CLK_t));  // open: clr
  T_Flip_Flop t_ff_1 (
    .clk(CLK_t), .T(1'b1), .Q(BYTECOUNT), .reset(SHOULDTRANSMIT), .en(DATA_WRITEENABLE));  // open: Qn, preset
  Multiplexer #(.width(8), .enable("false")) multiplexer_9 (
    .in0({8{1'b0}}), .in1(DATAIN), .out(WORDIN), .sel(and_10_out));
  and and_9 (and_9_out, ~BYTECOUNT, SCIN[1]);  // AND_Gate
  // Probe on {WORDIN, TXBUFFER}
  and and_10 (and_10_out, BYTECOUNT, DATA_WRITEENABLE);
  // NOT_Gate not_8 has open pins: in=TIDLE, out=open
  Register u_BRD (.D(UPDATE_VALS), .en(BRD_WRITEENABLE), .Q(BRD), .clk(CLK_t));  // open: clr
  nand nand_1 (nand_1_out, READ, WRITE);
  Multiplexer #(.select(4), .width(8)) multiplexer_10 (
    .in1({FE_W, SC_W[6], OR_W, NF_W, SC[3:2], DR, ENA_IN}), .in2({FE, SC[6], OR, NF, SC[3:2], DR, ENA}),
    .in5(IM_W), .in6({FEIM, IM[6:2], DRIM, IM[0]}), .in9(DATA_W), .in10(DATA_FROM_RX), .in13(BRD_W),
    .in14(BRD), .out(UPDATE_VALS), .sel({ADDR, READ, WRITE}), .en(nand_2_out));  // open: in0, in3, in4, in7, in8, in11, in12, in15
  nand nand_2 (nand_2_out, READ, WRITE);
  Demultiplexer #(.select(4)) demultiplexer_2 (
    .out1(SC_WRITEENABLE), .out5(IM_WRITEENABLE), .out9(DATA_WRITEENABLE), .out13(demultiplexer_2_out13),
    .in(1'b1), .sel({ADDR, READ, WRITE}), .en(nand_1_out));  // open: out0, out2, out3, out4, out6, out7, out8, out10, out11, out12, out14, out15
  Comparator #(.mode("unsigned")) comparator_1 (.a(UPDATE_VALS), .b(8'h3), .lt(comparator_1_lt));  // open: gt, eq
  Comparator #(.mode("unsigned")) comparator_2 (.a(UPDATE_VALS), .b(8'hf), .gt(comparator_2_gt));  // open: eq, lt
  and and_11 (BRD_WRITEENABLE, demultiplexer_2_out13, ~comparator_1_lt, ~comparator_2_gt, ENA);  // AND_Gate

  // Other names for the same wires on the sheet: BRDIN[7:0] = BRD_W; IM (some bits) = {FEIM, DRIM}; TBNFIM = IM[2];
  //   TXIIM = IM[3]; NIM = IM[4]; ORIM = IM[5]; SDEIM = IM[6]; IMIN[7:0] = IM_W;
  //   SC (some bits) = {FE, OR, NF, DR, ENA}; SDE = SC[6]; SC_W (some bits) = {FE_W, OR_W, NF_W, SC[3:2], DR, ENA_IN};
  //   TBNF = SC[2]; TXI = SC[3]; SDE_W = SC_W[6]; ENA_W = ENA_IN; SCIN (some bits) = {FEC, ORC, NFC, ENA_IN};
  //   TF_IN = SCIN[1]; SDEC = SCIN[6]; TXIN[7:0] = DATA_W; WORDIN[7:0] = TXBUFFER
endmodule

module edit_register (
  input  [7:0] _8_bit,
  input  [2:0] BIT,
  input  V,
  input  Enable,
  output [7:0] updated_8_bits
);

  wire and_9_out, and_10_out, and_11_out, and_12_out, and_13_out, and_14_out, and_15_out, and_16_out,
       and_17_out, and_18_out, and_19_out, and_20_out, and_21_out, and_22_out, and_23_out, and_24_out,
       demultiplexer_1_out0, demultiplexer_1_out1, demultiplexer_1_out2, demultiplexer_1_out3,
       demultiplexer_1_out4, demultiplexer_1_out5, demultiplexer_1_out6, demultiplexer_1_out7, s0, s1, s2,
       s3, s4, s5, s6, s7;

  Demultiplexer #(.select(3), .disabled(0), .enable("false")) demultiplexer_1 (
    .out0(demultiplexer_1_out0), .out1(demultiplexer_1_out1), .out2(demultiplexer_1_out2),
    .out3(demultiplexer_1_out3), .out4(demultiplexer_1_out4), .out5(demultiplexer_1_out5),
    .out6(demultiplexer_1_out6), .out7(demultiplexer_1_out7), .in(1'b1), .sel(BIT));
  and and_1 (s0, Enable, demultiplexer_1_out0);
  and and_2 (s1, Enable, demultiplexer_1_out1);
  and and_3 (s2, Enable, demultiplexer_1_out2);
  and and_4 (s3, Enable, demultiplexer_1_out3);
  and and_5 (s4, Enable, demultiplexer_1_out4);
  and and_6 (s5, Enable, demultiplexer_1_out5);
  and and_7 (s6, Enable, demultiplexer_1_out6);
  and and_8 (s7, Enable, demultiplexer_1_out7);
  and and_9 (and_9_out, s0, V);
  and and_10 (and_10_out, ~s0, _8_bit[0]);  // AND_Gate
  and and_11 (and_11_out, s1, V);
  and and_12 (and_12_out, ~s1, _8_bit[1]);  // AND_Gate
  and and_13 (and_13_out, s2, V);
  and and_14 (and_14_out, ~s2, _8_bit[2]);  // AND_Gate
  and and_15 (and_15_out, s3, V);
  and and_16 (and_16_out, ~s3, _8_bit[3]);  // AND_Gate
  and and_17 (and_17_out, s4, V);
  and and_18 (and_18_out, ~s4, _8_bit[4]);  // AND_Gate
  and and_19 (and_19_out, s5, V);
  and and_20 (and_20_out, ~s5, _8_bit[5]);  // AND_Gate
  and and_21 (and_21_out, s6, V);
  and and_22 (and_22_out, ~s6, _8_bit[6]);  // AND_Gate
  and and_23 (and_23_out, s7, V);
  and and_24 (and_24_out, ~s7, _8_bit[7]);  // AND_Gate
  or or_1 (updated_8_bits[0], and_9_out, and_10_out);
  or or_2 (updated_8_bits[1], and_11_out, and_12_out);
  or or_3 (updated_8_bits[2], and_13_out, and_14_out);
  or or_4 (updated_8_bits[3], and_15_out, and_16_out);
  or or_5 (updated_8_bits[4], and_17_out, and_18_out);
  or or_6 (updated_8_bits[5], and_19_out, and_20_out);
  or or_7 (updated_8_bits[6], and_21_out, and_22_out);
  or or_8 (updated_8_bits[7], and_23_out, and_24_out);

  // Other names for the same wires on the sheet: b1 = BIT[0]; b2 = BIT[1]; b3 = BIT[2]; E = Enable; F[7:0] = _8_bit;
  //   F_star[7:0] = updated_8_bits

  // Notes on the sheet:
  //   Enable: pull=up
endmodule

module BIT_SAMPLER (
  input  RX,
  input  CLK,
  input  [7:0] BRD,
  output out_4,
  output out_5,
  output out_6
);

  wire adder_1_cout, ADV, and_1_out, and_2_out, and_3_out, and_4_out, and_5_out, and_6_out, and_8_out,
       and_9_out, and_12_out, and_13_out, BRD_isodd, CLK_t, comparator_1_eq, comparator_2_eq,
       comparator_3_eq, comparator_4_eq, comparator_5_eq, comparator_6_eq, comparator_7_eq, comparator_8_eq,
       data_bit_star, DELAY, DELAYED, multiplexer_2_out, new_data_signal_star, noise_flag_star, or_1_out,
       or_2_out, or_3_out, or_4_out, or_5_out, or_6_out, S1, S2, S3;
  wire [3:0] ADVANCE_VAL, BRD_1, BRD_1_2, BRD_2, BRD_COUNT;
  wire [7:1] divider_1_rem;

  Clock clock_1 (.out(CLK_t));
  Divider divider_1 (.a(BRD), .b(8'h2), .rem({divider_1_rem, BRD_isodd}));  // open: out, upper
  Subtractor #(.width(4)) subtractor_1 (.a(BRD[3:0]), .b(4'b0001), .out(BRD_1));  // open: bin, bout
  Divider #(.width(4)) divider_2 (.a(BRD_1), .b(4'b0010), .out(BRD_1_2));  // open: upper, rem
  Divider #(.width(4)) divider_3 (.a(BRD[3:0]), .b(4'b0010), .out(BRD_2));  // open: upper, rem
  and and_1 (and_1_out, BRD_isodd, comparator_1_eq);
  Comparator #(.width(4), .mode("unsigned")) comparator_1 (
    .a(BRD_COUNT), .b(4'b0000), .eq(comparator_1_eq));  // open: gt, lt
  and and_2 (and_2_out, ~BRD_isodd, comparator_2_eq);  // AND_Gate
  Comparator #(.width(4), .mode("unsigned")) comparator_2 (
    .a(BRD_COUNT), .b(4'b0001), .eq(comparator_2_eq));  // open: gt, lt
  and and_3 (and_3_out, BRD_isodd, comparator_3_eq);
  Comparator #(.width(4), .mode("unsigned")) comparator_3 (
    .a(BRD_COUNT), .b(BRD_1_2), .eq(comparator_3_eq));  // open: gt, lt
  and and_4 (and_4_out, ~BRD_isodd, comparator_4_eq);  // AND_Gate
  Comparator #(.width(4), .mode("unsigned")) comparator_4 (
    .a(BRD_COUNT), .b(BRD_2), .eq(comparator_4_eq));  // open: gt, lt
  Comparator #(.width(4), .mode("unsigned")) comparator_5 (
    .a(BRD_COUNT), .b(BRD_1), .eq(comparator_5_eq));  // open: gt, lt
  and and_5 (and_5_out, S1, S2, ~RX);  // AND_Gate
  and and_6 (and_6_out, ~S1, ~S2, RX);  // AND_Gate
  Comparator #(.width(4), .mode("unsigned")) comparator_6 (
    .a(BRD_COUNT), .b(BRD_1), .eq(comparator_6_eq));  // open: gt, lt
  or or_1 (or_1_out, and_1_out, and_2_out);
  or or_2 (or_2_out, and_3_out, and_4_out);
  Multiplexer multiplexer_1 (.in0(RX), .sel(ADV));  // open: in1, out, en
  or or_3 (or_3_out, and_5_out, and_6_out);
  and and_7 (ADV, or_3_out, comparator_6_eq);
  and and_8 (and_8_out, RX, S2, ~S1);  // AND_Gate
  or or_4 (or_4_out, and_8_out, and_9_out);
  and and_9 (and_9_out, ~RX, ~S2, S1);  // AND_Gate
  and and_10 (DELAY, or_4_out, comparator_7_eq);
  Comparator #(.width(4), .mode("unsigned")) comparator_7 (
    .a(BRD_COUNT), .b(BRD_1), .eq(comparator_7_eq));  // open: gt, lt
  or or_5 (or_5_out, or_1_out, ADV);
  D_Flip_Flop d_ff_1 (.clk(CLK_t), .D(RX), .Q(S2), .en(or_2_out));  // open: Qn, preset, reset
  assign S3 = comparator_5_eq ? RX : 1'bz;  // Controlled_Buffer controlled_buffer_1
  BRD u_brd_1 (
    .BRD(BRD[3:0]), .Clock(CLK_t), .in_3(ADV), .ADVANCE_VAL(ADVANCE_VAL), .in_5(DELAY), .B(BRD_COUNT));  // open: BRD_2, BRD_COUNT, BRDO, BRD_is0
  D_Flip_Flop d_ff_2 (.clk(CLK_t), .D(RX), .Q(S1), .en(or_5_out));  // open: Qn, preset, reset
  // Probe on BRD_COUNT
  Multiplexer #(.enable("false")) multiplexer_2 (.in0(DELAY), .in1(1'b0), .out(multiplexer_2_out), .sel(DELAYED));
  // Probe on BRD_COUNT
  Comparator #(.width(4), .mode("unsigned")) comparator_8 (
    .a(BRD_COUNT), .b(BRD_1), .eq(comparator_8_eq));  // open: gt, lt
  D_Flip_Flop d_ff_3 (.clk(CLK_t), .D(multiplexer_2_out), .Q(DELAYED));  // open: Qn, preset, en, reset
  Adder #(.width(1)) adder_1 (.a(S1), .b(S2), .cin(S3), .cout(adder_1_cout));  // open: out
  and and_11 (new_data_signal_star, comparator_8_eq, ~ADV);  // AND_Gate
  D_Flip_Flop d_ff_4 (.clk(CLK_t), .D(new_data_signal_star), .Q(out_4));  // open: Qn, preset, en, reset
  D_Flip_Flop d_ff_5 (.clk(CLK_t), .D(noise_flag_star), .Q(out_6));  // open: Qn, preset, en, reset
  Multiplexer #(.width(4), .enable("false")) multiplexer_3 (
    .in0(4'b0010), .in1(4'b0001), .out(ADVANCE_VAL), .sel(BRD_isodd));
  Multiplexer #(.enable("false")) multiplexer_4 (
    .in0(1'b0), .in1(adder_1_cout), .out(data_bit_star), .sel(new_data_signal_star));
  // Probe on ADVANCE_VAL
  Adder #(.width(4)) adder_2 (.b(4'b0001));  // open: a, out, cin, cout
  and and_12 (and_12_out, ~S1, S2, ~S3);  // AND_Gate
  or or_6 (or_6_out, and_12_out, and_13_out);
  and and_13 (and_13_out, S1, ~S2, S3);  // AND_Gate
  Multiplexer #(.enable("false")) multiplexer_5 (
    .in0(1'b0), .in1(or_6_out), .out(noise_flag_star), .sel(new_data_signal_star));
  D_Flip_Flop d_ff_6 (.clk(CLK_t), .D(data_bit_star), .Q(out_5));  // open: Qn, preset, en, reset

  // Other names for the same wires on the sheet: BRD4BIT[3:0] = BRD[3:0]; data_bit = out_5; new_data_signal = out_4;
  //   noise_flag = out_6

  // Notes on the sheet:
  //   RX: pull=down
  //   ADVANCING
  //   when brd count cycle is on its last cycle
endmodule

module BIT_DESTUFFER (
  input  RX,
  input  CLK,
  output Start_Signal,
  output [21:0] WORD_OUT,
  output NEW_WORD_SIGNAL,
  output parity_word_signal,
  output FRAME_ERROR
);

  wire _5_0s, _5_1s, _6_0s, _7_Consecutive0s_star, and_1_out, and_2_out, and_4_out, and_5_out, and_11_out,
       and_12_out, and_13_out, CLK_t, clock_2_out, comparator_2_lt, comparator_7_eq, comparator_8_eq,
       comparator_9_eq, comparator_12_eq, comparator_13_eq, comparator_14_gt, comparator_15_lt, d_ff_1_q,
       d_ff_1_qn, FIFO2_count_22, FIFO_count_22, IDLE, multiplexer_8_out, NEW_WORD_SIGNAL_t, not_2_out,
       not_3_out, or_1_out, or_3_out, or_5_out, or_6_out, Parallel_unload, parity_word_signal_t, SIS,
       stuff_bit, WordFrame;
  wire [4:0] adder_3_out, adder_4_out, Consecutive0s, Consecutive0s___1, Consecutive0s_star, Consecutive1s,
       Consecutive1s___1, Consecutive1s_star, FIFO2count, FIFOcount, multiplexer_1_out, multiplexer_2_out,
       multiplexer_5_out, multiplexer_6_out, register_4_q, WordFrame_count;
  wire [6:0] multiplexer_7_out;
  wire [21:0] FIFO_output;

  Multiplexer #(.width(5), .enable("false")) multiplexer_1 (
    .in0({5{1'b0}}), .in1(5'b00001), .out(multiplexer_1_out), .sel(Start_Signal));
  Clock clock_1 (.out(CLK_t));
  Multiplexer #(.width(5), .enable("false")) multiplexer_2 (
    .in0({5{1'b0}}), .in1(multiplexer_1_out), .out(multiplexer_2_out), .sel(RX));
  Comparator #(.width(5), .mode("unsigned")) comparator_1 (.b(5'b00110));  // open: a, gt, eq, lt
  Comparator #(.width(5), .mode("unsigned")) comparator_2 (
    .a(Consecutive0s_star), .b(5'b00111), .lt(comparator_2_lt));  // open: gt, eq
  not not_1 (_7_Consecutive0s_star, comparator_2_lt);
  Multiplexer #(.width(5), .enable("false")) multiplexer_3 (
    .in0(multiplexer_2_out), .in1(Consecutive1s___1), .out(Consecutive1s_star), .sel(and_1_out));
  and and_1 (and_1_out, RX, ~Start_Signal, ~stuff_bit);  // AND_Gate
  Adder #(.width(5)) adder_1 (.a(Consecutive1s), .b(5'b00001), .out(Consecutive1s___1));  // open: cin, cout
  or or_1 (or_1_out, RX, stuff_bit);
  Adder #(.width(5)) adder_2 (.a(Consecutive0s), .b(5'b00001), .out(Consecutive0s___1));  // open: cin, cout
  and and_2 (and_2_out, FIFO_count_22, SIS);
  Multiplexer #(.width(5), .enable("false")) multiplexer_4 (
    .in0(Consecutive0s___1), .in1({5{1'b0}}), .out(Consecutive0s_star), .sel(or_1_out));
  not not_2 (not_2_out, FRAME_ERROR);
  and and_3 (SIS, WordFrame, ~stuff_bit);  // AND_Gate
  or or_2 (Parallel_unload, and_2_out, _6_0s);
  Multiplexer #(.width(5)) multiplexer_5 (
    .in0(Consecutive1s_star), .in1(5'b00001), .out(multiplexer_5_out), .sel(and_4_out));  // open: en
  and and_4 (and_4_out, Parallel_unload, RX);
  Multiplexer #(.width(5)) multiplexer_6 (
    .in0(Consecutive0s_star), .in1(5'b00001), .out(multiplexer_6_out), .sel(and_5_out));  // open: en
  and and_5 (and_5_out, Parallel_unload, not_3_out);
  not not_3 (not_3_out, RX);
  and and_6 (NEW_WORD_SIGNAL, not_2_out, NEW_WORD_SIGNAL_t);
  and and_7 (parity_word_signal, not_2_out, parity_word_signal_t);
  _22FIFO fifo1 (
    .CLK(CLK_t), .Serial_In(RX), .Serial_In_Signal(SIS), .Parallel_Unload(Parallel_unload),
    .FIFO_count(FIFOcount), .Parallel_Out(FIFO_output));  // open: Serial_Out_Signal, Parallel_Signal, Paralell_In_Count, Parallel_In, Serial_Out
  Multiplexer #(.width(7)) multiplexer_7 (
    .in0(7'b0110000), .in1(7'b0110001), .out(multiplexer_7_out), .sel(RX), .en(SIS));
  Clock clock_2 (.out(clock_2_out));
  TTY #(.rows(20), .cols(5)) tty_1 (.data(multiplexer_7_out), .clk(clock_2_out));  // open: we, clr
  // Probe on multiplexer_5_out
  Register #(.width(5)) register_1 (.D(multiplexer_5_out), .Q(Consecutive1s), .clk(CLK_t));  // open: en, clr
  // Probe on multiplexer_6_out
  // Probe on FIFOcount
  // Probe on Consecutive1s
  // Probe on Consecutive0s
  Register #(.width(5)) register_2 (.D(multiplexer_6_out), .Q(Consecutive0s), .clk(CLK_t));  // open: en, clr
  and and_8 (NEW_WORD_SIGNAL_t, Parallel_unload, FIFO2_count_22);
  and and_9 (parity_word_signal_t, _6_0s, Parallel_unload);
  or or_3 (or_3_out, Parallel_unload, _6_0s);
  // Probe on FIFO2count
  _22FIFO fifo2 (
    .CLK(CLK_t), .Parallel_Signal(or_3_out), .Parallel_Unload(or_3_out), .Paralell_In_Count(FIFOcount),
    .Parallel_In(FIFO_output), .FIFO_count(FIFO2count), .Parallel_Out(WORD_OUT));  // open: Serial_In, Serial_In_Signal, Serial_Out_Signal, Serial_Out
  Multiplexer #(.enable("false")) multiplexer_8 (.in0(_5_1s), .in1(_5_0s), .out(multiplexer_8_out), .sel(RX));
  D_Flip_Flop d_ff_1 (
    .clk(CLK_t), .D(Start_Signal), .Q(d_ff_1_q), .Qn(d_ff_1_qn), .en(d_ff_1_qn), .reset(_6_0s));  // open: preset
  D_Flip_Flop d_ff_2 (.clk(CLK_t), .D(_7_Consecutive0s_star), .Q(IDLE), .reset(RX));  // open: Qn, preset, en
  Adder #(.width(5)) adder_3 (.a(WordFrame_count), .b(5'b00001), .out(adder_3_out));  // open: cin, cout
  Comparator #(.width(5), .mode("unsigned")) comparator_3 (
    .a(Consecutive1s), .b(5'b00110), .eq(Start_Signal));  // open: gt, lt
  Comparator #(.width(5), .mode("unsigned")) comparator_4 (
    .a(Consecutive0s), .b(5'b00101), .eq(_5_0s));  // open: gt, lt
  or or_4 (WordFrame, Start_Signal, d_ff_1_q);
  Register #(.width(5)) register_3 (.D(adder_3_out), .en(WordFrame), .Q(WordFrame_count), .clk(CLK_t), .clr(_6_0s));
  and and_10 (stuff_bit, WordFrame, multiplexer_8_out, ~IDLE);  // AND_Gate
  D_Flip_Flop d_ff_3 (.clk(CLK_t));  // open: D, Q, Qn, preset, en, reset
  D_Flip_Flop d_ff_4 (.clk(CLK_t));  // open: D, Q, Qn, preset, en, reset
  Comparator #(.width(5), .mode("unsigned")) comparator_5 (
    .a(FIFOcount), .b(5'b10110), .eq(FIFO_count_22));  // open: gt, lt
  Comparator #(.width(5), .mode("unsigned")) comparator_6 (
    .a(FIFO2count), .b(5'b10110), .eq(FIFO2_count_22));  // open: gt, lt
  Comparator #(.width(5), .mode("unsigned")) comparator_7 (
    .a(FIFOcount), .b(5'b00110), .eq(comparator_7_eq));  // open: gt, lt
  Comparator #(.width(5), .mode("unsigned")) comparator_8 (
    .a({5{1'b0}}), .b(FIFOcount), .eq(comparator_8_eq));  // open: gt, lt
  Comparator #(.width(5), .mode("unsigned")) comparator_9 (
    .a({5{1'b0}}), .b(register_4_q), .eq(comparator_9_eq));  // open: gt, lt
  Adder #(.width(5)) adder_4 (.a(register_4_q), .b(5'b00001), .out(adder_4_out));  // open: cin, cout
  Comparator #(.width(5), .mode("unsigned")) comparator_10 (
    .a(Consecutive0s), .b(5'b00110), .eq(_6_0s));  // open: gt, lt
  Comparator #(.width(5), .mode("unsigned")) comparator_11 (
    .a(Consecutive1s), .b(5'b00101), .eq(_5_1s));  // open: gt, lt
  Comparator #(.width(5), .mode("unsigned")) comparator_12 (
    .a(FIFO2count), .b({5{1'b0}}), .eq(comparator_12_eq));  // open: gt, lt
  or or_5 (or_5_out, ~comparator_8_eq, ~comparator_9_eq);  // OR_Gate
  Register #(.width(5)) register_4 (.D(adder_4_out), .en(Parallel_unload), .Q(register_4_q), .clk(CLK_t));  // open: clr
  // Probe on register_4_q
  Comparator #(.width(5), .mode("unsigned")) comparator_13 (
    .a(register_4_q), .b(5'b00001), .eq(comparator_13_eq));  // open: gt, lt
  or or_6 (or_6_out, comparator_13_eq, comparator_14_gt);
  Comparator #(.width(5), .mode("unsigned")) comparator_14 (
    .a(FIFOcount), .b(5'b10110), .gt(comparator_14_gt));  // open: eq, lt
  D_Flip_Flop d_ff_5 (.clk(CLK_t));  // open: D, Q, Qn, preset, en, reset
  D_Flip_Flop d_ff_6 (.clk(CLK_t));  // open: D, Q, Qn, preset, en, reset
  and and_11 (and_11_out, comparator_7_eq, _6_0s, comparator_12_eq);
  and and_12 (and_12_out, Start_Signal, or_5_out, WordFrame);
  Comparator #(.width(5), .mode("unsigned")) comparator_15 (
    .a(5'b10000), .b(register_4_q), .lt(comparator_15_lt));  // open: gt, eq
  and and_13 (and_13_out, or_6_out, _6_0s);
  or or_7 (FRAME_ERROR, and_11_out, and_12_out, comparator_15_lt, and_13_out);

  // Other names for the same wires on the sheet: _6_1s = Start_Signal; StartFrame = Start_Signal; StopFrame = _6_0s

  // Notes on the sheet:
  //   this rx is coming from the bit sampler with their signal on 
  //   SETTING UP THE STATES
  //   COUNTING WHILE IN WORDFRAME
  //   Reset when stop frame received
endmodule

module SECDED_DECODER (
  input  CLK,
  input  WIS,
  input  PARITY_SIGNAL,
  input  [21:0] in_4,
  input  START_FRAME,
  output FRAME_ERROR,
  output SECDED_ERROR,
  output [4:0] DATAWORD_COUNT,
  output [15:0] out_9,
  output [15:0] out_10,
  output [15:0] out_11,
  output [15:0] out_12,
  output [15:0] out_13,
  output [15:0] out_14,
  output [15:0] out_15,
  output [15:0] out_16,
  output [15:0] out_17,
  output [15:0] out_18,
  output [15:0] out_19,
  output [15:0] out_20,
  output [15:0] out_21,
  output [15:0] out_22,
  output [15:0] out_23,
  output [15:0] out_24
);

  wire and_1_out, and_2_out, and_3_out, and_4_out, and_5_out, and_6_out, and_7_out, and_8_out, and_9_out,
       and_10_out, and_11_out, and_12_out, and_13_out, and_14_out, and_15_out, and_16_out, and_17_out,
       and_18_out, CLK_t, DE, DE_count_1, NO_ERROR, or_1_out, s0, s1, s2, s3, s4, s5, s6, s7, s8, s9, s10,
       s11, s12, s13, s14, s15, SINGLE_ERROR, UNDETECTABLE_ERROR;
  wire [4:0] _16FIFO_count, DE_count, most_recent_DE_location, n5badd1_1_out_2;
  wire [15:0] COMPUTED_PARITY, DOUBLE_ERROR_CORRECTED, PO0, PO1, PO2, PO3, PO4, PO5, PO6, PO7, PO8, PO9,
       PO10, PO11, PO12, PO13, PO14, PO15, SHIFT_WORD;
  wire [21:0] n16fifo_1_parallel_out_0, n16fifo_1_parallel_out_1, n16fifo_1_parallel_out_2,
       n16fifo_1_parallel_out_3, n16fifo_1_parallel_out_4, n16fifo_1_parallel_out_5,
       n16fifo_1_parallel_out_6, n16fifo_1_parallel_out_7, n16fifo_1_parallel_out_8,
       n16fifo_1_parallel_out_9, n16fifo_1_parallel_out_10, n16fifo_1_parallel_out_11,
       n16fifo_1_parallel_out_12, n16fifo_1_parallel_out_13, n16fifo_1_parallel_out_14,
       n16fifo_1_parallel_out_15, secded_1_out_2;

  Clock clock_1 (.out(CLK_t));
  SECDED_22bit_DETECT DATA_WORD_SECDED (
    ._22_IN(in_4), ._16_OUT(SHIFT_WORD), .NO_ERROR(NO_ERROR), .DOUBLE_ERROR(DE),
    .UNDETECTABLE_ERROR(UNDETECTABLE_ERROR), .SINGLE_ERROR_FIXED(SINGLE_ERROR));
  Demultiplexer #(.select(5), .enable("false")) demultiplexer_1 (
    .out0(s0), .out1(s1), .out2(s2), .out3(s3), .out4(s4), .out5(s5), .out6(s6), .out7(s7), .out8(s8),
    .out9(s9), .out10(s10), .out11(s11), .out12(s12), .out13(s13), .out14(s14), .out15(s15), .in(1'b1),
    .sel(most_recent_DE_location));  // open: out16, out17, out18, out19, out20, out21, out22, out23, out24, out25, out26, out27, out28, out29, out30, out31
  Comparator #(.width(5), .mode("unsigned")) comparator_1 (
    .a(DE_count), .b({5{1'b0}}), .gt(SECDED_ERROR));  // open: eq, lt
  Comparator #(.width(5), .mode("unsigned")) comparator_2 (
    .a(DE_count), .b(5'b00001), .gt(FRAME_ERROR));  // open: eq, lt
  _5bADD1 u_5badd1_1 (.in_1(DE_count), .out_2(n5badd1_1_out_2));
  Register #(.width(5)) register_1 (.D(n5badd1_1_out_2), .en(DE), .Q(DE_count), .clk(CLK_t), .clr(START_FRAME));
  Register #(.width(5)) register_2 (
    .D(_16FIFO_count), .en(DE), .Q(most_recent_DE_location), .clk(CLK_t), .clr(START_FRAME));
  assign DOUBLE_ERROR_CORRECTED = SHIFT_WORD ^ COMPUTED_PARITY;  // XOR_Gate xor_1, 16 bits wide
  or or_1 (or_1_out, NO_ERROR, SINGLE_ERROR);
  Comparator #(.width(5), .mode("unsigned")) comparator_3 (
    .a(DE_count), .b(5'b00001), .eq(DE_count_1));  // open: gt, lt
  Register #(.width(16)) register_3 (
    .D(DOUBLE_ERROR_CORRECTED), .en(and_1_out), .Q(COMPUTED_PARITY), .clk(CLK_t), .clr(START_FRAME));
  and and_1 (and_1_out, WIS, or_1_out);
  and and_2 (and_2_out, WIS, ~PARITY_SIGNAL);  // AND_Gate
  SECDED secded_1 (.in_1(SHIFT_WORD), .out_2(secded_1_out_2));
  _16FIFO u_16fifo_1 (
    .CLK(CLK_t), .Word_In(secded_1_out_2), .Word_In_Signal(and_2_out),
    .Parallel_Unload_Signal(PARITY_SIGNAL), .FIFO_count(_16FIFO_count),
    .Parallel_out_0(n16fifo_1_parallel_out_0), .Parallel_out_1(n16fifo_1_parallel_out_1),
    .Parallel_out_2(n16fifo_1_parallel_out_2), .Parallel_out_3(n16fifo_1_parallel_out_3),
    .Parallel_out_4(n16fifo_1_parallel_out_4), .Parallel_out_5(n16fifo_1_parallel_out_5),
    .Parallel_out_6(n16fifo_1_parallel_out_6), .Parallel_out_7(n16fifo_1_parallel_out_7),
    .Parallel_out_8(n16fifo_1_parallel_out_8), .Parallel_out_9(n16fifo_1_parallel_out_9),
    .Parallel_out_10(n16fifo_1_parallel_out_10), .Parallel_out_11(n16fifo_1_parallel_out_11),
    .Parallel_out_12(n16fifo_1_parallel_out_12), .Parallel_out_13(n16fifo_1_parallel_out_13),
    .Parallel_out_14(n16fifo_1_parallel_out_14), .Parallel_out_15(n16fifo_1_parallel_out_15));  // open: Word_Out_Signal, Parallel_load_signal, Paralell_In_Count, Parallel_In_0, Parallel_In_1, Parallel_In_2, Parallel_In_3, Parallel_In_4, Parallel_In_5, Parallel_In_6, Parallel_In_7, Parallel_In_8, Parallel_In_9, Parallel_In_10, Parallel_In_11, Parallel_In_12, Parallel_In_13, Parallel_In_14, Parallel_In_15, Word_Out
  Multiplexer #(.width(5), .enable("false")) multiplexer_1 (
    .in0({5{1'b0}}), .in1(_16FIFO_count), .out(DATAWORD_COUNT), .sel(PARITY_SIGNAL));
  SECDED_22_TO_16 secded_22_to_16_1 (.in_1(n16fifo_1_parallel_out_0), .out_2(PO0));
  SECDED_22_TO_16 secded_22_to_16_2 (.in_1(n16fifo_1_parallel_out_1), .out_2(PO1));
  SECDED_22_TO_16 secded_22_to_16_3 (.in_1(n16fifo_1_parallel_out_2), .out_2(PO2));
  SECDED_22_TO_16 secded_22_to_16_4 (.in_1(n16fifo_1_parallel_out_3), .out_2(PO3));
  SECDED_22_TO_16 secded_22_to_16_5 (.in_1(n16fifo_1_parallel_out_4), .out_2(PO4));
  SECDED_22_TO_16 secded_22_to_16_6 (.in_1(n16fifo_1_parallel_out_5), .out_2(PO5));
  SECDED_22_TO_16 secded_22_to_16_7 (.in_1(n16fifo_1_parallel_out_6), .out_2(PO6));
  SECDED_22_TO_16 secded_22_to_16_8 (.in_1(n16fifo_1_parallel_out_7), .out_2(PO7));
  SECDED_22_TO_16 secded_22_to_16_9 (.in_1(n16fifo_1_parallel_out_8), .out_2(PO8));
  SECDED_22_TO_16 secded_22_to_16_10 (.in_1(n16fifo_1_parallel_out_9), .out_2(PO9));
  SECDED_22_TO_16 secded_22_to_16_11 (.in_1(n16fifo_1_parallel_out_10), .out_2(PO10));
  SECDED_22_TO_16 secded_22_to_16_12 (.in_1(n16fifo_1_parallel_out_11), .out_2(PO11));
  SECDED_22_TO_16 secded_22_to_16_13 (.in_1(n16fifo_1_parallel_out_12), .out_2(PO12));
  SECDED_22_TO_16 secded_22_to_16_14 (.in_1(n16fifo_1_parallel_out_13), .out_2(PO13));
  SECDED_22_TO_16 secded_22_to_16_15 (.in_1(n16fifo_1_parallel_out_14), .out_2(PO14));
  SECDED_22_TO_16 secded_22_to_16_16 (.in_1(n16fifo_1_parallel_out_15), .out_2(PO15));
  Multiplexer #(.width(16)) multiplexer_2 (
    .in0(PO0), .in1(DOUBLE_ERROR_CORRECTED), .out(out_9), .sel(and_3_out), .en(PARITY_SIGNAL));
  and and_3 (and_3_out, DE_count_1, ~NO_ERROR, s0);  // AND_Gate
  Multiplexer #(.width(16)) multiplexer_3 (
    .in0(PO1), .in1(DOUBLE_ERROR_CORRECTED), .out(out_10), .sel(and_5_out), .en(PARITY_SIGNAL));
  Multiplexer #(.width(16)) multiplexer_4 (
    .in0(PO2), .in1(DOUBLE_ERROR_CORRECTED), .out(out_11), .sel(and_4_out), .en(PARITY_SIGNAL));
  and and_4 (and_4_out, DE_count_1, ~NO_ERROR, s2);  // AND_Gate
  Multiplexer #(.width(16)) multiplexer_5 (
    .in0(PO3), .in1(DOUBLE_ERROR_CORRECTED), .out(out_12), .sel(and_6_out), .en(PARITY_SIGNAL));
  Multiplexer #(.width(16)) multiplexer_6 (
    .in0(PO4), .in1(DOUBLE_ERROR_CORRECTED), .out(out_13), .sel(and_7_out), .en(PARITY_SIGNAL));
  Multiplexer #(.width(16)) multiplexer_7 (
    .in0(PO6), .in1(DOUBLE_ERROR_CORRECTED), .out(out_15), .sel(and_9_out), .en(PARITY_SIGNAL));
  and and_5 (and_5_out, DE_count_1, ~NO_ERROR, s1);  // AND_Gate
  and and_6 (and_6_out, DE_count_1, ~NO_ERROR, s3);  // AND_Gate
  and and_7 (and_7_out, DE_count_1, ~NO_ERROR, s4);  // AND_Gate
  Multiplexer #(.width(16)) multiplexer_8 (
    .in0(PO5), .in1(DOUBLE_ERROR_CORRECTED), .out(out_14), .sel(and_8_out), .en(PARITY_SIGNAL));
  and and_8 (and_8_out, DE_count_1, ~NO_ERROR, s5);  // AND_Gate
  and and_9 (and_9_out, DE_count_1, ~NO_ERROR, s6);  // AND_Gate
  Multiplexer #(.width(16)) multiplexer_9 (
    .in0(PO7), .in1(DOUBLE_ERROR_CORRECTED), .out(out_16), .sel(and_10_out), .en(PARITY_SIGNAL));
  and and_10 (and_10_out, DE_count_1, ~NO_ERROR, s7);  // AND_Gate
  Multiplexer #(.width(16)) multiplexer_10 (
    .in0(PO8), .in1(DOUBLE_ERROR_CORRECTED), .out(out_17), .sel(and_11_out), .en(PARITY_SIGNAL));
  and and_11 (and_11_out, DE_count_1, ~NO_ERROR, s8);  // AND_Gate
  Multiplexer #(.width(16)) multiplexer_11 (
    .in0(PO9), .in1(DOUBLE_ERROR_CORRECTED), .out(out_18), .sel(and_12_out), .en(PARITY_SIGNAL));
  and and_12 (and_12_out, DE_count_1, ~NO_ERROR, s9);  // AND_Gate
  Multiplexer #(.width(16)) multiplexer_12 (
    .in0(PO10), .in1(DOUBLE_ERROR_CORRECTED), .out(out_19), .sel(and_13_out), .en(PARITY_SIGNAL));
  and and_13 (and_13_out, DE_count_1, ~NO_ERROR, s10);  // AND_Gate
  Multiplexer #(.width(16)) multiplexer_13 (
    .in0(PO11), .in1(DOUBLE_ERROR_CORRECTED), .out(out_20), .sel(and_14_out), .en(PARITY_SIGNAL));
  and and_14 (and_14_out, DE_count_1, ~NO_ERROR, s11);  // AND_Gate
  Multiplexer #(.width(16)) multiplexer_14 (
    .in0(PO12), .in1(DOUBLE_ERROR_CORRECTED), .out(out_21), .sel(and_15_out), .en(PARITY_SIGNAL));
  and and_15 (and_15_out, DE_count_1, ~NO_ERROR, s12);  // AND_Gate
  Multiplexer #(.width(16)) multiplexer_15 (
    .in0(PO13), .in1(DOUBLE_ERROR_CORRECTED), .out(out_22), .sel(and_16_out), .en(PARITY_SIGNAL));
  and and_16 (and_16_out, DE_count_1, ~NO_ERROR, s13);  // AND_Gate
  Multiplexer #(.width(16)) multiplexer_16 (
    .in0(PO14), .in1(DOUBLE_ERROR_CORRECTED), .out(out_23), .sel(and_17_out), .en(PARITY_SIGNAL));
  and and_17 (and_17_out, DE_count_1, ~NO_ERROR, s14);  // AND_Gate
  Multiplexer #(.width(16)) multiplexer_17 (
    .in0(PO15), .in1(DOUBLE_ERROR_CORRECTED), .out(out_24), .sel(and_18_out), .en(PARITY_SIGNAL));
  and and_18 (and_18_out, DE_count_1, ~NO_ERROR, s15);  // AND_Gate

  // Other names for the same wires on the sheet: WORD_IN[21:0] = in_4
endmodule

// 22bit-flip
module _22bit_flip_register (
  input  [21:0] _22in,
  input  [4:0] index,
  output [21:0] _22out
);

  wire comparator_2_lt, n8bit_get_bit_1_value, not_1_out, select_0_7, select_8_15, select_16_21;
  wire [2:0] index_8_15, index_16_21, index_to_be_read, multiplexer_1_out, multiplexer_4_out;
  wire [4:3] subtractor_1_out, subtractor_2_out;
  wire [7:0] edited_8_bits, frame_to_be_edited, multiplexer_2_out, multiplexer_5_out;
  wire [7:7] new_16_21;

  // Probe on index
  Comparator #(.width(5), .mode("unsigned")) comparator_1 (.a(index), .b(5'b01000), .lt(select_0_7));  // open: gt, eq
  Comparator #(.width(5), .mode("unsigned")) comparator_2 (
    .a(index), .b(5'b10000), .lt(comparator_2_lt));  // open: gt, eq
  and and_1 (select_8_15, ~select_0_7, comparator_2_lt);  // AND_Gate
  and and_2 (select_16_21, ~select_0_7, ~comparator_2_lt);  // AND_Gate
  Subtractor #(.width(5)) subtractor_1 (
    .a(index), .b(5'b01000), .out({subtractor_1_out, index_8_15}));  // open: bin, bout
  Subtractor #(.width(5)) subtractor_2 (
    .a(index), .b(5'b10000), .out({subtractor_2_out, index_16_21}));  // open: bin, bout
  Multiplexer #(.width(3), .enable("false")) multiplexer_1 (
    .in1(index[2:0]), .out(multiplexer_1_out), .sel(select_0_7));  // open: in0
  Multiplexer #(.width(8), .enable("false")) multiplexer_2 (
    .in1(_22in[7:0]), .out(multiplexer_2_out), .sel(select_0_7));  // open: in0
  Multiplexer #(.width(8), .enable("false")) multiplexer_3 (
    .in0(_22in[7:0]), .in1(edited_8_bits), .out(_22out[7:0]), .sel(select_0_7));
  Multiplexer #(.width(3), .enable("false")) multiplexer_4 (
    .in0(multiplexer_1_out), .in1(index_8_15), .out(multiplexer_4_out), .sel(select_8_15));
  Multiplexer #(.width(8), .enable("false")) multiplexer_5 (
    .in0(multiplexer_2_out), .in1(_22in[15:8]), .out(multiplexer_5_out), .sel(select_8_15));
  not not_1 (not_1_out, n8bit_get_bit_1_value);
  _8bit_get_bit u_8bit_get_bit_1 (
    ._8bit_in(frame_to_be_edited), ._3bit_index(index_to_be_read), .Value(n8bit_get_bit_1_value));
  Multiplexer #(.width(8), .enable("false")) multiplexer_6 (
    .in0(_22in[15:8]), .in1(edited_8_bits), .out(_22out[15:8]), .sel(select_8_15));
  Multiplexer #(.width(8), .enable("false")) multiplexer_7 (
    .in0(multiplexer_5_out), .in1({2'b00, _22in[21:16]}), .out(frame_to_be_edited), .sel(select_16_21));
  edit_register edit_register_1 (
    ._8_bit(frame_to_be_edited), .BIT(index_to_be_read), .V(not_1_out), .Enable(1'b1),
    .updated_8_bits(edited_8_bits));
  Multiplexer #(.width(3), .enable("false")) multiplexer_8 (
    .in0(multiplexer_4_out), .in1(index_16_21), .out(index_to_be_read), .sel(select_16_21));
  // Probe on edited_8_bits
  Multiplexer #(.width(8), .enable("false")) multiplexer_9 (
    .in0({2'b00, _22in[21:16]}), .in1(edited_8_bits), .out({{2{new_16_21[7]}}, _22out[21:16]}),
    .sel(select_16_21));
  // also tied to GND on the sheet: new_16_21[7]

  // Other names for the same wires on the sheet: _0_7[7:0] = _22in[7:0]; _8_15[7:0] = _22in[15:8];
  //   _16_21[5:0] = _22in[21:16]; index_0_7[2:0] = index[2:0]; new_0_7[7:0] = _22out[7:0];
  //   new_8_15[7:0] = _22out[15:8]; new_16_21[6:0] = {new_16_21[7], _22out[21:16]}
endmodule

module _8bit_get_bit (
  input  [7:0] _8bit_in,
  input  [2:0] _3bit_index,
  output Value
);

  wire and_1_out, and_2_out, and_3_out, and_4_out, and_5_out, and_6_out, and_7_out, and_8_out,
       demultiplexer_1_out0, demultiplexer_1_out1, demultiplexer_1_out2, demultiplexer_1_out3,
       demultiplexer_1_out4, demultiplexer_1_out5, demultiplexer_1_out6, demultiplexer_1_out7, s0, s1, s2,
       s3, s4, s5, s6, s7;

  Demultiplexer #(.select(3), .disabled(0), .enable("false")) demultiplexer_1 (
    .out0(demultiplexer_1_out0), .out1(demultiplexer_1_out1), .out2(demultiplexer_1_out2),
    .out3(demultiplexer_1_out3), .out4(demultiplexer_1_out4), .out5(demultiplexer_1_out5),
    .out6(demultiplexer_1_out6), .out7(demultiplexer_1_out7), .in(1'b1), .sel(_3bit_index));
  and and_1 (and_1_out, s0, _8bit_in[0]);
  and and_2 (and_2_out, s1, _8bit_in[1]);
  and and_3 (and_3_out, s2, _8bit_in[2]);
  and and_4 (and_4_out, s3, _8bit_in[3]);
  and and_5 (and_5_out, s4, _8bit_in[4]);
  and and_6 (and_6_out, s5, _8bit_in[5]);
  and and_7 (and_7_out, s6, _8bit_in[6]);
  and and_8 (and_8_out, s7, _8bit_in[7]);
  and and_9 (s0, 1'b1, demultiplexer_1_out0);
  and and_10 (s1, 1'b1, demultiplexer_1_out1);
  and and_11 (s2, 1'b1, demultiplexer_1_out2);
  and and_12 (s3, 1'b1, demultiplexer_1_out3);
  and and_13 (s4, 1'b1, demultiplexer_1_out4);
  and and_14 (s5, 1'b1, demultiplexer_1_out5);
  and and_15 (s6, 1'b1, demultiplexer_1_out6);
  and and_16 (s7, 1'b1, demultiplexer_1_out7);
  or or_1 (Value, and_1_out, and_2_out, and_3_out, and_4_out, and_5_out, and_6_out, and_7_out, and_8_out);

  // Other names for the same wires on the sheet: V = Value
endmodule
module SECDED_22bit_DETECT (
  input  [21:0] _22_IN,
  output [15:0] _16_OUT,
  output NO_ERROR,
  output DOUBLE_ERROR,
  output UNDETECTABLE_ERROR,
  output SINGLE_ERROR_FIXED
);

  wire comparator_2_eq, DE1, DE2, demultiplexer_1_out2, or_1_out, R0, Within_bounds;
  wire [4:0] ERR_INDEX;
  wire [15:0] _16_SINGLE_ERROR_CORRECTED, multiplexer_1_out;
  wire [16:0] n22bit_flip_register_1__22out;
  wire [21:0] ENCODED_RECEIVED;
  wire [21:3] XOR_ed;

  // Probe on ERR_INDEX
  Comparator #(.width(5), .mode("unsigned")) comparator_1 (
    .a(ERR_INDEX), .b(5'b10110), .lt(Within_bounds));  // open: gt, eq
  Demultiplexer #(.select(2), .disabled(0), .enable("false")) demultiplexer_1 (
    .out0(DE1), .out1(UNDETECTABLE_ERROR), .out2(demultiplexer_1_out2), .out3(SINGLE_ERROR_FIXED), .in(1'b1),
    .sel({Within_bounds, R0}));
  Comparator #(.width(5), .mode("unsigned")) comparator_2 (
    .a(ERR_INDEX), .b({5{1'b0}}), .eq(comparator_2_eq));  // open: gt, lt
  or or_1 (or_1_out, UNDETECTABLE_ERROR, DOUBLE_ERROR);
  Multiplexer #(.width(16), .enable("false")) multiplexer_1 (
    .in0({_22_IN[21:17], _22_IN[15:9], _22_IN[7:5], _22_IN[3]}), .in1({16{1'b0}}), .out(multiplexer_1_out),
    .sel(or_1_out));
  and and_1 (NO_ERROR, demultiplexer_1_out2, comparator_2_eq);
  and and_2 (DE2, demultiplexer_1_out2, ~comparator_2_eq);  // AND_Gate
  Multiplexer #(.width(16), .enable("false")) multiplexer_2 (
    .in0(multiplexer_1_out), .in1(_16_SINGLE_ERROR_CORRECTED), .out(_16_OUT), .sel(SINGLE_ERROR_FIXED));
  or or_2 (DOUBLE_ERROR, DE2, DE1);
  _22bit_flip_register u_22bit_flip_register_1 (
    ._22in(_22_IN), .index(ERR_INDEX),
    ._22out({_16_SINGLE_ERROR_CORRECTED[15:11], n22bit_flip_register_1__22out[16], _16_SINGLE_ERROR_CORRECTED[10:4], n22bit_flip_register_1__22out[8], _16_SINGLE_ERROR_CORRECTED[3:1], n22bit_flip_register_1__22out[4], _16_SINGLE_ERROR_CORRECTED[0], n22bit_flip_register_1__22out[2:0]}));
  // Probe on {_22_IN[21:17], _22_IN[15:9], _22_IN[7:5], _22_IN[3]}
  SECDED secded_1 (.in_1({_22_IN[21:17], _22_IN[15:9], _22_IN[7:5], _22_IN[3]}), .out_2(ENCODED_RECEIVED));
  assign {XOR_ed[21:17], ERR_INDEX[4], XOR_ed[15:9], ERR_INDEX[3], XOR_ed[7:5], ERR_INDEX[2], XOR_ed[3], ERR_INDEX[1:0], R0} = _22_IN ^ ENCODED_RECEIVED;  // XOR_Gate xor_1, 22 bits wide
  // Probe on ERR_INDEX
  // Probe on ENCODED_RECEIVED

  // Other names for the same wires on the sheet: _16_SHIFT_WORD[15:0] = _16_OUT; DE = DOUBLE_ERROR;
  //   SINGLE_ERROR = SINGLE_ERROR_FIXED; C0 = _22_IN[0]; WORD_IN[21:0] = _22_IN; C1 = _22_IN[1]; C2 = _22_IN[2];
  //   RECEIVED_DATA[15:0] = {_22_IN[21:17], _22_IN[15:9], _22_IN[7:5], _22_IN[3]}; C3 = _22_IN[4]; C4 = _22_IN[8];
  //   C5 = _22_IN[16]; XOR_ed (some bits) = {ERR_INDEX, R0}; R1 = ERR_INDEX[0]; R2 = ERR_INDEX[1]; R3 = ERR_INDEX[2];
  //   R4 = ERR_INDEX[3]; R5 = ERR_INDEX[4]
endmodule

module SECDED_22_TO_16 (
  input  [21:0] in_1,
  output [15:0] out_2
);


  assign out_2 = {in_1[21:17], in_1[15:9], in_1[7:5], in_1[3]};

  // Other names for the same wires on the sheet: C0 = in_1[0]; WORD_IN[21:0] = in_1; C1 = in_1[1]; C2 = in_1[2];
  //   RECEIVED_DATA[15:0] = {in_1[21:17], in_1[15:9], in_1[7:5], in_1[3]}; C3 = in_1[4]; C4 = in_1[8]; C5 = in_1[16]
endmodule
