// Logisim project Project4Given.circ as structural Verilog: 10 circuits, main circuit NIC
module main (
  input  En_Noise
);

  wire CLK, keyboard_1_avail, multiplexer_1_out, nic_1_int, nic_1_tx, noisychannel_1_out,
       terminalcontroller_1_cs, terminalcontroller_1_kben, terminalcontroller_1_o,
       terminalcontroller_1_ttyen, terminalcontroller_1_w;
  wire [1:0] terminalcontroller_1_addr;
  wire [6:0] keyboard_1_data, terminalcontroller_1_ttydata;
  wire [7:0] nic_1_dataout, terminalcontroller_1_dataout, terminalcontroller_1_status;

  TTY tty_1 (.data(terminalcontroller_1_ttydata), .clk(CLK), .we(terminalcontroller_1_ttyen));  // open: clr
  Keyboard keyboard_1 (
    .clk(CLK), .re(terminalcontroller_1_kben), .avail(keyboard_1_avail), .data(keyboard_1_data));  // open: clr
  LED DR (.in(terminalcontroller_1_status[1]));
  LED TBNF (.in(terminalcontroller_1_status[2]));
  LED TXI (.in(terminalcontroller_1_status[3]));
  LED NF (.in(terminalcontroller_1_status[4]));
  LED OR (.in(terminalcontroller_1_status[5]));
  LED SDE (.in(terminalcontroller_1_status[6]));
  LED FE (.in(terminalcontroller_1_status[7]));
  Clock clock_1 (.out(CLK));
  TerminalController terminalcontroller_1 (
    .TTYEN(terminalcontroller_1_ttyen), .TTYDATA(terminalcontroller_1_ttydata),
    .STATUS(terminalcontroller_1_status), .KBEN(terminalcontroller_1_kben), .KBRDY(keyboard_1_avail),
    .KBDATA(keyboard_1_data), .CLK(CLK), .DIV(4'b0011), .INT(nic_1_int), .CS(terminalcontroller_1_cs),
    .O(terminalcontroller_1_o), .W(terminalcontroller_1_w), .ADDR(terminalcontroller_1_addr),
    .DATAOUT(terminalcontroller_1_dataout), .DATAIN(nic_1_dataout));
  NIC nic_1 (
    .INT(nic_1_int), .CS(terminalcontroller_1_cs), .O(terminalcontroller_1_o), .W(terminalcontroller_1_w),
    .ADDR(terminalcontroller_1_addr), .DATAIN(terminalcontroller_1_dataout), .DATAOUT(nic_1_dataout),
    .CLK(CLK), .TX(nic_1_tx), .RX(multiplexer_1_out));
  Shift_Register #(.length(32)) shift_register_1 (
    .in(nic_1_tx), .clk(CLK));  // open: shift, out, load, clr, d0, q0, d1, q1, d2, q2, d3, q3, d4, q4, d5, q5, d6, q6, d7, q7, d8, q8, d9, q9, d10, q10, d11, q11, d12, q12, d13, q13, d14, q14, d15, q15, d16, q16, d17, q17, d18, q18, d19, q19, d20, q20, d21, q21, d22, q22, d23, q23, d24, q24, d25, q25, d26, q26, d27, q27, d28, q28, d29, q29, d30, q30, d31, q31
  Shift_Register #(.length(32)) shift_register_2 (
    .in(multiplexer_1_out), .clk(CLK));  // open: shift, out, load, clr, d0, q0, d1, q1, d2, q2, d3, q3, d4, q4, d5, q5, d6, q6, d7, q7, d8, q8, d9, q9, d10, q10, d11, q11, d12, q12, d13, q13, d14, q14, d15, q15, d16, q16, d17, q17, d18, q18, d19, q19, d20, q20, d21, q21, d22, q22, d23, q23, d24, q24, d25, q25, d26, q26, d27, q27, d28, q28, d29, q29, d30, q30, d31, q31
  NoisyChannel noisychannel_1 (.In(nic_1_tx), .Rate(16'h800), .CLK(CLK), .Out(noisychannel_1_out));
  Multiplexer #(.enable("false")) multiplexer_1 (
    .in0(nic_1_tx), .in1(noisychannel_1_out), .out(multiplexer_1_out), .sel(En_Noise));

  // Notes on the sheet:
  //   Div
  //   Noise Rate
endmodule

module TerminalController (
  input  KBRDY,
  input  [6:0] KBDATA,
  input  INT,
  input  [7:0] DATAIN,
  input  CLK,
  input  [3:0] DIV,
  output KBEN,
  output CS,
  output O,
  output TTYEN,
  output W,
  output [6:0] TTYDATA,
  output [1:0] ADDR,
  output [7:0] STATUS,
  output [7:0] DATAOUT
);

  wire DOCHECKS, JMP, not_4_out, not_5_out, not_6_out, STATUSEN, TF, TTYDATAOUTSEL, TTYENP;
  wire [1:0] and_2_out, DATAOUTSEL;
  wire [7:0] DATABUSBYTE, INST, JUMPTARGET, multiplexer_1_out, multiplexer_3_out;
  wire [7:7] multiplexer_2_out;
  wire [23:11] rom_1_data;

  ROM #(.dataWidth(24)) rom_1 (
    .addr(INST),
    .data({rom_1_data[23:21], ADDR, KBEN, TTYENP, DATAOUTSEL, TTYDATAOUTSEL, rom_1_data[13:11], DOCHECKS, STATUSEN, JMP, DATABUSBYTE}),
    .sel(1'b1));
  not not_1 (W, rom_1_data[21]);
  not not_2 (O, rom_1_data[22]);
  not not_3 (CS, rom_1_data[23]);
  assign DATAOUT = not_4_out ? multiplexer_1_out : 8'bz;  // Controlled_Buffer controlled_buffer_1
  Multiplexer #(.select(2), .width(8), .enable("false")) multiplexer_1 (
    .in0({4'b0000, DIV}), .in1(DATABUSBYTE), .in2({1'b1, KBDATA}), .in3({8{1'b0}}), .out(multiplexer_1_out),
    .sel(DATAOUTSEL));
  not not_4 (not_4_out, W);
  Multiplexer #(.width(8), .enable("false")) multiplexer_2 (
    .in0(DATAIN), .in1(DATABUSBYTE), .out({multiplexer_2_out[7], TTYDATA}), .sel(TTYDATAOUTSEL));
  and and_1 (TTYEN, multiplexer_2_out[7], TTYENP);
  Counter counter_1 (.load(JMP), .D(JUMPTARGET), .count(not_5_out), .Q(INST), .clk(CLK));  // open: carry, clr
  not not_5 (not_5_out, JMP);
  Multiplexer #(.width(8), .enable("false")) multiplexer_3 (
    .in0(8'h20), .in1(8'h30), .out(multiplexer_3_out), .sel(TF));
  and and_2 (and_2_out[0], KBRDY, DOCHECKS);
  and and_3 (and_2_out[1], DOCHECKS, not_6_out);
  not not_6 (not_6_out, INT);
  Comparator #(.width(7), .mode("unsigned")) comparator_1 (.a(KBDATA), .b(7'b0001010), .eq(TF));  // open: gt, lt
  Register register_1 (.D(DATAIN), .en(STATUSEN), .Q(STATUS), .clk(CLK));  // open: clr
  Multiplexer #(.select(2), .width(8), .enable("false")) multiplexer_4 (
    .in0(DATABUSBYTE), .in1(multiplexer_3_out), .in2(8'h10), .in3(8'h10), .out(JUMPTARGET), .sel(and_2_out));

  // Other names for the same wires on the sheet: KBDATABUSBYTE[6:0] = KBDATA

  // Notes on the sheet:
  //   contents of rom_1 (hex, n*v repeats v):
  //   0 b80000 b80000 0 a88002 a88002 0 a08001 a08001 0 c00000 c00000 c00200 509 0 0 d00000 d00000 d20000
  //   109 12*0 b10000 b10000 b10000 40000 109 11*0 b10000 b10000 b10000 40000 a08003 a08003 109
endmodule

module NIC (
  input  CS,
  input  O,
  input  W,
  input  RX,
  input  [1:0] ADDR,
  input  [7:0] DATAIN,
  input  CLK,
  output INT,
  output TX,
  output [7:0] DATAOUT
);

  wire CS_t, INT_t, O_t, W_t;

  not not_1 (INT, INT_t);
  not not_2 (CS_t, CS);
  not not_3 (O_t, O);
  not not_4 (W_t, W);

  // Other names for the same wires on the sheet: minus_CS = CS; minus_INT = INT; minus_O = O; minus_W = W
endmodule

module NoisyChannel (
  input  [15:0] Rate,
  input  In,
  input  CLK,
  output Out
);

  wire Flip;
  wire [15:0] RNG;
  wire [31:0] adder_1_out, multiplier_1_out, SEED;

  xor xor_1 (Out, In, Flip);
  Multiplier #(.width(32)) multiplier_1 (.a(SEED), .b(32'h15a4e35), .out(multiplier_1_out));  // open: cin, cout
  Adder #(.width(32)) adder_1 (.a(multiplier_1_out), .b(32'h1), .out(adder_1_out));  // open: cin, cout
  Comparator #(.width(16), .mode("unsigned")) comparator_1 (.a(RNG), .b(Rate), .lt(Flip));  // open: gt, eq
  Register #(.width(32)) register_1 (.D(adder_1_out), .Q(SEED), .clk(CLK));  // open: en, clr
  assign RNG = SEED[15:0] ^ SEED[31:16];  // XOR_Gate xor_2, 16 bits wide
endmodule

module BRD (
  input  [3:0] BRD,
  input  Clock,
  output [3:0] BRD_2,
  output BRDO
);

  wire CLK;
  wire [3:0] BRD_1, C, C_1, multiplexer_1_out;

  Multiplexer #(.width(4), .enable("false")) multiplexer_1 (
    .in0(C_1), .in1(BRD_1), .out(multiplexer_1_out), .sel(BRDO));
  Clock clock_1 (.out(CLK));
  Register #(.width(4)) register_1 (.D(multiplexer_1_out), .Q(C), .clk(CLK));  // open: en, clr
  nor nor_1 (BRDO, C[0], C[1], C[2], C[3]);
  Subtractor #(.width(4)) subtractor_1 (.a(C), .b(4'b0000), .out(C_1), .bin(1'b1));  // open: bout
  Subtractor #(.width(4)) subtractor_2 (.a(BRD), .b(4'b0000), .out(BRD_1), .bin(1'b1));  // open: bout

  assign BRD_2 = BRD;

  // Other names for the same wires on the sheet: is0 = BRDO; O = BRDO

  // Notes on the sheet:
  //   BRD: pull=down
endmodule

module _22FIFO (
  input  CLK,
  input  Serial_In,
  input  Serial_In_Signal,
  input  Serial_Out_Signal,
  input  Parallel_Signal,
  input  Parallel_Unload,
  input  [4:0] Paralell_In_Count,
  input  [21:0] Parallel_In,
  output Serial_Out,
  output [4:0] FIFO_count,
  output [21:0] Parallel_Out
);

  wire _21, SIOO, SOO;
  wire [4:0] BACK, BACK_star, FRONT, FRONT_P, FRONT_S, FRONT_S_star, FRONT_SI, FRONT_SO, FRONT_star,
       n5bsub1_1_out_2, n5bsub1_2_out_2, subtractor_1_out, subtractor_2_out;
  wire [20:0] FIFO_S;
  wire [21:0] FIFO, FIFO_P, FIFO_star;

  Subtractor #(.width(5)) subtractor_1 (.b(Paralell_In_Count), .out(subtractor_1_out));  // open: a, bin, bout
  Multiplexer #(.width(22), .enable("false")) multiplexer_1 (
    .in0(FIFO), .in1(Parallel_In), .out(FIFO_P), .sel(Parallel_Signal));
  Adder #(.width(5)) adder_1 (.a(subtractor_1_out), .b(5'b00001), .out(FRONT_P));  // open: cin, cout
  Adder #(.width(5)) adder_2 (.a(FRONT_S), .b(5'b00001), .out(FRONT_SI));  // open: cin, cout
  _5bSUB1 u_5bsub1_1 (.in_1(FRONT_SI), .out_2(n5bsub1_1_out_2));
  Multiplexer #(.select(5), .enable("false")) multiplexer_2 (
    .in0(Serial_In), .in1(FIFO_S[0]), .in2(FIFO_S[1]), .in3(FIFO_S[2]), .in4(FIFO_S[3]), .in5(FIFO_S[4]),
    .in6(FIFO_S[5]), .in7(FIFO_S[6]), .in8(FIFO_S[7]), .in9(FIFO_S[8]), .in10(FIFO_S[9]), .in11(FIFO_S[10]),
    .in12(FIFO_S[11]), .in13(FIFO_S[12]), .in14(FIFO_S[13]), .in15(FIFO_S[14]), .in16(FIFO_S[15]),
    .in17(FIFO_S[16]), .in18(FIFO_S[17]), .in19(FIFO_S[18]), .in20(FIFO_S[19]), .in21(FIFO_S[20]),
    .out(SIOO), .sel(n5bsub1_1_out_2));  // open: in22, in23, in24, in25, in26, in27, in28, in29, in30, in31
  Register #(.width(22)) u_FIFO (.D(FIFO_star), .Q(FIFO));  // open: en, clk, clr
  assign Parallel_Out = Parallel_Unload ? FIFO : 22'bz;  // Controlled_Buffer controlled_buffer_1
  Multiplexer #(.select(5), .enable("false")) multiplexer_3 (
    .in0(FIFO_S[0]), .in1(FIFO_S[1]), .in2(FIFO_S[2]), .in3(FIFO_S[3]), .in4(FIFO_S[4]), .in5(FIFO_S[5]),
    .in6(FIFO_S[6]), .in7(FIFO_S[7]), .in8(FIFO_S[8]), .in9(FIFO_S[9]), .in10(FIFO_S[10]), .in11(FIFO_S[11]),
    .in12(FIFO_S[12]), .in13(FIFO_S[13]), .in14(FIFO_S[14]), .in15(FIFO_S[15]), .in16(FIFO_S[16]),
    .in17(FIFO_S[17]), .in18(FIFO_S[18]), .in19(FIFO_S[19]), .in20(FIFO_S[20]), .in21(_21), .out(SOO),
    .sel(n5bsub1_2_out_2));  // open: in22, in23, in24, in25, in26, in27, in28, in29, in30, in31
  _5bSUB1 u_5bsub1_2 (.in_1(FRONT_S), .out_2(n5bsub1_2_out_2));
  Register #(.width(5)) u_FRONT (.D(FRONT_star), .Q(FRONT));  // open: en, clk, clr
  Subtractor #(.width(5)) subtractor_2 (.a(BACK_star), .b(FRONT_star), .out(subtractor_2_out));  // open: bin, bout
  Subtractor #(.width(5)) subtractor_3 (.a(FRONT_S), .b(5'b00001), .out(FRONT_SO));  // open: bin, bout
  Adder #(.width(5)) adder_3 (.a(subtractor_2_out), .b(5'b00001), .out(FIFO_count));  // open: cin, cout
  Register #(.width(5)) u_BACK (.D(BACK_star), .Q(BACK));  // open: en, clk, clr
  Multiplexer #(.select(2), .enable("false")) multiplexer_4 (
    .in2(SOO), .in3(SIOO), .out(Serial_Out), .sel({Serial_Out_Signal, Serial_In_Signal}));  // open: in0, in1
  Multiplexer #(.select(2), .width(5), .enable("false")) multiplexer_5 (
    .in1(FRONT_SI), .in2(FRONT_SO), .in3(FRONT), .out(FRONT_S_star),
    .sel({Serial_Out_Signal, Serial_In_Signal}));  // open: in0

  // Other names for the same wires on the sheet: SIS = Serial_In_Signal; SOS = Serial_Out_Signal;
  //   FC[4:0] = FIFO_count; FIFO_S[21] = _21; FIFO_SI[21:0] = {FIFO_S, Serial_In}; SI = Serial_In;
  //   PS = Parallel_Signal; PU = Parallel_Unload; PX[21:0] = Parallel_In; PXC[4:0] = Paralell_In_Count;
  //   PXO[21:0] = Parallel_Out; SXO = Serial_Out
endmodule

module _5bADD1 (
  input  [4:0] in_1,
  output [4:0] out_2
);

  Adder #(.width(5)) adder_1 (.a(in_1), .b(5'b00001), .out(out_2));  // open: cin, cout
endmodule

// SUB1
module _5bSUB1 (
  input  [4:0] in_1,
  output [4:0] out_2
);

  Subtractor #(.width(5)) subtractor_1 (.a(in_1), .b(5'b00001), .out(out_2));  // open: bin, bout
endmodule

module P_LOADER (
  input  [21:0] in_1,
  input  [21:0] in_2,
  input  [4:0] in_3
);


  // Other names for the same wires on the sheet: C[4:0] = in_3; F1 = in_1[0]; FIFO[21:0] = in_1; O0[21:0] = in_1;
  //   F2 = in_1[1]; O1[21:0] = {in_1[21:1], in_2[0]}; F3 = in_1[2]; O2[21:0] = {in_1[21:2], in_2[1:0]}; F4 = in_1[3];
  //   O3[21:0] = {in_1[21:3], in_2[2:0]}; F5 = in_1[4]; O4[21:0] = {in_1[21:4], in_2[3:0]}; F6 = in_1[5];
  //   O5[21:0] = {in_1[21:5], in_2[4:0]}; F7 = in_1[6]; O6[21:0] = {in_1[21:6], in_2[5:0]};
  //   O7[21:0] = {in_1[21:7], in_2[6:0]}; O8[21:0] = {in_1[21:8], in_2[7:0]}; P1 = in_2[0]; PIN[21:0] = in_2;
  //   P2 = in_2[1]; P3 = in_2[2]; P4 = in_2[3]; P5 = in_2[4]; P6 = in_2[5]; P7 = in_2[6]; F8 = in_1[7]; F9 = in_1[8];
  //   F10 = in_1[9]; F11 = in_1[10]; F12 = in_1[11]; F13 = in_1[12]; F14 = in_1[13]; F15 = in_1[14]; F16 = in_1[15];
  //   F17 = in_1[16]; F18 = in_1[17]; F19 = in_1[18]; F20 = in_1[19]; F21 = in_1[20]; F22 = in_1[21]; P8 = in_2[7];
  //   P9 = in_2[8]; P10 = in_2[9]; P11 = in_2[10]; P12 = in_2[11]; P13 = in_2[12]; P14 = in_2[13]; P15 = in_2[14];
  //   P16 = in_2[15]; P17 = in_2[16]; P18 = in_2[17]; P19 = in_2[18]; P20 = in_2[19]; P21 = in_2[20]; P22 = in_2[21]
endmodule

module PL_Comp (
  input  [4:0] in_1,
  input  [4:0] in_2,
  output [4:0] index_1,
  output should_update
);

  wire comparator_1_eq, comparator_1_lt;

  Comparator #(.width(5), .mode("unsigned")) comparator_1 (
    .a(in_2), .b(in_1), .eq(comparator_1_eq), .lt(comparator_1_lt));  // open: gt
  or or_1 (should_update, comparator_1_eq, comparator_1_lt);
  Subtractor #(.width(5)) subtractor_1 (.a(in_2), .b(5'b00001), .out(index_1));  // open: bin, bout

  // Other names for the same wires on the sheet: index[4:0] = in_2; tunnel[4:0] = in_1
endmodule
