// Logisim project p4-extra credit.circ as structural Verilog
module bit_sampler (
  input  RX,
  input  CLK,
  input  [7:0] BRD,
  output out_4,
  output out_5,
  output out_6
);

  wire ADV, and_3_out, and_4_out, and_5_out, and_6_out, and_7_out, and_8_out, and_9_out, and_10_out,
       BRD_isodd, CLK_t, comparator_1_eq, comparator_2_eq, comparator_3_eq, comparator_4_eq, comparator_5_eq,
       comparator_6_eq, comparator_7_eq, d_ff_1_q, DELAY, ENABLE, multiplexer_1_out, multiplexer_2_out,
       or_1_out, or_2_out, or_3_out, or_4_out, or_5_out, REALCLK, S1, S2, S3, t_ff_1_q;
  wire [3:0] BRD_1, BRD_1_2, BRD_2, BRD_4BIT, BRD_COUNT;
  wire [7:1] divider_3_rem;

  // AND_Gate and_1 has open pins: in0=ENABLE, out=open
  Subtractor #(.width(4)) subtractor_1 (.a(BRD[3:0]), .b(4'b0001), .out(BRD_1));  // open: bin, bout
  Divider #(.width(4)) divider_1 (.a(BRD_1), .b(4'b0010), .out(BRD_1_2));  // open: upper, rem
  Divider #(.width(4)) divider_2 (.a(BRD_4BIT), .b(4'b0010), .out(BRD_2));  // open: upper, rem
  Clock clock_1 (.out(CLK_t));
  and and_2 (REALCLK, CLK_t, ENABLE);
  or or_1 (or_1_out, ~RX, RX);  // OR_Gate
  Comparator #(.width(4), .mode("unsigned")) comparator_1 (
    .a(BRD_COUNT), .b(4'b0000), .eq(comparator_1_eq));  // open: gt, lt
  Comparator #(.width(4), .mode("unsigned")) comparator_2 (
    .a(BRD_COUNT), .b(4'b0001), .eq(comparator_2_eq));  // open: gt, lt
  Comparator #(.width(4), .mode("unsigned")) comparator_3 (
    .a(BRD_COUNT), .b(BRD_1_2), .eq(comparator_3_eq));  // open: gt, lt
  Comparator #(.width(4), .mode("unsigned")) comparator_4 (
    .a(BRD_COUNT), .b(BRD_2), .eq(comparator_4_eq));  // open: gt, lt
  Comparator #(.width(4), .mode("unsigned")) comparator_5 (
    .a(BRD_COUNT), .b(BRD_1), .eq(comparator_5_eq));  // open: gt, lt
  T_Flip_Flop t_ff_1 (.clk(CLK_t), .T(or_1_out), .Q(t_ff_1_q));  // open: Qn, preset, reset, en
  and and_3 (and_3_out, BRD_isodd, comparator_1_eq);
  or or_2 (or_2_out, and_3_out, and_4_out);
  and and_4 (and_4_out, ~BRD_isodd, comparator_2_eq);  // AND_Gate
  and and_5 (and_5_out, BRD_isodd, comparator_3_eq);
  or or_3 (or_3_out, and_5_out, and_6_out);
  and and_6 (and_6_out, ~BRD_isodd, comparator_4_eq);  // AND_Gate
  D_Flip_Flop d_ff_1 (.clk(CLK_t), .D(t_ff_1_q), .Q(d_ff_1_q));  // open: Qn, preset, en, reset
  Multiplexer multiplexer_1 (.in0(RX), .in1(S2), .out(multiplexer_1_out), .sel(ADV));  // open: en
  D_Flip_Flop d_ff_2 (.clk(REALCLK), .D(RX), .Q(S2), .en(or_4_out));  // open: Qn, preset, reset
  or or_4 (or_4_out, or_3_out, ADV);
  assign S3 = comparator_5_eq ? multiplexer_2_out : 1'bz;  // Controlled_Buffer controlled_buffer_1
  Multiplexer multiplexer_2 (.in0(RX), .out(multiplexer_2_out), .sel(ADV));  // open: in1, en
  and and_7 (and_7_out, S1, S2, ~RX);  // AND_Gate
  and and_8 (and_8_out, ~S1, ~S2, RX);  // AND_Gate
  Comparator #(.width(4), .mode("unsigned")) comparator_6 (
    .a(BRD_COUNT), .b(BRD_1), .eq(comparator_6_eq));  // open: gt, lt
  and and_9 (and_9_out, RX, S2, ~S1);  // AND_Gate
  and and_10 (and_10_out, ~RX, ~S2, S1);  // AND_Gate
  Comparator #(.width(4), .mode("unsigned")) comparator_7 (
    .a(BRD_COUNT), .b(BRD_1), .eq(comparator_7_eq));  // open: gt, lt
  xor xor_1 (ENABLE, d_ff_1_q, t_ff_1_q);
  D_Flip_Flop d_ff_3 (.clk(REALCLK), .D(multiplexer_1_out), .Q(S1), .en(or_5_out));  // open: Qn, preset, reset
  or or_5 (or_5_out, or_2_out, ADV);
  and and_11 (ADV, and_7_out, and_8_out, comparator_6_eq);
  and and_12 (DELAY, and_9_out, and_10_out, comparator_7_eq);
  Divider divider_3 (.a(BRD), .b(8'h2), .rem({divider_3_rem, BRD_isodd}));  // open: out, upper

  // Other names for the same wires on the sheet: BRD4BIT[3:0] = BRD[3:0]; data_bit = out_5; new_data_signal = out_4;
  //   noise_flag = out_6
endmodule

module BRD (
  input  [3:0] BRD,
  input  Clock,
  input  RESET,
  input  RESET_2,
  output [3:0] BRD_2,
  output [3:0] BRD_COUNT,
  output BRDO,
  output BRD_is0
);

  wire undriven;
  wire [3:0] BRD_1, C, C_1, multiplexer_1_out, multiplexer_2_out, multiplexer_3_out;

  Multiplexer #(.width(4), .enable("false")) multiplexer_1 (
    .in0(C_1), .in1(BRD_1), .out(multiplexer_1_out), .sel(BRD_is0));
  Subtractor #(.width(4)) subtractor_1 (.a(C), .b(4'b0000), .out(C_1), .bin(1'b1));  // open: bout
  Subtractor #(.width(4)) subtractor_2 (.a(BRD), .b(4'b0000), .out(BRD_1), .bin(1'b1));  // open: bout
  Multiplexer #(.width(4), .enable("false")) multiplexer_2 (
    .in0(multiplexer_1_out), .in1(4'b0000), .out(multiplexer_2_out), .sel(RESET));
  nor nor_1 (BRD_is0, C[0], C[1], C[2], C[3]);
  Multiplexer #(.width(4), .enable("false")) multiplexer_3 (
    .in0(multiplexer_2_out), .in1(4'b0001), .out(multiplexer_3_out), .sel(RESET_2));
  Subtractor #(.width(4)) subtractor_3 (.a(BRD), .b(C), .out(BRD_COUNT), .bin(1'b1));  // open: bout
  // Probe on BRD_COUNT
  Register #(.width(4)) register_1 (.D(multiplexer_3_out), .Q(C), .clk(Clock), .clr(undriven));  // open: en

  assign BRD_2 = BRD;
  assign BRDO = BRD_is0;

  // Other names for the same wires on the sheet: CLK = Clock; is0 = BRD_is0; O = BRD_is0

  // Notes on the sheet:
  //   BRD: pull=down
  //   RESET: pull=down
  //   RESET_2: pull=down
endmodule

module BIT_DESTUFFER (
  input  RX,
  input  CLK,
  input  ENABLE
);

  wire [2:0] CONS_0, CONS_1;

  Register #(.width(3)) register_1 (.en(ENABLE), .Q(CONS_1), .clk(CLK));  // open: D, clr
  D_Flip_Flop d_ff_1 (.clk(CLK), .en(ENABLE));  // open: D, Q, Qn, preset, reset
  Register #(.width(3)) register_2 (.en(ENABLE), .Q(CONS_0), .clk(CLK));  // open: D, clr
  D_Flip_Flop d_ff_2 (.clk(CLK), .en(ENABLE));  // open: D, Q, Qn, preset, reset
endmodule
